// Logisim project 6502BUSMUX.circ as structural Verilog: 27 circuits, main circuit BogusSystem
module BogusSystem (
  input  RDY,
  input  nNMI,
  input  nIRQ,
  input  nRES,
  input  in_5,
  input  in_6,
  input  in_7,
  input  in_8,
  input  in_9,
  input  in_10,
  input  in_11,
  input  in_12
);

  wire mos_6502_1_phi2, mos_6502_1_r_w, mos_6502_1_sync, not_1_out, not_2_out, PHI0_out, pull_resistor_1_node;
  wire [7:0] mos_6502_1_d0_2, mos_6502_1_flag, ram_1_data;
  wire [15:0] mos_6502_1_a0;

  Clock PHI0 (.out(PHI0_out));
  Pull_Resistor #(.pull(1)) pull_resistor_1 (.node(pull_resistor_1_node));
  MOS_6502 mos_6502_1 (
    .SYNC(mos_6502_1_sync), .A0(mos_6502_1_a0[0]), .A1(mos_6502_1_a0[1]), .A2(mos_6502_1_a0[2]),
    .A3(mos_6502_1_a0[3]), .A4(mos_6502_1_a0[4]), .A5(mos_6502_1_a0[5]), .A6(mos_6502_1_a0[6]),
    .A7(mos_6502_1_a0[7]), .D0(ram_1_data[0]), .D1(ram_1_data[1]), .D2(ram_1_data[2]), .D3(ram_1_data[3]),
    .D4(ram_1_data[4]), .D5(ram_1_data[5]), .D6(ram_1_data[6]), .D7(ram_1_data[7]),
    .D0_2(mos_6502_1_d0_2[0]), .D1_2(mos_6502_1_d0_2[1]), .D2_2(mos_6502_1_d0_2[2]),
    .D3_2(mos_6502_1_d0_2[3]), .D4_2(mos_6502_1_d0_2[4]), .D5_2(mos_6502_1_d0_2[5]),
    .D6_2(mos_6502_1_d0_2[6]), .D7_2(mos_6502_1_d0_2[7]), .nNMI(nNMI), .nIRQ(nIRQ), .RDY(RDY), .nRES(nRES),
    .PHI2(mos_6502_1_phi2), .SO(pull_resistor_1_node), .R_W(mos_6502_1_r_w), .A8(mos_6502_1_a0[8]),
    .A9(mos_6502_1_a0[9]), .A10(mos_6502_1_a0[10]), .A11(mos_6502_1_a0[11]), .A12(mos_6502_1_a0[12]),
    .A13(mos_6502_1_a0[13]), .A14(mos_6502_1_a0[14]), .A15(mos_6502_1_a0[15]), .PHI0(PHI0_out),
    .FLAG(mos_6502_1_flag));  // open: PHI1
  not not_1 (not_1_out, nRES);
  Counter #(.width(32), .max('hffffffff)) counter_1 (
    .count(1'b1), .clk(mos_6502_1_phi2), .clr(not_1_out));  // open: load, D, Q, carry
  not not_2 (not_2_out, mos_6502_1_r_w);
  LED C (.in(mos_6502_1_flag[0]));
  LED Z (.in(mos_6502_1_flag[1]));
  LED I (.in(mos_6502_1_flag[2]));
  LED D (.in(mos_6502_1_flag[3]));
  LED B (.in(mos_6502_1_flag[4]));
  LED V (.in(mos_6502_1_flag[6]));
  LED N (.in(mos_6502_1_flag[7]));
  Counter #(.width(32), .max('hffffffff)) counter_2 (
    .count(1'b1), .clk(mos_6502_1_sync), .clr(not_1_out));  // open: load, D, Q, carry
  Hex_Digit_Display hex_digit_display_1 (.value(mos_6502_1_a0[11:8]));  // open: dp
  Hex_Digit_Display hex_digit_display_2 (.value(mos_6502_1_a0[15:12]));  // open: dp
  RAM #(.addrWidth(16), .bus("separate")) ram_1 (
    .addr(mos_6502_1_a0), .din(mos_6502_1_d0_2), .data(ram_1_data), .str(not_2_out), .sel(mos_6502_1_phi2),
    .clk(mos_6502_1_phi2), .ld(mos_6502_1_r_w));  // open: clr
  Hex_Digit_Display hex_digit_display_3 (.value(mos_6502_1_a0[7:4]));  // open: dp
  Hex_Digit_Display hex_digit_display_4 (.value(mos_6502_1_a0[3:0]));  // open: dp

  // Notes on the sheet:
  //   CLK Counter
  //   Instr Counter
endmodule

// MOS 6502
module MOS_6502 (
  input  nNMI,
  input  nIRQ,
  input  RDY,
  input  nRES,
  input  SO,
  input  PHI0,
  input  D0,
  input  D1,
  input  D2,
  input  D3,
  input  D4,
  input  D5,
  input  D6,
  input  D7,
  output PHI1,
  output PHI2,
  output R_W,
  output SYNC,
  output A0,
  output A1,
  output A2,
  output A3,
  output A4,
  output A5,
  output D0_2,
  output A6,
  output D1_2,
  output D2_2,
  output A7,
  output D3_2,
  output D4_2,
  output D5_2,
  output D6_2,
  output D7_2,
  output [7:0] FLAG,
  output A8,
  output A9,
  output A10,
  output A11,
  output A12,
  output A13,
  output A14,
  output A15
);

  wire _0_ADD, _1_PC, ACR, ADH_ABH, ADH_PCH, ADL_ABL, ADL_ADD, ADL_PCL, ANDS, AVR, d_ff_1_q, d_ff_2_qn,
       d_ff_3_q, DB_ADD, decoder_trans_1__6, decoder_trans_1__7, decoder_trans_1__8, decoder_trans_1__9,
       decoder_trans_1__10, decoder_trans_1__11, decoder_trans_1__12, decoder_trans_1__13,
       decoder_trans_1__14, decoder_trans_1__15, decoder_trans_1__16, decoder_trans_1__17,
       decoder_trans_1__18, decoder_trans_1__19, decoder_trans_1__20, decoder_trans_1__21,
       decoder_trans_1__22, decoder_trans_1__23, decoder_trans_1__24, decoder_trans_1__25,
       decoder_trans_1__26, decoder_trans_1__27, decoder_trans_1__28, decoder_trans_1__29,
       decoder_trans_1__30, decoder_trans_1__31, decoder_trans_1__32, decoder_trans_1__33,
       decoder_trans_1__34, decoder_trans_1__35, decoder_trans_1__36, decoder_trans_1__37,
       decoder_trans_1__38, decoder_trans_1__39, decoder_trans_1__40, decoder_trans_1__41,
       decoder_trans_1__42, decoder_trans_1__43, decoder_trans_1__44, decoder_trans_1__45,
       decoder_trans_1__46, decoder_trans_1__47, decoder_trans_1__48, decoder_trans_1__49,
       decoder_trans_1__50, decoder_trans_1__51, decoder_trans_1__52, decoder_trans_1__53,
       decoder_trans_1__54, decoder_trans_1__55, decoder_trans_1__56, decoder_trans_1__57,
       decoder_trans_1__58, decoder_trans_1__59, decoder_trans_1__60, decoder_trans_1__61,
       decoder_trans_1__62, decoder_trans_1__63, decoder_trans_1__64, decoder_trans_1__65,
       decoder_trans_1__66, decoder_trans_1__67, decoder_trans_1__68, decoder_trans_1__69,
       decoder_trans_1__70, decoder_trans_1__71, decoder_trans_1__72, decoder_trans_1__73,
       decoder_trans_1__74, decoder_trans_1__75, decoder_trans_1__76, decoder_trans_1__77,
       decoder_trans_1__78, decoder_trans_1__79, decoder_trans_1__80, decoder_trans_1__81,
       decoder_trans_1__82, decoder_trans_1__83, decoder_trans_1__84, decoder_trans_1__85,
       decoder_trans_1__86, decoder_trans_1__87, decoder_trans_1__88, decoder_trans_1__89,
       decoder_trans_1__90, decoder_trans_1__91, decoder_trans_1__92, decoder_trans_1__93,
       decoder_trans_1__94, decoder_trans_1__95, decoder_trans_1__96, decoder_trans_1__97,
       decoder_trans_1__98, decoder_trans_1__99, decoder_trans_1__100, decoder_trans_1__101,
       decoder_trans_1__102, decoder_trans_1__103, decoder_trans_1__104, decoder_trans_1__105,
       decoder_trans_1__106, decoder_trans_1__107, decoder_trans_1__108, decoder_trans_1__109,
       decoder_trans_1__110, decoder_trans_1__111, decoder_trans_1__112, decoder_trans_1__113,
       decoder_trans_1__114, decoder_trans_1__115, decoder_trans_1__116, decoder_trans_1__117,
       decoder_trans_1__118, decoder_trans_1__119, decoder_trans_1__120, decoder_trans_1__121,
       decoder_trans_1__122, decoder_trans_1__123, decoder_trans_1__124, decoder_trans_1__125,
       decoder_trans_1__126, decoder_trans_1__127, decoder_trans_1__128, decoder_trans_1_d0,
       decoder_trans_1_d1, decoder_trans_1_d2, decoder_trans_1_d3, decoder_trans_1_d4, decoder_trans_1_d5,
       EORS, extended_cycle_counter_1_nt2, extended_cycle_counter_1_nt3, extended_cycle_counter_1_nt4,
       extended_cycle_counter_1_nt5, irqp_latch_not_q, nACIN, nDAA, NDB_ADD, nDSA, not_1_out, not_2_out, nT6,
       nT7, ORS, P_DB, PCH_ADH, PCH_PCH, PCL_ADL, PCL_PCL, prdy_latch1_not_q, prdy_latch2_not_q,
       predecode_1_implied, predecode_1_ntwocycle, random_logic_1__0_adh0, random_logic_1__0_adh17,
       random_logic_1__0_adl0, random_logic_1__0_adl1, random_logic_1__0_adl2, random_logic_1__0_ir,
       random_logic_1_ac_db, random_logic_1_ac_sb, random_logic_1_add_adl, random_logic_1_add_sb06,
       random_logic_1_add_sb7, random_logic_1_dl_adh, random_logic_1_dl_adl, random_logic_1_dl_db,
       random_logic_1_fetch, random_logic_1_nready, random_logic_1_nt0, random_logic_1_nt1x,
       random_logic_1_pch_db, random_logic_1_pcl_db, random_logic_1_s_adl, random_logic_1_s_sb,
       random_logic_1_tres2, random_logic_1_x_sb, random_logic_1_y_sb, rd_latch_q, RESP, S_S, SB_AC, SB_ADD,
       SB_ADH, SB_DB, SB_S, SB_X, SB_Y, SRS, SUMS, T1, WR;
  wire [3:0] register_9_q, register_9_q_2;
  wire [7:0] AC, AD, and_1_out, and_2_out, bit_extender_1_out, bit_extender_2_out, bit_extender_3_out,
       bus_mux_1_adh, bus_mux_1_adh_2, bus_mux_1_adl, bus_mux_1_adl_2, bus_mux_1_db_2, bus_mux_1_db_3, DB,
       DL, or_1_out, pc_1_pch, pc_1_pcl, predecode_1_pd, register_5_q, register_7_q, register_8_q, S, SB, X,
       Y;

  buf buffer_1 (SYNC, T1);
  EXTENDED_CYCLE_COUNTER extended_cycle_counter_1 (
    .T1(T1), .nT2(extended_cycle_counter_1_nt2), .nT3(extended_cycle_counter_1_nt3),
    .nT4(extended_cycle_counter_1_nt4), .PHI1(PHI1), .nready(random_logic_1_nready),
    .TRES2(random_logic_1_tres2), .nT5(extended_cycle_counter_1_nt5), .PHI2(PHI2));
  D_Flip_Flop #(.trigger("high")) d_ff_1 (.clk(PHI2), .D(nNMI), .Q(d_ff_1_q));  // open: Qn, preset, en, reset
  DECODER_TRANS decoder_trans_1 (
    .nT5(extended_cycle_counter_1_nt5), .nT4(extended_cycle_counter_1_nt4),
    .nT3(extended_cycle_counter_1_nt3), .nT2(extended_cycle_counter_1_nt2), .IR0(register_9_q[0]),
    .IR1(register_9_q[1]), .IR7(register_9_q_2[3]), .IR4(register_9_q_2[0]), .IR3(register_9_q[3]),
    .IR2(register_9_q[2]), .IR6(register_9_q_2[2]), .IR5(register_9_q_2[1]), .nT0(random_logic_1_nt0),
    .nT1X(random_logic_1_nt1x), .d0(decoder_trans_1_d0), .d1(decoder_trans_1_d1), .d2(decoder_trans_1_d2),
    .d3(decoder_trans_1_d3), .d4(decoder_trans_1_d4), .d5(decoder_trans_1_d5), ._6(decoder_trans_1__6),
    ._7(decoder_trans_1__7), ._8(decoder_trans_1__8), ._9(decoder_trans_1__9), ._10(decoder_trans_1__10),
    ._11(decoder_trans_1__11), ._12(decoder_trans_1__12), ._13(decoder_trans_1__13),
    ._14(decoder_trans_1__14), ._15(decoder_trans_1__15), ._16(decoder_trans_1__16),
    ._17(decoder_trans_1__17), ._18(decoder_trans_1__18), ._19(decoder_trans_1__19),
    ._20(decoder_trans_1__20), ._21(decoder_trans_1__21), ._22(decoder_trans_1__22),
    ._23(decoder_trans_1__23), ._24(decoder_trans_1__24), ._25(decoder_trans_1__25),
    ._26(decoder_trans_1__26), ._27(decoder_trans_1__27), ._28(decoder_trans_1__28),
    ._29(decoder_trans_1__29), ._30(decoder_trans_1__30), ._31(decoder_trans_1__31),
    ._32(decoder_trans_1__32), ._33(decoder_trans_1__33), ._34(decoder_trans_1__34),
    ._35(decoder_trans_1__35), ._36(decoder_trans_1__36), ._37(decoder_trans_1__37),
    ._38(decoder_trans_1__38), ._39(decoder_trans_1__39), ._40(decoder_trans_1__40),
    ._41(decoder_trans_1__41), ._42(decoder_trans_1__42), ._43(decoder_trans_1__43),
    ._44(decoder_trans_1__44), ._45(decoder_trans_1__45), ._46(decoder_trans_1__46),
    ._47(decoder_trans_1__47), ._48(decoder_trans_1__48), ._49(decoder_trans_1__49),
    ._50(decoder_trans_1__50), ._51(decoder_trans_1__51), ._52(decoder_trans_1__52),
    ._53(decoder_trans_1__53), ._54(decoder_trans_1__54), ._55(decoder_trans_1__55),
    ._56(decoder_trans_1__56), ._57(decoder_trans_1__57), ._58(decoder_trans_1__58),
    ._59(decoder_trans_1__59), ._60(decoder_trans_1__60), ._61(decoder_trans_1__61),
    ._62(decoder_trans_1__62), ._63(decoder_trans_1__63), ._64(decoder_trans_1__64),
    ._65(decoder_trans_1__65), ._66(decoder_trans_1__66), ._67(decoder_trans_1__67),
    ._68(decoder_trans_1__68), ._69(decoder_trans_1__69), ._70(decoder_trans_1__70),
    ._71(decoder_trans_1__71), ._72(decoder_trans_1__72), ._73(decoder_trans_1__73),
    ._74(decoder_trans_1__74), ._75(decoder_trans_1__75), ._76(decoder_trans_1__76),
    ._77(decoder_trans_1__77), ._78(decoder_trans_1__78), ._79(decoder_trans_1__79),
    ._80(decoder_trans_1__80), ._81(decoder_trans_1__81), ._82(decoder_trans_1__82),
    ._83(decoder_trans_1__83), ._84(decoder_trans_1__84), ._85(decoder_trans_1__85),
    ._86(decoder_trans_1__86), ._87(decoder_trans_1__87), ._88(decoder_trans_1__88),
    ._89(decoder_trans_1__89), ._90(decoder_trans_1__90), ._91(decoder_trans_1__91),
    ._92(decoder_trans_1__92), ._93(decoder_trans_1__93), ._94(decoder_trans_1__94),
    ._95(decoder_trans_1__95), ._96(decoder_trans_1__96), ._97(decoder_trans_1__97),
    ._98(decoder_trans_1__98), ._99(decoder_trans_1__99), ._100(decoder_trans_1__100),
    ._101(decoder_trans_1__101), ._102(decoder_trans_1__102), ._103(decoder_trans_1__103),
    ._104(decoder_trans_1__104), ._105(decoder_trans_1__105), ._106(decoder_trans_1__106),
    ._107(decoder_trans_1__107), ._108(decoder_trans_1__108), ._109(decoder_trans_1__109),
    ._110(decoder_trans_1__110), ._111(decoder_trans_1__111), ._112(decoder_trans_1__112),
    ._113(decoder_trans_1__113), ._114(decoder_trans_1__114), ._115(decoder_trans_1__115),
    ._116(decoder_trans_1__116), ._117(decoder_trans_1__117), ._118(decoder_trans_1__118),
    ._119(decoder_trans_1__119), ._120(decoder_trans_1__120), ._121(decoder_trans_1__121),
    ._122(decoder_trans_1__122), ._123(decoder_trans_1__123), ._124(decoder_trans_1__124),
    ._125(decoder_trans_1__125), ._126(decoder_trans_1__126), ._127(decoder_trans_1__127),
    ._128(decoder_trans_1__128), .nPRDY(prdy_latch2_not_q));
  RANDOM_LOGIC random_logic_1 (
    .X0(decoder_trans_1_d0), .X1(decoder_trans_1_d1), .X2(decoder_trans_1_d2), .X3(decoder_trans_1_d3),
    .X4(decoder_trans_1_d4), .X5(decoder_trans_1_d5), .X6(decoder_trans_1__6), .X7(decoder_trans_1__7),
    .X8(decoder_trans_1__8), .X9(decoder_trans_1__9), .X10(decoder_trans_1__10), .X11(decoder_trans_1__11),
    .X12(decoder_trans_1__12), .X13(decoder_trans_1__13), .X14(decoder_trans_1__14),
    .X15(decoder_trans_1__15), .X16(decoder_trans_1__16), .X17(decoder_trans_1__17),
    .X18(decoder_trans_1__18), .X19(decoder_trans_1__19), .X20(decoder_trans_1__20),
    .X21(decoder_trans_1__21), .X22(decoder_trans_1__22), .X23(decoder_trans_1__23),
    .X24(decoder_trans_1__24), .X25(decoder_trans_1__25), .X26(decoder_trans_1__26),
    .X27(decoder_trans_1__27), .X28(decoder_trans_1__28), .X29(decoder_trans_1__29),
    .X30(decoder_trans_1__30), .X31(decoder_trans_1__31), .X32(decoder_trans_1__32),
    .X33(decoder_trans_1__33), .X34(decoder_trans_1__34), .X35(decoder_trans_1__35),
    .X36(decoder_trans_1__36), .X37(decoder_trans_1__37), .X38(decoder_trans_1__38),
    .X39(decoder_trans_1__39), .X40(decoder_trans_1__40), .X41(decoder_trans_1__41),
    .X42(decoder_trans_1__42), .X43(decoder_trans_1__43), .X44(decoder_trans_1__44),
    .X45(decoder_trans_1__45), .X46(decoder_trans_1__46), .X47(decoder_trans_1__47),
    .X48(decoder_trans_1__48), .X49(decoder_trans_1__49), .X50(decoder_trans_1__50),
    .X51(decoder_trans_1__51), .X52(decoder_trans_1__52), .X53(decoder_trans_1__53),
    .X54(decoder_trans_1__54), .X55(decoder_trans_1__55), .X56(decoder_trans_1__56),
    .X57(decoder_trans_1__57), .X58(decoder_trans_1__58), .X59(decoder_trans_1__59),
    .X60(decoder_trans_1__60), .X61(decoder_trans_1__61), .X62(decoder_trans_1__62),
    .X63(decoder_trans_1__63), .X64(decoder_trans_1__64), .X65(decoder_trans_1__65),
    .X66(decoder_trans_1__66), .X67(decoder_trans_1__67), .X68(decoder_trans_1__68),
    .X69(decoder_trans_1__69), .X70(decoder_trans_1__70), .X71(decoder_trans_1__71),
    .X72(decoder_trans_1__72), .X73(decoder_trans_1__73), .X74(decoder_trans_1__74),
    .X75(decoder_trans_1__75), .X76(decoder_trans_1__76), .X77(decoder_trans_1__77),
    .X78(decoder_trans_1__78), .X79(decoder_trans_1__79), .X80(decoder_trans_1__80),
    .X81(decoder_trans_1__81), .X82(decoder_trans_1__82), .X83(decoder_trans_1__83),
    .X84(decoder_trans_1__84), .X85(decoder_trans_1__85), .X86(decoder_trans_1__86),
    .X87(decoder_trans_1__87), .X88(decoder_trans_1__88), .X89(decoder_trans_1__89),
    .X90(decoder_trans_1__90), .X91(decoder_trans_1__91), .X92(decoder_trans_1__92),
    .X93(decoder_trans_1__93), .X94(decoder_trans_1__94), .X95(decoder_trans_1__95),
    .X96(decoder_trans_1__96), .X97(decoder_trans_1__97), .X98(decoder_trans_1__98),
    .X99(decoder_trans_1__99), .X100(decoder_trans_1__100), .X101(decoder_trans_1__101),
    .X102(decoder_trans_1__102), .X103(decoder_trans_1__103), .X104(decoder_trans_1__104),
    .X105(decoder_trans_1__105), .X106(decoder_trans_1__106), .X107(decoder_trans_1__107),
    .X108(decoder_trans_1__108), .X109(decoder_trans_1__109), .X110(decoder_trans_1__110),
    .X111(decoder_trans_1__111), .X112(decoder_trans_1__112), .X113(decoder_trans_1__113),
    .X114(decoder_trans_1__114), .X115(decoder_trans_1__115), .X116(decoder_trans_1__116),
    .X117(decoder_trans_1__117), .X118(decoder_trans_1__118), .X119(decoder_trans_1__119),
    .X120(decoder_trans_1__120), .X121(decoder_trans_1__121), .X122(decoder_trans_1__122),
    .X123(decoder_trans_1__123), .X124(decoder_trans_1__124), .X125(decoder_trans_1__125),
    .X126(decoder_trans_1__126), .X127(decoder_trans_1__127), .X128(decoder_trans_1__128), .nNMIP(d_ff_1_q),
    .nIRQP(irqp_latch_not_q), .RESP(RESP), .RDY(RDY), .nT0(random_logic_1_nt0), .nT1X(random_logic_1_nt1x),
    .PHI1(PHI1), .PHI2(PHI2), .nTWOCYCLE(predecode_1_ntwocycle), .IMPLIED(predecode_1_implied),
    .FETCH(random_logic_1_fetch), .WR(WR), .DB_IN(bus_mux_1_db_2), .AVR(AVR), .ADH_ABH(ADH_ABH),
    .ADL_ABL(ADL_ABL), .Y_SB(random_logic_1_y_sb), .X_SB(random_logic_1_x_sb),
    ._0_ADL0(random_logic_1__0_adl0), ._0_ADL1(random_logic_1__0_adl1), ._0_ADL2(random_logic_1__0_adl2),
    .SB_Y(SB_Y), .SB_X(SB_X), .S_SB(random_logic_1_s_sb), .S_ADL(random_logic_1_s_adl), .SB_S(SB_S),
    .S_S(S_S), ._0_IR(random_logic_1__0_ir), .NDB_ADD(NDB_ADD), .DB_ADD(DB_ADD), ._0_ADD(_0_ADD),
    .SB_ADD(SB_ADD), .ADL_ADD(ADL_ADD), .ANDS(ANDS), .EORS(EORS), .ORS(ORS), .nACIN(nACIN), .SUMS(SUMS),
    .nDAA(nDAA), .ADD_SB7(random_logic_1_add_sb7), .ADD_SB06(random_logic_1_add_sb06),
    .ADD_ADL(random_logic_1_add_adl), .nDSA(nDSA), .nIR5(not_2_out), .SB_AC(SB_AC),
    .AC_SB(random_logic_1_ac_sb), .DL_ADH(random_logic_1_dl_adh), .DL_DB(random_logic_1_dl_db),
    .DL_ADL(random_logic_1_dl_adl), ._0_ADH17(random_logic_1__0_adh17), .AC_DB(random_logic_1_ac_db),
    .SB_DB(SB_DB), .SB_ADH(SB_ADH), .SO(SO), .SRS(SRS), ._1_PC(_1_PC), .ADL_PCL(ADL_PCL), .PCL_PCL(PCL_PCL),
    .PCH_ADH(PCH_ADH), .PCL_ADL(PCL_ADL), .PCH_DB(random_logic_1_pch_db), .PCL_DB(random_logic_1_pcl_db),
    .P_DB(P_DB), .ADH_PCH(ADH_PCH), .PCH_PCH(PCH_PCH), .ACR(ACR), .T1(T1), .DB_OUT(FLAG),
    ._0_ADH0(random_logic_1__0_adh0), .TRES2(random_logic_1_tres2), .nREADY(random_logic_1_nready),
    .nT6(nT6), .nT7(nT7));
  BUS_MUX bus_mux_1 (
    .SB_DB(SB_DB), .DL_DB(random_logic_1_dl_db), .PCL_DB(random_logic_1_pcl_db),
    .PCH_DB(random_logic_1_pch_db), .P_DB(P_DB), .AC_DB(random_logic_1_ac_db), .ACC_DATA(AC),
    .FLAG_DATA(FLAG), .DL(DL), .X_SB(random_logic_1_x_sb), .Y_SB(random_logic_1_y_sb),
    .S_SB(random_logic_1_s_sb), .SB_ADH(SB_ADH), .AC_SB(random_logic_1_ac_sb),
    .ADD_SB06(random_logic_1_add_sb06), .ADD_SB7(random_logic_1_add_sb7), .ADD_DATA(AD), .S_REG(S),
    .Y_REG(Y), .X_REG(X), .S_ADL(random_logic_1_s_adl), .DL_ADL(random_logic_1_dl_adl),
    .ADD_ADL(random_logic_1_add_adl), .PCL_ADL(PCL_ADL), ._0_ADL0(random_logic_1__0_adl0),
    ._0_ADL1(random_logic_1__0_adl1), ._0_ADL2(random_logic_1__0_adl2), .PCL_DATA(pc_1_pcl),
    .DL_ADH(random_logic_1_dl_adh), .PCH_ADH(PCH_ADH), ._0_ADH0(random_logic_1__0_adh0),
    ._0_ADH17(random_logic_1__0_adh17), .PCH_DATA(pc_1_pch), .DB(DB), .SB(SB), .ADL(bus_mux_1_adl),
    .ADH(bus_mux_1_adh), .ADL_2(bus_mux_1_adl_2), .ADH_2(bus_mux_1_adh_2), .DB_2(bus_mux_1_db_2),
    .DB_3(bus_mux_1_db_3));
  D_Flip_Flop #(.trigger("high")) d_ff_2 (.clk(PHI2), .D(nIRQ), .Qn(d_ff_2_qn));  // open: Q, preset, en, reset
  Register #(.trigger("high")) register_1 (
    .D(bus_mux_1_adl), .en(ADL_ABL), .Q({A7, A6, A5, A4, A3, A2, A1, A0}), .clk(PHI1));  // open: clr
  Register #(.trigger("high")) register_2 (
    .D(bus_mux_1_adh), .en(ADH_ABH), .Q({A15, A14, A13, A12, A11, A10, A9, A8}), .clk(PHI1));  // open: clr
  D_Latch irqp_latch (.EN(PHI1), .D(d_ff_2_qn), .NOT_Q(irqp_latch_not_q));  // open: Q
  assign bit_extender_1_out = {{7{S_S}}, S_S};  // Bit_Extender bit_extender_1
  assign bit_extender_2_out = {{7{SB_S}}, SB_S};  // Bit_Extender bit_extender_2
  assign and_1_out = S & bit_extender_1_out;  // AND_Gate and_1, 8 bits wide
  assign or_1_out = and_1_out | and_2_out;  // OR_Gate or_1, 8 bits wide
  assign and_2_out = SB & bit_extender_2_out;  // AND_Gate and_2, 8 bits wide
  Register #(.trigger("high")) register_3 (.D(SB), .en(SB_X), .Q(X), .clk(PHI1));  // open: clr
  Register #(.trigger("high")) register_4 (.D(SB), .en(SB_Y), .Q(Y), .clk(PHI1));  // open: clr
  Register #(.trigger("high")) register_5 (.D(or_1_out), .Q(register_5_q), .clk(PHI1));  // open: en, clr
  Register #(.trigger("high")) register_6 (.D(register_5_q), .Q(S), .clk(PHI2));  // open: en, clr
  not not_1 (not_1_out, RDY);
  D_Latch prdy_latch1 (.EN(PHI2), .D(not_1_out), .NOT_Q(prdy_latch1_not_q));  // open: Q
  ALU alu_1 (
    .PHI2(PHI2), .NDB_ADD(NDB_ADD), .DB_ADD(DB_ADD), ._0_ADD(_0_ADD), .SB_ADD(SB_ADD), .ADL_ADD(ADL_ADD),
    .ANDS(ANDS), .EORS(EORS), .ORS(ORS), .SRS(SRS), .SUMS(SUMS), .SB_AC(SB_AC), .nACIN(nACIN), .nDAA(nDAA),
    .nDSA(nDSA), .ADL_IN(bus_mux_1_adl_2), .ACR(ACR), .AVR(AVR), .ACC(AC), .ADD(AD), .SB_IN(SB),
    .DB_IN(bus_mux_1_db_3), .PHI1(PHI1));
  D_Flip_Flop #(.trigger("high")) d_ff_3 (.clk(PHI2), .D(nRES), .Q(d_ff_3_q));  // open: Qn, preset, en, reset
  D_Latch prdy_latch2 (.EN(PHI1), .D(prdy_latch1_not_q), .NOT_Q(prdy_latch2_not_q));  // open: Q
  Hex_Digit_Display hex_digit_display_1 (.value({A15, A14, A13, A12}));  // open: dp
  Hex_Digit_Display hex_digit_display_2 (.value({A11, A10, A9, A8}));  // open: dp
  Hex_Digit_Display hex_digit_display_3 (.value({A7, A6, A5, A4}));  // open: dp
  Counter #(.width(32), .max('hffffffff)) counter_1 (.clk(T1), .clr(RESP));  // open: load, D, count, Q, carry
  D_Latch resp_latch (.EN(PHI1), .D(d_ff_3_q), .NOT_Q(RESP));  // open: Q
  Hex_Digit_Display hex_digit_display_4 (.value({A3, A2, A1, A0}));  // open: dp
  PC pc_1 (
    .PHI2(PHI2), .ADH_PCH(ADH_PCH), .PCH_PCH(PCH_PCH), .ADL_PCL(ADL_PCL), .PCL_PCL(PCL_PCL), ._1_PC(_1_PC),
    .PCL(pc_1_pcl), .PCH(pc_1_pch), .ADH_IN(bus_mux_1_adh_2), .ADL_IN(bus_mux_1_adl_2), .PHI1(PHI1));
  // Probe on X
  // Probe on Y
  // Probe on S
  // Probe on DL
  // Probe on AC
  // Probe on AD
  // Probe on FLAG
  LED led_1 (.in(P_DB));
  // Probe on DB
  LED led_2 (.in(SB_DB));
  // Probe on SB
  LED led_3 (.in(SB_ADH));
  // Probe on bus_mux_1_adh_2
  // Probe on bus_mux_1_adl_2
  LED led_4 (.in(PCH_ADH));
  LED led_5 (.in(PCL_ADL));
  LED C (.in(FLAG[0]));
  LED Z (.in(FLAG[1]));
  LED I (.in(FLAG[2]));
  LED D (.in(FLAG[3]));
  LED B (.in(FLAG[4]));
  LED V (.in(FLAG[6]));
  LED N (.in(FLAG[7]));
  CLOCKGEN clockgen_1 (.PHI0(PHI0), .PHI2(PHI2), .PHI1(PHI1));
  not not_2 (not_2_out, register_9_q_2[1]);
  // Probe on pc_1_pch
  // Probe on pc_1_pcl
  Hex_Digit_Display hex_digit_display_5 (.value(register_9_q_2));  // open: dp
  PREDECODE predecode_1 (
    .PHI2(PHI2), ._0_IR(random_logic_1__0_ir), .D0(D0), .D1(D1), .D2(D2), .D3(D3), .D4(D4), .D5(D5), .D6(D6),
    .D7(D7), .PD(predecode_1_pd), .IMPLIED(predecode_1_implied), .nTWOCYCLE(predecode_1_ntwocycle));
  Register #(.trigger("high")) register_7 (
    .D({D7, D6, D5, D4, D3, D2, D1, D0}), .Q(register_7_q), .clk(PHI2));  // open: en, clr
  Bit_Extender #(.in_width(1), .out_width(8), .\type ("sign")) bit_extender_3 (.out(bit_extender_3_out));  // open: in
  D_Latch rd_latch (.EN(PHI1), .D(WR), .Q(rd_latch_q));  // open: NOT_Q
  Register #(.trigger("high")) register_8 (.D(DB), .Q(register_8_q), .clk(PHI1));  // open: en, clr
  D_Latch RWLatch (.EN(PHI1), .D(WR), .NOT_Q(R_W));  // open: Q
  Hex_Digit_Display hex_digit_display_6 (.value(register_9_q));  // open: dp
  Register #(.trigger("high")) register_9 (
    .D(predecode_1_pd), .en(random_logic_1_fetch), .Q({register_9_q_2, register_9_q}), .clk(PHI1));  // open: clr
  Register #(.trigger("high")) register_10 (.D(register_7_q), .Q(DL), .clk(PHI1));  // open: en, clr
  // AND_Gate and_3 has open pins: in1=bit_extender_3_out, out=open
  assign {D7_2, D6_2, D5_2, D4_2, D3_2, D2_2, D1_2, D0_2} = rd_latch_q ? register_8_q : 8'bz;  // Controlled_Buffer controlled_buffer_1

  // Other names for the same wires on the sheet: P[7:0] = FLAG

  // Notes on the sheet:
  //   D0_2: pull=down
  //   D5_2: pull=down
  //   D4: pull=down
  //   D2: pull=down
  //   D3: pull=down
  //   D0: pull=down
  //   D6: pull=down
  //   D5: pull=down
  //   D4_2: pull=down
  //   D6_2: pull=down
  //   D7_2: pull=down
  //   D1_2: pull=down
  //   FLAG: pull=down
  //   D2_2: pull=down
  //   D1: pull=down
  //   D3_2: pull=down
  //   D7: pull=down
  //   PHI2
  //   PHI1
  //   The pin layout corresponds to the real chip
  //   PHI1
  //   PHI2
  //   /NMIP
  //   /IRQP
  //   REGS
  //   X
  //   Y
  //   STACK POINTER
  //   /PRDY
  //   CURRENT ADDRESS
  //   INSTR COUNTER
  //   RESP
  //   PHI2
  //   PHI1
  //   DL
  //   DOR
  //   OPCODE
  //   IR
  //   PHI1
  //   PHI2
endmodule

module CLOCKGEN (
  input  PHI0,
  output PHI2,
  output PHI1
);

  wire not_1_out;

  not not_1 (not_1_out, PHI0);
  not not_2 (PHI1, PHI0);
  not not_3 (PHI2, not_1_out);
endmodule

// DECODER
module DECODER_TRANS (
  input  nT5,
  input  nT4,
  input  nT3,
  input  nT2,
  input  IR0,
  input  IR1,
  input  IR7,
  input  IR4,
  input  IR3,
  input  IR2,
  input  IR6,
  input  IR5,
  input  nT0,
  input  nT1X,
  input  nPRDY,
  output d0,
  output d1,
  output d2,
  output d3,
  output d4,
  output d5,
  output _6,
  output _7,
  output _8,
  output _9,
  output _10,
  output _11,
  output _12,
  output _13,
  output _14,
  output _15,
  output _16,
  output _17,
  output _18,
  output _19,
  output _20,
  output _21,
  output _22,
  output _23,
  output _24,
  output _25,
  output _26,
  output _27,
  output _28,
  output _29,
  output _30,
  output _31,
  output _32,
  output _33,
  output _34,
  output _35,
  output _36,
  output _37,
  output _38,
  output _39,
  output _40,
  output _41,
  output _42,
  output _43,
  output _44,
  output _45,
  output _46,
  output _47,
  output _48,
  output _49,
  output _50,
  output _51,
  output _52,
  output _53,
  output _54,
  output _55,
  output _56,
  output _57,
  output _58,
  output _59,
  output _60,
  output _61,
  output _62,
  output _63,
  output _64,
  output _65,
  output _66,
  output _67,
  output _68,
  output _69,
  output _70,
  output _71,
  output _72,
  output _73,
  output _74,
  output _75,
  output _76,
  output _77,
  output _78,
  output _79,
  output _80,
  output _81,
  output _82,
  output _83,
  output _84,
  output _85,
  output _86,
  output _87,
  output _88,
  output _89,
  output _90,
  output _91,
  output _92,
  output _93,
  output _94,
  output _95,
  output _96,
  output _97,
  output _98,
  output _99,
  output _100,
  output _101,
  output _102,
  output _103,
  output _104,
  output _105,
  output _106,
  output _107,
  output _108,
  output _109,
  output _110,
  output _111,
  output _112,
  output _113,
  output _114,
  output _115,
  output _116,
  output _117,
  output _118,
  output _119,
  output _120,
  output _121,
  output _122,
  output _123,
  output _124,
  output _125,
  output _126,
  output _127,
  output _128
);

  wire not_1_out, not_2_out, not_3_out, not_4_out, not_5_out, not_6_out, not_7_out, not_8_out, or_1_out,
       pull_resistor_121_node;

  not not_1 (not_1_out, IR1);
  or or_1 (or_1_out, IR1, IR0);
  not not_2 (not_2_out, IR0);
  not not_3 (not_3_out, IR7);
  not not_4 (not_4_out, IR4);
  not not_5 (not_5_out, IR3);
  not not_6 (not_6_out, IR2);
  not not_7 (not_7_out, IR6);
  not not_8 (not_8_out, IR5);
  Pull_Resistor #(.pull(1)) pull_resistor_1 (.node(d1));
  Pull_Resistor #(.pull(1)) pull_resistor_2 (.node(d0));
  Transistor #(.\type ("n")) transistor_1 (.in(1'b0), .out(d1), .gate(nT3));
  Transistor #(.\type ("n")) transistor_2 (.in(1'b0), .out(d0), .gate(or_1_out));
  Transistor #(.\type ("n")) transistor_3 (.in(1'b0), .out(d1), .gate(not_2_out));
  Transistor #(.\type ("n")) transistor_4 (.in(1'b0), .out(d0), .gate(not_3_out));
  Transistor #(.\type ("n")) transistor_5 (.in(1'b0), .out(d1), .gate(not_4_out));
  Transistor #(.\type ("n")) transistor_6 (.in(1'b0), .out(d1), .gate(IR3));
  Transistor #(.\type ("n")) transistor_7 (.in(1'b0), .out(d1), .gate(IR2));
  Transistor #(.\type ("n")) transistor_8 (.in(1'b0), .out(d0), .gate(not_6_out));
  Transistor #(.\type ("n")) transistor_9 (.in(1'b0), .out(d0), .gate(IR6));
  Transistor #(.\type ("n")) transistor_10 (.in(1'b0), .out(d0), .gate(IR5));
  Pull_Resistor #(.pull(1)) pull_resistor_3 (.node(d2));
  Transistor #(.\type ("n")) transistor_11 (.in(1'b0), .out(d2), .gate(nT2));
  Transistor #(.\type ("n")) transistor_12 (.in(1'b0), .out(d2), .gate(not_2_out));
  Transistor #(.\type ("n")) transistor_13 (.in(1'b0), .out(d2), .gate(not_4_out));
  Transistor #(.\type ("n")) transistor_14 (.in(1'b0), .out(d2), .gate(not_5_out));
  Transistor #(.\type ("n")) transistor_15 (.in(1'b0), .out(d2), .gate(IR2));
  Pull_Resistor #(.pull(1)) pull_resistor_4 (.node(d3));
  Transistor #(.\type ("n")) transistor_16 (.in(1'b0), .out(d3), .gate(or_1_out));
  Transistor #(.\type ("n")) transistor_17 (.in(1'b0), .out(d3), .gate(not_3_out));
  Transistor #(.\type ("n")) transistor_18 (.in(1'b0), .out(d3), .gate(IR4));
  Transistor #(.\type ("n")) transistor_19 (.in(1'b0), .out(d3), .gate(not_5_out));
  Transistor #(.\type ("n")) transistor_20 (.in(1'b0), .out(d3), .gate(IR2));
  Transistor #(.\type ("n")) transistor_21 (.in(1'b0), .out(d3), .gate(IR5));
  Transistor #(.\type ("n")) transistor_22 (.in(1'b0), .out(d3), .gate(nT0));
  Pull_Resistor #(.pull(1)) pull_resistor_5 (.node(d4));
  Pull_Resistor #(.pull(1)) pull_resistor_6 (.node(d5));
  Transistor #(.\type ("n")) transistor_23 (.in(1'b0), .out(d4), .gate(or_1_out));
  Transistor #(.\type ("n")) transistor_24 (.in(1'b0), .out(d5), .gate(or_1_out));
  Transistor #(.\type ("n")) transistor_25 (.in(1'b0), .out(d5), .gate(not_3_out));
  Transistor #(.\type ("n")) transistor_26 (.in(1'b0), .out(d4), .gate(not_3_out));
  Transistor #(.\type ("n")) transistor_27 (.in(1'b0), .out(d5), .gate(IR4));
  Transistor #(.\type ("n")) transistor_28 (.in(1'b0), .out(d4), .gate(not_4_out));
  Transistor #(.\type ("n")) transistor_29 (.in(1'b0), .out(d4), .gate(not_5_out));
  Transistor #(.\type ("n")) transistor_30 (.in(1'b0), .out(d4), .gate(IR2));
  Transistor #(.\type ("n")) transistor_31 (.in(1'b0), .out(d4), .gate(IR6));
  Transistor #(.\type ("n")) transistor_32 (.in(1'b0), .out(d5), .gate(not_7_out));
  Transistor #(.\type ("n")) transistor_33 (.in(1'b0), .out(d4), .gate(IR5));
  Transistor #(.\type ("n")) transistor_34 (.in(1'b0), .out(d5), .gate(IR5));
  Transistor #(.\type ("n")) transistor_35 (.in(1'b0), .out(d5), .gate(nT0));
  Transistor #(.\type ("n")) transistor_36 (.in(1'b0), .out(d4), .gate(nT0));
  Pull_Resistor #(.pull(1)) pull_resistor_7 (.node(_6));
  Transistor #(.\type ("n")) transistor_37 (.in(1'b0), .out(_6), .gate(nT2));
  Transistor #(.\type ("n")) transistor_38 (.in(1'b0), .out(_6), .gate(not_4_out));
  Transistor #(.\type ("n")) transistor_39 (.in(1'b0), .out(_6), .gate(not_6_out));
  Pull_Resistor #(.pull(1)) pull_resistor_8 (.node(_7));
  Transistor #(.\type ("n")) transistor_40 (.in(1'b0), .out(_7), .gate(not_1_out));
  Transistor #(.\type ("n")) transistor_41 (.in(1'b0), .out(_7), .gate(not_3_out));
  Transistor #(.\type ("n")) transistor_42 (.in(1'b0), .out(_7), .gate(IR6));
  Pull_Resistor #(.pull(1)) pull_resistor_9 (.node(_9));
  Pull_Resistor #(.pull(1)) pull_resistor_10 (.node(_8));
  Transistor #(.\type ("n")) transistor_43 (.in(1'b0), .out(_8), .gate(nT2));
  Transistor #(.\type ("n")) transistor_44 (.in(1'b0), .out(_9), .gate(not_1_out));
  Transistor #(.\type ("n")) transistor_45 (.in(1'b0), .out(_8), .gate(not_2_out));
  Transistor #(.\type ("n")) transistor_46 (.in(1'b0), .out(_9), .gate(not_3_out));
  Transistor #(.\type ("n")) transistor_47 (.in(1'b0), .out(_8), .gate(IR4));
  Transistor #(.\type ("n")) transistor_48 (.in(1'b0), .out(_9), .gate(IR4));
  Transistor #(.\type ("n")) transistor_49 (.in(1'b0), .out(_8), .gate(IR3));
  Transistor #(.\type ("n")) transistor_50 (.in(1'b0), .out(_9), .gate(not_5_out));
  Transistor #(.\type ("n")) transistor_51 (.in(1'b0), .out(_8), .gate(IR2));
  Transistor #(.\type ("n")) transistor_52 (.in(1'b0), .out(_9), .gate(IR2));
  Transistor #(.\type ("n")) transistor_53 (.in(1'b0), .out(_9), .gate(IR6));
  Transistor #(.\type ("n")) transistor_54 (.in(1'b0), .out(_9), .gate(IR5));
  Transistor #(.\type ("n")) transistor_55 (.in(1'b0), .out(_9), .gate(nT0));
  Pull_Resistor #(.pull(1)) pull_resistor_11 (.node(_10));
  Transistor #(.\type ("n")) transistor_56 (.in(1'b0), .out(_10), .gate(not_1_out));
  Transistor #(.\type ("n")) transistor_57 (.in(1'b0), .out(_10), .gate(not_3_out));
  Transistor #(.\type ("n")) transistor_58 (.in(1'b0), .out(_10), .gate(IR4));
  Transistor #(.\type ("n")) transistor_59 (.in(1'b0), .out(_10), .gate(not_5_out));
  Transistor #(.\type ("n")) transistor_60 (.in(1'b0), .out(_10), .gate(IR2));
  Transistor #(.\type ("n")) transistor_61 (.in(1'b0), .out(_10), .gate(not_7_out));
  Transistor #(.\type ("n")) transistor_62 (.in(1'b0), .out(_10), .gate(IR5));
  Transistor #(.\type ("n")) transistor_63 (.in(1'b0), .out(_10), .gate(nT0));
  Pull_Resistor #(.pull(1)) pull_resistor_12 (.node(_11));
  Transistor #(.\type ("n")) transistor_64 (.in(1'b0), .out(_11), .gate(or_1_out));
  Transistor #(.\type ("n")) transistor_65 (.in(1'b0), .out(_11), .gate(not_3_out));
  Transistor #(.\type ("n")) transistor_66 (.in(1'b0), .out(_11), .gate(IR4));
  Transistor #(.\type ("n")) transistor_67 (.in(1'b0), .out(_11), .gate(not_7_out));
  Transistor #(.\type ("n")) transistor_68 (.in(1'b0), .out(_11), .gate(not_8_out));
  Transistor #(.\type ("n")) transistor_69 (.in(1'b0), .out(_11), .gate(nT0));
  Pull_Resistor #(.pull(1)) pull_resistor_13 (.node(_13));
  Pull_Resistor #(.pull(1)) pull_resistor_14 (.node(_12));
  Transistor #(.\type ("n")) transistor_70 (.in(1'b0), .out(_13), .gate(not_1_out));
  Transistor #(.\type ("n")) transistor_71 (.in(1'b0), .out(_12), .gate(not_1_out));
  Transistor #(.\type ("n")) transistor_72 (.in(1'b0), .out(_12), .gate(not_3_out));
  Transistor #(.\type ("n")) transistor_73 (.in(1'b0), .out(_13), .gate(not_3_out));
  Transistor #(.\type ("n")) transistor_74 (.in(1'b0), .out(_13), .gate(not_4_out));
  Transistor #(.\type ("n")) transistor_75 (.in(1'b0), .out(_13), .gate(not_5_out));
  Transistor #(.\type ("n")) transistor_76 (.in(1'b0), .out(_13), .gate(IR2));
  Transistor #(.\type ("n")) transistor_77 (.in(1'b0), .out(_12), .gate(IR6));
  Transistor #(.\type ("n")) transistor_78 (.in(1'b0), .out(_13), .gate(IR6));
  Transistor #(.\type ("n")) transistor_79 (.in(1'b0), .out(_13), .gate(IR5));
  Transistor #(.\type ("n")) transistor_80 (.in(1'b0), .out(_12), .gate(IR5));
  Transistor #(.\type ("n")) transistor_81 (.in(1'b0), .out(_13), .gate(nT0));
  Pull_Resistor #(.pull(1)) pull_resistor_15 (.node(_14));
  Transistor #(.\type ("n")) transistor_82 (.in(1'b0), .out(_14), .gate(not_1_out));
  Transistor #(.\type ("n")) transistor_83 (.in(1'b0), .out(_14), .gate(not_3_out));
  Transistor #(.\type ("n")) transistor_84 (.in(1'b0), .out(_14), .gate(IR6));
  Transistor #(.\type ("n")) transistor_85 (.in(1'b0), .out(_14), .gate(not_8_out));
  Transistor #(.\type ("n")) transistor_86 (.in(1'b0), .out(_14), .gate(nT0));
  Pull_Resistor #(.pull(1)) pull_resistor_16 (.node(_15));
  Transistor #(.\type ("n")) transistor_87 (.in(1'b0), .out(_15), .gate(not_1_out));
  Transistor #(.\type ("n")) transistor_88 (.in(1'b0), .out(_15), .gate(not_3_out));
  Transistor #(.\type ("n")) transistor_89 (.in(1'b0), .out(_15), .gate(IR4));
  Transistor #(.\type ("n")) transistor_90 (.in(1'b0), .out(_15), .gate(not_5_out));
  Transistor #(.\type ("n")) transistor_91 (.in(1'b0), .out(_15), .gate(IR2));
  Transistor #(.\type ("n")) transistor_92 (.in(1'b0), .out(_15), .gate(not_7_out));
  Transistor #(.\type ("n")) transistor_93 (.in(1'b0), .out(_15), .gate(IR5));
  Transistor #(.\type ("n")) transistor_94 (.in(1'b0), .out(_15), .gate(nT1X));
  Pull_Resistor #(.pull(1)) pull_resistor_17 (.node(_16));
  Pull_Resistor #(.pull(1)) pull_resistor_18 (.node(_17));
  Transistor #(.\type ("n")) transistor_95 (.in(1'b0), .out(_17), .gate(not_1_out));
  Transistor #(.\type ("n")) transistor_96 (.in(1'b0), .out(_16), .gate(or_1_out));
  Transistor #(.\type ("n")) transistor_97 (.in(1'b0), .out(_16), .gate(not_3_out));
  Transistor #(.\type ("n")) transistor_98 (.in(1'b0), .out(_17), .gate(not_3_out));
  Transistor #(.\type ("n")) transistor_99 (.in(1'b0), .out(_16), .gate(IR4));
  Transistor #(.\type ("n")) transistor_100 (.in(1'b0), .out(_17), .gate(not_4_out));
  Transistor #(.\type ("n")) transistor_101 (.in(1'b0), .out(_17), .gate(not_5_out));
  Transistor #(.\type ("n")) transistor_102 (.in(1'b0), .out(_16), .gate(not_5_out));
  Transistor #(.\type ("n")) transistor_103 (.in(1'b0), .out(_16), .gate(IR2));
  Transistor #(.\type ("n")) transistor_104 (.in(1'b0), .out(_17), .gate(IR2));
  Transistor #(.\type ("n")) transistor_105 (.in(1'b0), .out(_17), .gate(IR6));
  Transistor #(.\type ("n")) transistor_106 (.in(1'b0), .out(_16), .gate(not_7_out));
  Transistor #(.\type ("n")) transistor_107 (.in(1'b0), .out(_16), .gate(not_8_out));
  Transistor #(.\type ("n")) transistor_108 (.in(1'b0), .out(_17), .gate(not_8_out));
  Transistor #(.\type ("n")) transistor_109 (.in(1'b0), .out(_17), .gate(nT0));
  Transistor #(.\type ("n")) transistor_110 (.in(1'b0), .out(_16), .gate(nT1X));
  Pull_Resistor #(.pull(1)) pull_resistor_19 (.node(_18));
  Transistor #(.\type ("n")) transistor_111 (.in(1'b0), .out(_18), .gate(or_1_out));
  Transistor #(.\type ("n")) transistor_112 (.in(1'b0), .out(_18), .gate(not_3_out));
  Transistor #(.\type ("n")) transistor_113 (.in(1'b0), .out(_18), .gate(IR4));
  Transistor #(.\type ("n")) transistor_114 (.in(1'b0), .out(_18), .gate(not_5_out));
  Transistor #(.\type ("n")) transistor_115 (.in(1'b0), .out(_18), .gate(IR2));
  Transistor #(.\type ("n")) transistor_116 (.in(1'b0), .out(_18), .gate(IR5));
  Transistor #(.\type ("n")) transistor_117 (.in(1'b0), .out(_18), .gate(nT1X));
  Pull_Resistor #(.pull(1)) pull_resistor_20 (.node(_19));
  Transistor #(.\type ("n")) transistor_118 (.in(1'b0), .out(_19), .gate(or_1_out));
  Transistor #(.\type ("n")) transistor_119 (.in(1'b0), .out(_19), .gate(not_3_out));
  Transistor #(.\type ("n")) transistor_120 (.in(1'b0), .out(_19), .gate(not_6_out));
  Transistor #(.\type ("n")) transistor_121 (.in(1'b0), .out(_19), .gate(IR6));
  Transistor #(.\type ("n")) transistor_122 (.in(1'b0), .out(_19), .gate(not_8_out));
  Transistor #(.\type ("n")) transistor_123 (.in(1'b0), .out(_19), .gate(nT0));
  Pull_Resistor #(.pull(1)) pull_resistor_21 (.node(_20));
  Transistor #(.\type ("n")) transistor_124 (.in(1'b0), .out(_20), .gate(or_1_out));
  Transistor #(.\type ("n")) transistor_125 (.in(1'b0), .out(_20), .gate(not_3_out));
  Transistor #(.\type ("n")) transistor_126 (.in(1'b0), .out(_20), .gate(IR4));
  Transistor #(.\type ("n")) transistor_127 (.in(1'b0), .out(_20), .gate(IR6));
  Transistor #(.\type ("n")) transistor_128 (.in(1'b0), .out(_20), .gate(not_8_out));
  Transistor #(.\type ("n")) transistor_129 (.in(1'b0), .out(_20), .gate(nT0));
  Pull_Resistor #(.pull(1)) pull_resistor_22 (.node(_21));
  Transistor #(.\type ("n")) transistor_130 (.in(1'b0), .out(_21), .gate(or_1_out));
  Transistor #(.\type ("n")) transistor_131 (.in(1'b0), .out(_21), .gate(IR7));
  Transistor #(.\type ("n")) transistor_132 (.in(1'b0), .out(_21), .gate(IR4));
  Transistor #(.\type ("n")) transistor_133 (.in(1'b0), .out(_21), .gate(IR3));
  Transistor #(.\type ("n")) transistor_134 (.in(1'b0), .out(_21), .gate(IR2));
  Transistor #(.\type ("n")) transistor_135 (.in(1'b0), .out(_21), .gate(IR6));
  Transistor #(.\type ("n")) transistor_136 (.in(1'b0), .out(_21), .gate(not_8_out));
  Transistor #(.\type ("n")) transistor_137 (.in(1'b0), .out(_21), .gate(nT0));
  Pull_Resistor #(.pull(1)) pull_resistor_23 (.node(_22));
  Transistor #(.\type ("n")) transistor_138 (.in(1'b0), .out(_22), .gate(nT5));
  Transistor #(.\type ("n")) transistor_139 (.in(1'b0), .out(_22), .gate(or_1_out));
  Transistor #(.\type ("n")) transistor_140 (.in(1'b0), .out(_22), .gate(IR7));
  Transistor #(.\type ("n")) transistor_141 (.in(1'b0), .out(_22), .gate(IR4));
  Transistor #(.\type ("n")) transistor_142 (.in(1'b0), .out(_22), .gate(IR3));
  Transistor #(.\type ("n")) transistor_143 (.in(1'b0), .out(_22), .gate(IR2));
  Transistor #(.\type ("n")) transistor_144 (.in(1'b0), .out(_22), .gate(IR6));
  Transistor #(.\type ("n")) transistor_145 (.in(1'b0), .out(_22), .gate(IR5));
  Pull_Resistor #(.pull(1)) pull_resistor_24 (.node(_23));
  Transistor #(.\type ("n")) transistor_146 (.in(1'b0), .out(_23), .gate(or_1_out));
  Transistor #(.\type ("n")) transistor_147 (.in(1'b0), .out(_23), .gate(IR7));
  Transistor #(.\type ("n")) transistor_148 (.in(1'b0), .out(_23), .gate(IR4));
  Transistor #(.\type ("n")) transistor_149 (.in(1'b0), .out(_23), .gate(not_5_out));
  Transistor #(.\type ("n")) transistor_150 (.in(1'b0), .out(_23), .gate(IR2));
  Transistor #(.\type ("n")) transistor_151 (.in(1'b0), .out(_23), .gate(IR5));
  Transistor #(.\type ("n")) transistor_152 (.in(1'b0), .out(_23), .gate(nT0));
  Pull_Resistor #(.pull(1)) pull_resistor_25 (.node(_24));
  Pull_Resistor #(.pull(1)) pull_resistor_26 (.node(_25));
  Transistor #(.\type ("n")) transistor_153 (.in(1'b0), .out(_24), .gate(nT4));
  Transistor #(.\type ("n")) transistor_154 (.in(1'b0), .out(_25), .gate(nT3));
  Transistor #(.\type ("n")) transistor_155 (.in(1'b0), .out(_25), .gate(or_1_out));
  Transistor #(.\type ("n")) transistor_156 (.in(1'b0), .out(_24), .gate(or_1_out));
  Transistor #(.\type ("n")) transistor_157 (.in(1'b0), .out(_24), .gate(IR7));
  Transistor #(.\type ("n")) transistor_158 (.in(1'b0), .out(_25), .gate(IR7));
  Transistor #(.\type ("n")) transistor_159 (.in(1'b0), .out(_24), .gate(IR4));
  Transistor #(.\type ("n")) transistor_160 (.in(1'b0), .out(_25), .gate(IR4));
  Transistor #(.\type ("n")) transistor_161 (.in(1'b0), .out(_24), .gate(IR3));
  Transistor #(.\type ("n")) transistor_162 (.in(1'b0), .out(_25), .gate(not_5_out));
  Transistor #(.\type ("n")) transistor_163 (.in(1'b0), .out(_24), .gate(IR2));
  Transistor #(.\type ("n")) transistor_164 (.in(1'b0), .out(_25), .gate(IR2));
  Transistor #(.\type ("n")) transistor_165 (.in(1'b0), .out(_24), .gate(not_7_out));
  Transistor #(.\type ("n")) transistor_166 (.in(1'b0), .out(_24), .gate(not_8_out));
  Transistor #(.\type ("n")) transistor_167 (.in(1'b0), .out(_25), .gate(not_8_out));
  Pull_Resistor #(.pull(1)) pull_resistor_27 (.node(_26));
  Transistor #(.\type ("n")) transistor_168 (.in(1'b0), .out(_26), .gate(nT5));
  Transistor #(.\type ("n")) transistor_169 (.in(1'b0), .out(_26), .gate(or_1_out));
  Transistor #(.\type ("n")) transistor_170 (.in(1'b0), .out(_26), .gate(IR7));
  Transistor #(.\type ("n")) transistor_171 (.in(1'b0), .out(_26), .gate(IR4));
  Transistor #(.\type ("n")) transistor_172 (.in(1'b0), .out(_26), .gate(IR3));
  Transistor #(.\type ("n")) transistor_173 (.in(1'b0), .out(_26), .gate(IR2));
  Transistor #(.\type ("n")) transistor_174 (.in(1'b0), .out(_26), .gate(not_7_out));
  Transistor #(.\type ("n")) transistor_175 (.in(1'b0), .out(_26), .gate(IR5));
  Pull_Resistor #(.pull(1)) pull_resistor_28 (.node(_27));
  Transistor #(.\type ("n")) transistor_176 (.in(1'b0), .out(_27), .gate(not_1_out));
  Transistor #(.\type ("n")) transistor_177 (.in(1'b0), .out(_27), .gate(IR7));
  Transistor #(.\type ("n")) transistor_178 (.in(1'b0), .out(_27), .gate(not_7_out));
  Transistor #(.\type ("n")) transistor_179 (.in(1'b0), .out(_27), .gate(not_8_out));
  Pull_Resistor #(.pull(1)) pull_resistor_29 (.node(_29));
  Pull_Resistor #(.pull(1)) pull_resistor_30 (.node(_28));
  Transistor #(.\type ("n")) transistor_180 (.in(1'b0), .out(_28), .gate(nT2));
  Transistor #(.\type ("n")) transistor_181 (.in(1'b0), .out(_29), .gate(not_2_out));
  Transistor #(.\type ("n")) transistor_182 (.in(1'b0), .out(_29), .gate(IR7));
  Transistor #(.\type ("n")) transistor_183 (.in(1'b0), .out(_29), .gate(not_7_out));
  Transistor #(.\type ("n")) transistor_184 (.in(1'b0), .out(_29), .gate(IR5));
  Transistor #(.\type ("n")) transistor_185 (.in(1'b0), .out(_29), .gate(nT0));
  Pull_Resistor #(.pull(1)) pull_resistor_31 (.node(_30));
  Transistor #(.\type ("n")) transistor_186 (.in(1'b0), .out(_30), .gate(or_1_out));
  Transistor #(.\type ("n")) transistor_187 (.in(1'b0), .out(_30), .gate(IR7));
  Transistor #(.\type ("n")) transistor_188 (.in(1'b0), .out(_30), .gate(IR4));
  Transistor #(.\type ("n")) transistor_189 (.in(1'b0), .out(_30), .gate(not_5_out));
  Transistor #(.\type ("n")) transistor_190 (.in(1'b0), .out(_30), .gate(not_6_out));
  Transistor #(.\type ("n")) transistor_191 (.in(1'b0), .out(_30), .gate(not_7_out));
  Pull_Resistor #(.pull(1)) pull_resistor_32 (.node(_31));
  Transistor #(.\type ("n")) transistor_192 (.in(1'b0), .out(_31), .gate(nT2));
  Transistor #(.\type ("n")) transistor_193 (.in(1'b0), .out(_31), .gate(IR4));
  Transistor #(.\type ("n")) transistor_194 (.in(1'b0), .out(_31), .gate(not_5_out));
  Transistor #(.\type ("n")) transistor_195 (.in(1'b0), .out(_31), .gate(not_6_out));
  Pull_Resistor #(.pull(1)) pull_resistor_33 (.node(_33));
  Pull_Resistor #(.pull(1)) pull_resistor_34 (.node(_32));
  Transistor #(.\type ("n")) transistor_196 (.in(1'b0), .out(_33), .gate(nT2));
  Transistor #(.\type ("n")) transistor_197 (.in(1'b0), .out(_32), .gate(not_2_out));
  Transistor #(.\type ("n")) transistor_198 (.in(1'b0), .out(_32), .gate(IR7));
  Transistor #(.\type ("n")) transistor_199 (.in(1'b0), .out(_33), .gate(IR3));
  Transistor #(.\type ("n")) transistor_200 (.in(1'b0), .out(_32), .gate(IR6));
  Transistor #(.\type ("n")) transistor_201 (.in(1'b0), .out(_32), .gate(IR5));
  Transistor #(.\type ("n")) transistor_202 (.in(1'b0), .out(_32), .gate(nT0));
  Pull_Resistor #(.pull(1)) pull_resistor_35 (.node(_34));
  Transistor #(.\type ("n")) transistor_203 (.in(1'b0), .out(_34), .gate(nT0));
  Pull_Resistor #(.pull(1)) pull_resistor_36 (.node(_35));
  Transistor #(.\type ("n")) transistor_204 (.in(1'b0), .out(_35), .gate(nT2));
  Transistor #(.\type ("n")) transistor_205 (.in(1'b0), .out(_35), .gate(or_1_out));
  Transistor #(.\type ("n")) transistor_206 (.in(1'b0), .out(_35), .gate(IR7));
  Transistor #(.\type ("n")) transistor_207 (.in(1'b0), .out(_35), .gate(IR4));
  Transistor #(.\type ("n")) transistor_208 (.in(1'b0), .out(_35), .gate(IR2));
  Pull_Resistor #(.pull(1)) pull_resistor_37 (.node(_36));
  Transistor #(.\type ("n")) transistor_209 (.in(1'b0), .out(_36), .gate(nT3));
  Transistor #(.\type ("n")) transistor_210 (.in(1'b0), .out(_36), .gate(or_1_out));
  Transistor #(.\type ("n")) transistor_211 (.in(1'b0), .out(_36), .gate(IR7));
  Transistor #(.\type ("n")) transistor_212 (.in(1'b0), .out(_36), .gate(IR4));
  Pull_Resistor #(.pull(1)) pull_resistor_38 (.node(_37));
  Transistor #(.\type ("n")) transistor_213 (.in(1'b0), .out(_37), .gate(nT4));
  Transistor #(.\type ("n")) transistor_214 (.in(1'b0), .out(_37), .gate(or_1_out));
  Transistor #(.\type ("n")) transistor_215 (.in(1'b0), .out(_37), .gate(IR7));
  Transistor #(.\type ("n")) transistor_216 (.in(1'b0), .out(_37), .gate(IR4));
  Transistor #(.\type ("n")) transistor_217 (.in(1'b0), .out(_37), .gate(IR3));
  Transistor #(.\type ("n")) transistor_218 (.in(1'b0), .out(_37), .gate(IR2));
  Transistor #(.\type ("n")) transistor_219 (.in(1'b0), .out(_37), .gate(IR6));
  Pull_Resistor #(.pull(1)) pull_resistor_39 (.node(_38));
  Transistor #(.\type ("n")) transistor_220 (.in(1'b0), .out(_38), .gate(nT4));
  Transistor #(.\type ("n")) transistor_221 (.in(1'b0), .out(_38), .gate(or_1_out));
  Transistor #(.\type ("n")) transistor_222 (.in(1'b0), .out(_38), .gate(IR7));
  Transistor #(.\type ("n")) transistor_223 (.in(1'b0), .out(_38), .gate(IR4));
  Transistor #(.\type ("n")) transistor_224 (.in(1'b0), .out(_38), .gate(IR3));
  Transistor #(.\type ("n")) transistor_225 (.in(1'b0), .out(_38), .gate(IR2));
  Transistor #(.\type ("n")) transistor_226 (.in(1'b0), .out(_38), .gate(not_7_out));
  Transistor #(.\type ("n")) transistor_227 (.in(1'b0), .out(_38), .gate(IR5));
  Pull_Resistor #(.pull(1)) pull_resistor_40 (.node(_40));
  Pull_Resistor #(.pull(1)) pull_resistor_41 (.node(_39));
  Transistor #(.\type ("n")) transistor_228 (.in(1'b0), .out(_40), .gate(nT4));
  Transistor #(.\type ("n")) transistor_229 (.in(1'b0), .out(_39), .gate(nT3));
  Transistor #(.\type ("n")) transistor_230 (.in(1'b0), .out(_40), .gate(not_2_out));
  Transistor #(.\type ("n")) transistor_231 (.in(1'b0), .out(_39), .gate(not_2_out));
  Transistor #(.\type ("n")) transistor_232 (.in(1'b0), .out(_39), .gate(IR4));
  Transistor #(.\type ("n")) transistor_233 (.in(1'b0), .out(_40), .gate(not_4_out));
  Transistor #(.\type ("n")) transistor_234 (.in(1'b0), .out(_39), .gate(IR3));
  Transistor #(.\type ("n")) transistor_235 (.in(1'b0), .out(_40), .gate(IR3));
  Transistor #(.\type ("n")) transistor_236 (.in(1'b0), .out(_39), .gate(IR2));
  Transistor #(.\type ("n")) transistor_237 (.in(1'b0), .out(_40), .gate(IR2));
  Pull_Resistor #(.pull(1)) pull_resistor_42 (.node(_41));
  Transistor #(.\type ("n")) transistor_238 (.in(1'b0), .out(_41), .gate(nT2));
  Transistor #(.\type ("n")) transistor_239 (.in(1'b0), .out(_41), .gate(not_2_out));
  Transistor #(.\type ("n")) transistor_240 (.in(1'b0), .out(_41), .gate(not_4_out));
  Transistor #(.\type ("n")) transistor_241 (.in(1'b0), .out(_41), .gate(IR3));
  Transistor #(.\type ("n")) transistor_242 (.in(1'b0), .out(_41), .gate(IR2));
  Pull_Resistor #(.pull(1)) pull_resistor_43 (.node(_42));
  Transistor #(.\type ("n")) transistor_243 (.in(1'b0), .out(_42), .gate(nT3));
  Transistor #(.\type ("n")) transistor_244 (.in(1'b0), .out(_42), .gate(not_4_out));
  Transistor #(.\type ("n")) transistor_245 (.in(1'b0), .out(_42), .gate(not_5_out));
  Pull_Resistor #(.pull(1)) pull_resistor_44 (.node(_43));
  Pull_Resistor #(.pull(1)) pull_resistor_45 (.node(_44));
  Transistor #(.\type ("n")) transistor_246 (.in(1'b0), .out(_44), .gate(not_1_out));
  Transistor #(.\type ("n")) transistor_247 (.in(1'b0), .out(_43), .gate(or_1_out));
  Transistor #(.\type ("n")) transistor_248 (.in(1'b0), .out(_43), .gate(IR7));
  Transistor #(.\type ("n")) transistor_249 (.in(1'b0), .out(_44), .gate(not_3_out));
  Transistor #(.\type ("n")) transistor_250 (.in(1'b0), .out(_43), .gate(IR4));
  Transistor #(.\type ("n")) transistor_251 (.in(1'b0), .out(_43), .gate(not_5_out));
  Transistor #(.\type ("n")) transistor_252 (.in(1'b0), .out(_43), .gate(IR2));
  Transistor #(.\type ("n")) transistor_253 (.in(1'b0), .out(_44), .gate(not_7_out));
  Transistor #(.\type ("n")) transistor_254 (.in(1'b0), .out(_43), .gate(not_8_out));
  Transistor #(.\type ("n")) transistor_255 (.in(1'b0), .out(_44), .gate(not_8_out));
  Pull_Resistor #(.pull(1)) pull_resistor_46 (.node(_45));
  Transistor #(.\type ("n")) transistor_256 (.in(1'b0), .out(_45), .gate(nT4));
  Transistor #(.\type ("n")) transistor_257 (.in(1'b0), .out(_45), .gate(not_2_out));
  Transistor #(.\type ("n")) transistor_258 (.in(1'b0), .out(_45), .gate(IR4));
  Transistor #(.\type ("n")) transistor_259 (.in(1'b0), .out(_45), .gate(IR3));
  Transistor #(.\type ("n")) transistor_260 (.in(1'b0), .out(_45), .gate(IR2));
  Pull_Resistor #(.pull(1)) pull_resistor_47 (.node(_46));
  Transistor #(.\type ("n")) transistor_261 (.in(1'b0), .out(_46), .gate(nT3));
  Transistor #(.\type ("n")) transistor_262 (.in(1'b0), .out(_46), .gate(not_2_out));
  Transistor #(.\type ("n")) transistor_263 (.in(1'b0), .out(_46), .gate(not_4_out));
  Transistor #(.\type ("n")) transistor_264 (.in(1'b0), .out(_46), .gate(IR3));
  Transistor #(.\type ("n")) transistor_265 (.in(1'b0), .out(_46), .gate(IR2));
  Pull_Resistor #(.pull(1)) pull_resistor_48 (.node(_47));
  Pull_Resistor #(.pull(1)) pull_resistor_49 (.node(_48));
  Transistor #(.\type ("n")) transistor_266 (.in(1'b0), .out(_48), .gate(nT2));
  Transistor #(.\type ("n")) transistor_267 (.in(1'b0), .out(_48), .gate(or_1_out));
  Transistor #(.\type ("n")) transistor_268 (.in(1'b0), .out(_47), .gate(or_1_out));
  Transistor #(.\type ("n")) transistor_269 (.in(1'b0), .out(_48), .gate(IR7));
  Transistor #(.\type ("n")) transistor_270 (.in(1'b0), .out(_47), .gate(IR7));
  Transistor #(.\type ("n")) transistor_271 (.in(1'b0), .out(_47), .gate(IR4));
  Transistor #(.\type ("n")) transistor_272 (.in(1'b0), .out(_48), .gate(IR4));
  Transistor #(.\type ("n")) transistor_273 (.in(1'b0), .out(_48), .gate(IR3));
  Transistor #(.\type ("n")) transistor_274 (.in(1'b0), .out(_47), .gate(IR3));
  Transistor #(.\type ("n")) transistor_275 (.in(1'b0), .out(_47), .gate(IR2));
  Transistor #(.\type ("n")) transistor_276 (.in(1'b0), .out(_48), .gate(IR2));
  Transistor #(.\type ("n")) transistor_277 (.in(1'b0), .out(_48), .gate(IR6));
  Transistor #(.\type ("n")) transistor_278 (.in(1'b0), .out(_47), .gate(not_7_out));
  Transistor #(.\type ("n")) transistor_279 (.in(1'b0), .out(_48), .gate(not_8_out));
  Pull_Resistor #(.pull(1)) pull_resistor_50 (.node(_49));
  Transistor #(.\type ("n")) transistor_280 (.in(1'b0), .out(_49), .gate(or_1_out));
  Transistor #(.\type ("n")) transistor_281 (.in(1'b0), .out(_49), .gate(not_3_out));
  Transistor #(.\type ("n")) transistor_282 (.in(1'b0), .out(_49), .gate(IR4));
  Transistor #(.\type ("n")) transistor_283 (.in(1'b0), .out(_49), .gate(not_7_out));
  Transistor #(.\type ("n")) transistor_284 (.in(1'b0), .out(_49), .gate(nT0));
  Pull_Resistor #(.pull(1)) pull_resistor_51 (.node(_50));
  Transistor #(.\type ("n")) transistor_285 (.in(1'b0), .out(_50), .gate(not_2_out));
  Transistor #(.\type ("n")) transistor_286 (.in(1'b0), .out(_50), .gate(not_3_out));
  Transistor #(.\type ("n")) transistor_287 (.in(1'b0), .out(_50), .gate(not_7_out));
  Transistor #(.\type ("n")) transistor_288 (.in(1'b0), .out(_50), .gate(IR5));
  Transistor #(.\type ("n")) transistor_289 (.in(1'b0), .out(_50), .gate(nT0));
  Pull_Resistor #(.pull(1)) pull_resistor_52 (.node(_52));
  Pull_Resistor #(.pull(1)) pull_resistor_53 (.node(_51));
  Transistor #(.\type ("n")) transistor_290 (.in(1'b0), .out(_52), .gate(not_2_out));
  Transistor #(.\type ("n")) transistor_291 (.in(1'b0), .out(_51), .gate(not_2_out));
  Transistor #(.\type ("n")) transistor_292 (.in(1'b0), .out(_51), .gate(not_3_out));
  Transistor #(.\type ("n")) transistor_293 (.in(1'b0), .out(_51), .gate(not_7_out));
  Transistor #(.\type ("n")) transistor_294 (.in(1'b0), .out(_52), .gate(not_7_out));
  Transistor #(.\type ("n")) transistor_295 (.in(1'b0), .out(_52), .gate(not_8_out));
  Transistor #(.\type ("n")) transistor_296 (.in(1'b0), .out(_51), .gate(not_8_out));
  Transistor #(.\type ("n")) transistor_297 (.in(1'b0), .out(_52), .gate(nT0));
  Transistor #(.\type ("n")) transistor_298 (.in(1'b0), .out(_51), .gate(nT0));
  Pull_Resistor #(.pull(1)) pull_resistor_54 (.node(_53));
  Transistor #(.\type ("n")) transistor_299 (.in(1'b0), .out(_53), .gate(not_1_out));
  Transistor #(.\type ("n")) transistor_300 (.in(1'b0), .out(_53), .gate(IR7));
  Transistor #(.\type ("n")) transistor_301 (.in(1'b0), .out(_53), .gate(IR6));
  Transistor #(.\type ("n")) transistor_302 (.in(1'b0), .out(_53), .gate(not_8_out));
  Pull_Resistor #(.pull(1)) pull_resistor_55 (.node(_54));
  Transistor #(.\type ("n")) transistor_303 (.in(1'b0), .out(_54), .gate(nT3));
  Transistor #(.\type ("n")) transistor_304 (.in(1'b0), .out(_54), .gate(or_1_out));
  Transistor #(.\type ("n")) transistor_305 (.in(1'b0), .out(_54), .gate(IR7));
  Transistor #(.\type ("n")) transistor_306 (.in(1'b0), .out(_54), .gate(IR4));
  Transistor #(.\type ("n")) transistor_307 (.in(1'b0), .out(_54), .gate(not_5_out));
  Transistor #(.\type ("n")) transistor_308 (.in(1'b0), .out(_54), .gate(not_6_out));
  Transistor #(.\type ("n")) transistor_309 (.in(1'b0), .out(_54), .gate(not_7_out));
  Pull_Resistor #(.pull(1)) pull_resistor_56 (.node(_55));
  Pull_Resistor #(.pull(1)) pull_resistor_57 (.node(_56));
  Transistor #(.\type ("n")) transistor_310 (.in(1'b0), .out(_56), .gate(nT5));
  Transistor #(.\type ("n")) transistor_311 (.in(1'b0), .out(_55), .gate(not_1_out));
  Transistor #(.\type ("n")) transistor_312 (.in(1'b0), .out(_56), .gate(or_1_out));
  Transistor #(.\type ("n")) transistor_313 (.in(1'b0), .out(_56), .gate(IR7));
  Transistor #(.\type ("n")) transistor_314 (.in(1'b0), .out(_55), .gate(IR7));
  Transistor #(.\type ("n")) transistor_315 (.in(1'b0), .out(_56), .gate(IR4));
  Transistor #(.\type ("n")) transistor_316 (.in(1'b0), .out(_56), .gate(IR3));
  Transistor #(.\type ("n")) transistor_317 (.in(1'b0), .out(_56), .gate(IR2));
  Transistor #(.\type ("n")) transistor_318 (.in(1'b0), .out(_56), .gate(IR6));
  Transistor #(.\type ("n")) transistor_319 (.in(1'b0), .out(_55), .gate(IR6));
  Transistor #(.\type ("n")) transistor_320 (.in(1'b0), .out(_56), .gate(not_8_out));
  Pull_Resistor #(.pull(1)) pull_resistor_58 (.node(_57));
  Transistor #(.\type ("n")) transistor_321 (.in(1'b0), .out(_57), .gate(nT2));
  Transistor #(.\type ("n")) transistor_322 (.in(1'b0), .out(_57), .gate(or_1_out));
  Transistor #(.\type ("n")) transistor_323 (.in(1'b0), .out(_57), .gate(IR7));
  Transistor #(.\type ("n")) transistor_324 (.in(1'b0), .out(_57), .gate(IR4));
  Transistor #(.\type ("n")) transistor_325 (.in(1'b0), .out(_57), .gate(IR2));
  Pull_Resistor #(.pull(1)) pull_resistor_59 (.node(_58));
  Transistor #(.\type ("n")) transistor_326 (.in(1'b0), .out(_58), .gate(or_1_out));
  Transistor #(.\type ("n")) transistor_327 (.in(1'b0), .out(_58), .gate(not_3_out));
  Transistor #(.\type ("n")) transistor_328 (.in(1'b0), .out(_58), .gate(not_4_out));
  Transistor #(.\type ("n")) transistor_329 (.in(1'b0), .out(_58), .gate(not_5_out));
  Transistor #(.\type ("n")) transistor_330 (.in(1'b0), .out(_58), .gate(IR2));
  Transistor #(.\type ("n")) transistor_331 (.in(1'b0), .out(_58), .gate(IR6));
  Transistor #(.\type ("n")) transistor_332 (.in(1'b0), .out(_58), .gate(IR5));
  Transistor #(.\type ("n")) transistor_333 (.in(1'b0), .out(_58), .gate(nT0));
  Pull_Resistor #(.pull(1)) pull_resistor_60 (.node(_59));
  Pull_Resistor #(.pull(1)) pull_resistor_61 (.node(_60));
  Transistor #(.\type ("n")) transistor_334 (.in(1'b0), .out(_60), .gate(not_2_out));
  Transistor #(.\type ("n")) transistor_335 (.in(1'b0), .out(_59), .gate(not_2_out));
  Transistor #(.\type ("n")) transistor_336 (.in(1'b0), .out(_59), .gate(IR7));
  Transistor #(.\type ("n")) transistor_337 (.in(1'b0), .out(_60), .gate(not_7_out));
  Transistor #(.\type ("n")) transistor_338 (.in(1'b0), .out(_60), .gate(not_8_out));
  Transistor #(.\type ("n")) transistor_339 (.in(1'b0), .out(_59), .gate(nT1X));
  Transistor #(.\type ("n")) transistor_340 (.in(1'b0), .out(_60), .gate(nT1X));
  Pull_Resistor #(.pull(1)) pull_resistor_62 (.node(_61));
  Transistor #(.\type ("n")) transistor_341 (.in(1'b0), .out(_61), .gate(not_1_out));
  Transistor #(.\type ("n")) transistor_342 (.in(1'b0), .out(_61), .gate(IR7));
  Transistor #(.\type ("n")) transistor_343 (.in(1'b0), .out(_61), .gate(IR4));
  Transistor #(.\type ("n")) transistor_344 (.in(1'b0), .out(_61), .gate(not_5_out));
  Transistor #(.\type ("n")) transistor_345 (.in(1'b0), .out(_61), .gate(IR2));
  Transistor #(.\type ("n")) transistor_346 (.in(1'b0), .out(_61), .gate(nT1X));
  Pull_Resistor #(.pull(1)) pull_resistor_63 (.node(_62));
  Transistor #(.\type ("n")) transistor_347 (.in(1'b0), .out(_62), .gate(not_1_out));
  Transistor #(.\type ("n")) transistor_348 (.in(1'b0), .out(_62), .gate(not_3_out));
  Transistor #(.\type ("n")) transistor_349 (.in(1'b0), .out(_62), .gate(IR4));
  Transistor #(.\type ("n")) transistor_350 (.in(1'b0), .out(_62), .gate(not_5_out));
  Transistor #(.\type ("n")) transistor_351 (.in(1'b0), .out(_62), .gate(IR2));
  Transistor #(.\type ("n")) transistor_352 (.in(1'b0), .out(_62), .gate(IR6));
  Transistor #(.\type ("n")) transistor_353 (.in(1'b0), .out(_62), .gate(IR5));
  Transistor #(.\type ("n")) transistor_354 (.in(1'b0), .out(_62), .gate(nT0));
  Pull_Resistor #(.pull(1)) pull_resistor_64 (.node(_64));
  Pull_Resistor #(.pull(1)) pull_resistor_65 (.node(_63));
  Transistor #(.\type ("n")) transistor_355 (.in(1'b0), .out(_63), .gate(or_1_out));
  Transistor #(.\type ("n")) transistor_356 (.in(1'b0), .out(_64), .gate(not_2_out));
  Transistor #(.\type ("n")) transistor_357 (.in(1'b0), .out(_63), .gate(IR7));
  Transistor #(.\type ("n")) transistor_358 (.in(1'b0), .out(_64), .gate(not_3_out));
  Transistor #(.\type ("n")) transistor_359 (.in(1'b0), .out(_63), .gate(IR4));
  Transistor #(.\type ("n")) transistor_360 (.in(1'b0), .out(_63), .gate(not_5_out));
  Transistor #(.\type ("n")) transistor_361 (.in(1'b0), .out(_63), .gate(IR2));
  Transistor #(.\type ("n")) transistor_362 (.in(1'b0), .out(_64), .gate(IR6));
  Transistor #(.\type ("n")) transistor_363 (.in(1'b0), .out(_63), .gate(not_7_out));
  Transistor #(.\type ("n")) transistor_364 (.in(1'b0), .out(_64), .gate(not_8_out));
  Transistor #(.\type ("n")) transistor_365 (.in(1'b0), .out(_63), .gate(not_8_out));
  Transistor #(.\type ("n")) transistor_366 (.in(1'b0), .out(_64), .gate(nT0));
  Transistor #(.\type ("n")) transistor_367 (.in(1'b0), .out(_63), .gate(nT0));
  Pull_Resistor #(.pull(1)) pull_resistor_66 (.node(_65));
  Transistor #(.\type ("n")) transistor_368 (.in(1'b0), .out(_65), .gate(not_2_out));
  Transistor #(.\type ("n")) transistor_369 (.in(1'b0), .out(_65), .gate(nT0));
  Pull_Resistor #(.pull(1)) pull_resistor_67 (.node(_66));
  Transistor #(.\type ("n")) transistor_370 (.in(1'b0), .out(_66), .gate(or_1_out));
  Transistor #(.\type ("n")) transistor_371 (.in(1'b0), .out(_66), .gate(not_3_out));
  Transistor #(.\type ("n")) transistor_372 (.in(1'b0), .out(_66), .gate(IR4));
  Transistor #(.\type ("n")) transistor_373 (.in(1'b0), .out(_66), .gate(not_5_out));
  Transistor #(.\type ("n")) transistor_374 (.in(1'b0), .out(_66), .gate(IR2));
  Transistor #(.\type ("n")) transistor_375 (.in(1'b0), .out(_66), .gate(IR6));
  Transistor #(.\type ("n")) transistor_376 (.in(1'b0), .out(_66), .gate(not_8_out));
  Transistor #(.\type ("n")) transistor_377 (.in(1'b0), .out(_66), .gate(nT0));
  Pull_Resistor #(.pull(1)) pull_resistor_68 (.node(_68));
  Pull_Resistor #(.pull(1)) pull_resistor_69 (.node(_67));
  Transistor #(.\type ("n")) transistor_378 (.in(1'b0), .out(_68), .gate(not_1_out));
  Transistor #(.\type ("n")) transistor_379 (.in(1'b0), .out(_67), .gate(not_1_out));
  Transistor #(.\type ("n")) transistor_380 (.in(1'b0), .out(_67), .gate(IR7));
  Transistor #(.\type ("n")) transistor_381 (.in(1'b0), .out(_68), .gate(not_3_out));
  Transistor #(.\type ("n")) transistor_382 (.in(1'b0), .out(_67), .gate(IR4));
  Transistor #(.\type ("n")) transistor_383 (.in(1'b0), .out(_68), .gate(IR4));
  Transistor #(.\type ("n")) transistor_384 (.in(1'b0), .out(_67), .gate(not_5_out));
  Transistor #(.\type ("n")) transistor_385 (.in(1'b0), .out(_68), .gate(not_5_out));
  Transistor #(.\type ("n")) transistor_386 (.in(1'b0), .out(_68), .gate(IR2));
  Transistor #(.\type ("n")) transistor_387 (.in(1'b0), .out(_67), .gate(IR2));
  Transistor #(.\type ("n")) transistor_388 (.in(1'b0), .out(_68), .gate(IR6));
  Transistor #(.\type ("n")) transistor_389 (.in(1'b0), .out(_68), .gate(not_8_out));
  Transistor #(.\type ("n")) transistor_390 (.in(1'b0), .out(_68), .gate(nT0));
  Transistor #(.\type ("n")) transistor_391 (.in(1'b0), .out(_67), .gate(nT0));
  Pull_Resistor #(.pull(1)) pull_resistor_70 (.node(_69));
  Transistor #(.\type ("n")) transistor_392 (.in(1'b0), .out(_69), .gate(or_1_out));
  Transistor #(.\type ("n")) transistor_393 (.in(1'b0), .out(_69), .gate(IR7));
  Transistor #(.\type ("n")) transistor_394 (.in(1'b0), .out(_69), .gate(IR4));
  Transistor #(.\type ("n")) transistor_395 (.in(1'b0), .out(_69), .gate(not_6_out));
  Transistor #(.\type ("n")) transistor_396 (.in(1'b0), .out(_69), .gate(IR6));
  Transistor #(.\type ("n")) transistor_397 (.in(1'b0), .out(_69), .gate(not_8_out));
  Transistor #(.\type ("n")) transistor_398 (.in(1'b0), .out(_69), .gate(nT0));
  Pull_Resistor #(.pull(1)) pull_resistor_71 (.node(_70));
  Transistor #(.\type ("n")) transistor_399 (.in(1'b0), .out(_70), .gate(not_2_out));
  Transistor #(.\type ("n")) transistor_400 (.in(1'b0), .out(_70), .gate(IR7));
  Transistor #(.\type ("n")) transistor_401 (.in(1'b0), .out(_70), .gate(IR6));
  Transistor #(.\type ("n")) transistor_402 (.in(1'b0), .out(_70), .gate(not_8_out));
  Transistor #(.\type ("n")) transistor_403 (.in(1'b0), .out(_70), .gate(nT0));
  Pull_Resistor #(.pull(1)) pull_resistor_72 (.node(_71));
  Pull_Resistor #(.pull(1)) pull_resistor_73 (.node(_72));
  Transistor #(.\type ("n")) transistor_404 (.in(1'b0), .out(_72), .gate(nT5));
  Transistor #(.\type ("n")) transistor_405 (.in(1'b0), .out(_71), .gate(nT4));
  Transistor #(.\type ("n")) transistor_406 (.in(1'b0), .out(_72), .gate(not_2_out));
  Transistor #(.\type ("n")) transistor_407 (.in(1'b0), .out(_72), .gate(not_4_out));
  Transistor #(.\type ("n")) transistor_408 (.in(1'b0), .out(_71), .gate(not_4_out));
  Transistor #(.\type ("n")) transistor_409 (.in(1'b0), .out(_72), .gate(IR3));
  Transistor #(.\type ("n")) transistor_410 (.in(1'b0), .out(_71), .gate(not_5_out));
  Transistor #(.\type ("n")) transistor_411 (.in(1'b0), .out(_72), .gate(IR2));
  Pull_Resistor #(.pull(1)) pull_resistor_74 (.node(_73));
  Transistor #(.\type ("n")) transistor_412 (.in(1'b0), .out(_73), .gate(or_1_out));
  Transistor #(.\type ("n")) transistor_413 (.in(1'b0), .out(_73), .gate(not_4_out));
  Transistor #(.\type ("n")) transistor_414 (.in(1'b0), .out(_73), .gate(IR3));
  Transistor #(.\type ("n")) transistor_415 (.in(1'b0), .out(_73), .gate(IR2));
  Transistor #(.\type ("n")) transistor_416 (.in(1'b0), .out(_73), .gate(nT0));
  Transistor #(.\type ("n")) transistor_417 (.in(1'b0), .out(_73), .gate(nPRDY));
  Pull_Resistor #(.pull(1)) pull_resistor_75 (.node(_74));
  Pull_Resistor #(.pull(1)) pull_resistor_76 (.node(_75));
  Transistor #(.\type ("n")) transistor_418 (.in(1'b0), .out(_74), .gate(nT2));
  Transistor #(.\type ("n")) transistor_419 (.in(1'b0), .out(_75), .gate(not_1_out));
  Transistor #(.\type ("n")) transistor_420 (.in(1'b0), .out(_74), .gate(or_1_out));
  Transistor #(.\type ("n")) transistor_421 (.in(1'b0), .out(_74), .gate(IR7));
  Transistor #(.\type ("n")) transistor_422 (.in(1'b0), .out(_75), .gate(IR7));
  Transistor #(.\type ("n")) transistor_423 (.in(1'b0), .out(_75), .gate(IR4));
  Transistor #(.\type ("n")) transistor_424 (.in(1'b0), .out(_74), .gate(IR4));
  Transistor #(.\type ("n")) transistor_425 (.in(1'b0), .out(_74), .gate(not_5_out));
  Transistor #(.\type ("n")) transistor_426 (.in(1'b0), .out(_75), .gate(not_5_out));
  Transistor #(.\type ("n")) transistor_427 (.in(1'b0), .out(_75), .gate(IR2));
  Transistor #(.\type ("n")) transistor_428 (.in(1'b0), .out(_74), .gate(IR2));
  Transistor #(.\type ("n")) transistor_429 (.in(1'b0), .out(_75), .gate(not_7_out));
  Transistor #(.\type ("n")) transistor_430 (.in(1'b0), .out(_74), .gate(not_7_out));
  Transistor #(.\type ("n")) transistor_431 (.in(1'b0), .out(_74), .gate(IR5));
  Transistor #(.\type ("n")) transistor_432 (.in(1'b0), .out(_75), .gate(nT0));
  Pull_Resistor #(.pull(1)) pull_resistor_77 (.node(_76));
  Transistor #(.\type ("n")) transistor_433 (.in(1'b0), .out(_76), .gate(not_1_out));
  Transistor #(.\type ("n")) transistor_434 (.in(1'b0), .out(_76), .gate(IR7));
  Transistor #(.\type ("n")) transistor_435 (.in(1'b0), .out(_76), .gate(not_7_out));
  Pull_Resistor #(.pull(1)) pull_resistor_78 (.node(_77));
  Transistor #(.\type ("n")) transistor_436 (.in(1'b0), .out(_77), .gate(nT2));
  Transistor #(.\type ("n")) transistor_437 (.in(1'b0), .out(_77), .gate(or_1_out));
  Transistor #(.\type ("n")) transistor_438 (.in(1'b0), .out(_77), .gate(IR7));
  Transistor #(.\type ("n")) transistor_439 (.in(1'b0), .out(_77), .gate(IR4));
  Transistor #(.\type ("n")) transistor_440 (.in(1'b0), .out(_77), .gate(IR3));
  Transistor #(.\type ("n")) transistor_441 (.in(1'b0), .out(_77), .gate(IR2));
  Transistor #(.\type ("n")) transistor_442 (.in(1'b0), .out(_77), .gate(IR6));
  Transistor #(.\type ("n")) transistor_443 (.in(1'b0), .out(_77), .gate(IR5));
  Pull_Resistor #(.pull(1)) pull_resistor_79 (.node(_78));
  Pull_Resistor #(.pull(1)) pull_resistor_80 (.node(_79));
  Transistor #(.\type ("n")) transistor_444 (.in(1'b0), .out(_78), .gate(nT3));
  Transistor #(.\type ("n")) transistor_445 (.in(1'b0), .out(_78), .gate(or_1_out));
  Transistor #(.\type ("n")) transistor_446 (.in(1'b0), .out(_79), .gate(not_2_out));
  Transistor #(.\type ("n")) transistor_447 (.in(1'b0), .out(_78), .gate(IR7));
  Transistor #(.\type ("n")) transistor_448 (.in(1'b0), .out(_79), .gate(not_3_out));
  Transistor #(.\type ("n")) transistor_449 (.in(1'b0), .out(_78), .gate(IR4));
  Transistor #(.\type ("n")) transistor_450 (.in(1'b0), .out(_78), .gate(IR3));
  Transistor #(.\type ("n")) transistor_451 (.in(1'b0), .out(_78), .gate(IR2));
  Transistor #(.\type ("n")) transistor_452 (.in(1'b0), .out(_79), .gate(IR6));
  Transistor #(.\type ("n")) transistor_453 (.in(1'b0), .out(_78), .gate(IR6));
  Transistor #(.\type ("n")) transistor_454 (.in(1'b0), .out(_79), .gate(IR5));
  Transistor #(.\type ("n")) transistor_455 (.in(1'b0), .out(_78), .gate(not_8_out));
  Pull_Resistor #(.pull(1)) pull_resistor_81 (.node(_80));
  Transistor #(.\type ("n")) transistor_456 (.in(1'b0), .out(_80), .gate(nT2));
  Transistor #(.\type ("n")) transistor_457 (.in(1'b0), .out(_80), .gate(or_1_out));
  Transistor #(.\type ("n")) transistor_458 (.in(1'b0), .out(_80), .gate(not_4_out));
  Transistor #(.\type ("n")) transistor_459 (.in(1'b0), .out(_80), .gate(IR3));
  Transistor #(.\type ("n")) transistor_460 (.in(1'b0), .out(_80), .gate(IR2));
  Pull_Resistor #(.pull(1)) pull_resistor_82 (.node(_81));
  Transistor #(.\type ("n")) transistor_461 (.in(1'b0), .out(_81), .gate(nT2));
  Transistor #(.\type ("n")) transistor_462 (.in(1'b0), .out(_81), .gate(IR3));
  Transistor #(.\type ("n")) transistor_463 (.in(1'b0), .out(_81), .gate(not_6_out));
  Pull_Resistor #(.pull(1)) pull_resistor_83 (.node(_83));
  Pull_Resistor #(.pull(1)) pull_resistor_84 (.node(_82));
  Transistor #(.\type ("n")) transistor_464 (.in(1'b0), .out(_82), .gate(nT2));
  Transistor #(.\type ("n")) transistor_465 (.in(1'b0), .out(_83), .gate(nT2));
  Transistor #(.\type ("n")) transistor_466 (.in(1'b0), .out(_82), .gate(not_2_out));
  Transistor #(.\type ("n")) transistor_467 (.in(1'b0), .out(_82), .gate(IR3));
  Transistor #(.\type ("n")) transistor_468 (.in(1'b0), .out(_83), .gate(not_5_out));
  Transistor #(.\type ("n")) transistor_469 (.in(1'b0), .out(_82), .gate(IR2));
  Transistor #(.\type ("n")) transistor_470 (.in(1'b0), .out(_83), .gate(pull_resistor_121_node));
  Pull_Resistor #(.pull(1)) pull_resistor_85 (.node(_84));
  Transistor #(.\type ("n")) transistor_471 (.in(1'b0), .out(_84), .gate(nT5));
  Transistor #(.\type ("n")) transistor_472 (.in(1'b0), .out(_84), .gate(or_1_out));
  Transistor #(.\type ("n")) transistor_473 (.in(1'b0), .out(_84), .gate(IR7));
  Transistor #(.\type ("n")) transistor_474 (.in(1'b0), .out(_84), .gate(IR4));
  Transistor #(.\type ("n")) transistor_475 (.in(1'b0), .out(_84), .gate(IR3));
  Transistor #(.\type ("n")) transistor_476 (.in(1'b0), .out(_84), .gate(IR2));
  Transistor #(.\type ("n")) transistor_477 (.in(1'b0), .out(_84), .gate(not_7_out));
  Transistor #(.\type ("n")) transistor_478 (.in(1'b0), .out(_84), .gate(not_8_out));
  Pull_Resistor #(.pull(1)) pull_resistor_86 (.node(_85));
  Transistor #(.\type ("n")) transistor_479 (.in(1'b0), .out(_85), .gate(nT4));
  Pull_Resistor #(.pull(1)) pull_resistor_87 (.node(_86));
  Pull_Resistor #(.pull(1)) pull_resistor_88 (.node(_87));
  Transistor #(.\type ("n")) transistor_480 (.in(1'b0), .out(_86), .gate(nT3));
  Transistor #(.\type ("n")) transistor_481 (.in(1'b0), .out(_87), .gate(or_1_out));
  Transistor #(.\type ("n")) transistor_482 (.in(1'b0), .out(_87), .gate(IR7));
  Transistor #(.\type ("n")) transistor_483 (.in(1'b0), .out(_87), .gate(IR4));
  Transistor #(.\type ("n")) transistor_484 (.in(1'b0), .out(_87), .gate(IR3));
  Transistor #(.\type ("n")) transistor_485 (.in(1'b0), .out(_87), .gate(IR2));
  Transistor #(.\type ("n")) transistor_486 (.in(1'b0), .out(_87), .gate(IR5));
  Transistor #(.\type ("n")) transistor_487 (.in(1'b0), .out(_87), .gate(nT0));
  Pull_Resistor #(.pull(1)) pull_resistor_89 (.node(_88));
  Transistor #(.\type ("n")) transistor_488 (.in(1'b0), .out(_88), .gate(or_1_out));
  Transistor #(.\type ("n")) transistor_489 (.in(1'b0), .out(_88), .gate(IR7));
  Transistor #(.\type ("n")) transistor_490 (.in(1'b0), .out(_88), .gate(IR4));
  Transistor #(.\type ("n")) transistor_491 (.in(1'b0), .out(_88), .gate(not_5_out));
  Transistor #(.\type ("n")) transistor_492 (.in(1'b0), .out(_88), .gate(not_6_out));
  Transistor #(.\type ("n")) transistor_493 (.in(1'b0), .out(_88), .gate(not_7_out));
  Transistor #(.\type ("n")) transistor_494 (.in(1'b0), .out(_88), .gate(nT0));
  Pull_Resistor #(.pull(1)) pull_resistor_90 (.node(_89));
  Transistor #(.\type ("n")) transistor_495 (.in(1'b0), .out(_89), .gate(nT5));
  Transistor #(.\type ("n")) transistor_496 (.in(1'b0), .out(_89), .gate(not_2_out));
  Transistor #(.\type ("n")) transistor_497 (.in(1'b0), .out(_89), .gate(IR4));
  Transistor #(.\type ("n")) transistor_498 (.in(1'b0), .out(_89), .gate(IR3));
  Transistor #(.\type ("n")) transistor_499 (.in(1'b0), .out(_89), .gate(IR2));
  Pull_Resistor #(.pull(1)) pull_resistor_91 (.node(_90));
  Transistor #(.\type ("n")) transistor_500 (.in(1'b0), .out(_90), .gate(nT3));
  Transistor #(.\type ("n")) transistor_501 (.in(1'b0), .out(_90), .gate(not_5_out));
  Transistor #(.\type ("n")) transistor_502 (.in(1'b0), .out(_90), .gate(pull_resistor_121_node));
  Pull_Resistor #(.pull(1)) pull_resistor_92 (.node(_91));
  Transistor #(.\type ("n")) transistor_503 (.in(1'b0), .out(_91), .gate(nT4));
  Transistor #(.\type ("n")) transistor_504 (.in(1'b0), .out(_91), .gate(not_2_out));
  Transistor #(.\type ("n")) transistor_505 (.in(1'b0), .out(_91), .gate(not_4_out));
  Transistor #(.\type ("n")) transistor_506 (.in(1'b0), .out(_91), .gate(IR3));
  Transistor #(.\type ("n")) transistor_507 (.in(1'b0), .out(_91), .gate(IR2));
  Pull_Resistor #(.pull(1)) pull_resistor_93 (.node(_92));
  Transistor #(.\type ("n")) transistor_508 (.in(1'b0), .out(_92), .gate(nT3));
  Transistor #(.\type ("n")) transistor_509 (.in(1'b0), .out(_92), .gate(not_4_out));
  Transistor #(.\type ("n")) transistor_510 (.in(1'b0), .out(_92), .gate(not_5_out));
  Pull_Resistor #(.pull(1)) pull_resistor_94 (.node(_94));
  Pull_Resistor #(.pull(1)) pull_resistor_95 (.node(_93));
  Transistor #(.\type ("n")) transistor_511 (.in(1'b0), .out(_93), .gate(nT3));
  Transistor #(.\type ("n")) transistor_512 (.in(1'b0), .out(_94), .gate(or_1_out));
  Transistor #(.\type ("n")) transistor_513 (.in(1'b0), .out(_93), .gate(or_1_out));
  Transistor #(.\type ("n")) transistor_514 (.in(1'b0), .out(_94), .gate(IR7));
  Transistor #(.\type ("n")) transistor_515 (.in(1'b0), .out(_94), .gate(IR4));
  Transistor #(.\type ("n")) transistor_516 (.in(1'b0), .out(_93), .gate(not_4_out));
  Transistor #(.\type ("n")) transistor_517 (.in(1'b0), .out(_93), .gate(IR3));
  Transistor #(.\type ("n")) transistor_518 (.in(1'b0), .out(_94), .gate(IR3));
  Transistor #(.\type ("n")) transistor_519 (.in(1'b0), .out(_93), .gate(IR2));
  Transistor #(.\type ("n")) transistor_520 (.in(1'b0), .out(_94), .gate(IR2));
  Transistor #(.\type ("n")) transistor_521 (.in(1'b0), .out(_94), .gate(IR5));
  Pull_Resistor #(.pull(1)) pull_resistor_96 (.node(_95));
  Transistor #(.\type ("n")) transistor_522 (.in(1'b0), .out(_95), .gate(or_1_out));
  Transistor #(.\type ("n")) transistor_523 (.in(1'b0), .out(_95), .gate(IR7));
  Transistor #(.\type ("n")) transistor_524 (.in(1'b0), .out(_95), .gate(IR4));
  Transistor #(.\type ("n")) transistor_525 (.in(1'b0), .out(_95), .gate(IR3));
  Transistor #(.\type ("n")) transistor_526 (.in(1'b0), .out(_95), .gate(IR2));
  Transistor #(.\type ("n")) transistor_527 (.in(1'b0), .out(_95), .gate(IR6));
  Transistor #(.\type ("n")) transistor_528 (.in(1'b0), .out(_95), .gate(not_8_out));
  Pull_Resistor #(.pull(1)) pull_resistor_97 (.node(_96));
  Transistor #(.\type ("n")) transistor_529 (.in(1'b0), .out(_96), .gate(or_1_out));
  Transistor #(.\type ("n")) transistor_530 (.in(1'b0), .out(_96), .gate(IR7));
  Transistor #(.\type ("n")) transistor_531 (.in(1'b0), .out(_96), .gate(IR4));
  Transistor #(.\type ("n")) transistor_532 (.in(1'b0), .out(_96), .gate(not_5_out));
  Transistor #(.\type ("n")) transistor_533 (.in(1'b0), .out(_96), .gate(not_6_out));
  Transistor #(.\type ("n")) transistor_534 (.in(1'b0), .out(_96), .gate(not_7_out));
  Pull_Resistor #(.pull(1)) pull_resistor_98 (.node(_97));
  Transistor #(.\type ("n")) transistor_535 (.in(1'b0), .out(_97), .gate(not_3_out));
  Transistor #(.\type ("n")) transistor_536 (.in(1'b0), .out(_97), .gate(IR6));
  Transistor #(.\type ("n")) transistor_537 (.in(1'b0), .out(_97), .gate(IR5));
  Pull_Resistor #(.pull(1)) pull_resistor_99 (.node(_98));
  Transistor #(.\type ("n")) transistor_538 (.in(1'b0), .out(_98), .gate(nT4));
  Transistor #(.\type ("n")) transistor_539 (.in(1'b0), .out(_98), .gate(or_1_out));
  Transistor #(.\type ("n")) transistor_540 (.in(1'b0), .out(_98), .gate(IR7));
  Transistor #(.\type ("n")) transistor_541 (.in(1'b0), .out(_98), .gate(IR4));
  Transistor #(.\type ("n")) transistor_542 (.in(1'b0), .out(_98), .gate(IR3));
  Transistor #(.\type ("n")) transistor_543 (.in(1'b0), .out(_98), .gate(IR2));
  Transistor #(.\type ("n")) transistor_544 (.in(1'b0), .out(_98), .gate(IR6));
  Transistor #(.\type ("n")) transistor_545 (.in(1'b0), .out(_98), .gate(IR5));
  Pull_Resistor #(.pull(1)) pull_resistor_100 (.node(_99));
  Pull_Resistor #(.pull(1)) pull_resistor_101 (.node(_100));
  Transistor #(.\type ("n")) transistor_546 (.in(1'b0), .out(_100), .gate(nT2));
  Transistor #(.\type ("n")) transistor_547 (.in(1'b0), .out(_99), .gate(nT2));
  Transistor #(.\type ("n")) transistor_548 (.in(1'b0), .out(_100), .gate(or_1_out));
  Transistor #(.\type ("n")) transistor_549 (.in(1'b0), .out(_99), .gate(or_1_out));
  Transistor #(.\type ("n")) transistor_550 (.in(1'b0), .out(_100), .gate(IR7));
  Transistor #(.\type ("n")) transistor_551 (.in(1'b0), .out(_99), .gate(IR7));
  Transistor #(.\type ("n")) transistor_552 (.in(1'b0), .out(_99), .gate(IR4));
  Transistor #(.\type ("n")) transistor_553 (.in(1'b0), .out(_100), .gate(IR4));
  Transistor #(.\type ("n")) transistor_554 (.in(1'b0), .out(_99), .gate(not_5_out));
  Transistor #(.\type ("n")) transistor_555 (.in(1'b0), .out(_100), .gate(not_5_out));
  Transistor #(.\type ("n")) transistor_556 (.in(1'b0), .out(_99), .gate(IR2));
  Transistor #(.\type ("n")) transistor_557 (.in(1'b0), .out(_100), .gate(IR2));
  Transistor #(.\type ("n")) transistor_558 (.in(1'b0), .out(_99), .gate(IR6));
  Transistor #(.\type ("n")) transistor_559 (.in(1'b0), .out(_99), .gate(IR5));
  Transistor #(.\type ("n")) transistor_560 (.in(1'b0), .out(_100), .gate(IR5));
  Pull_Resistor #(.pull(1)) pull_resistor_102 (.node(_101));
  Transistor #(.\type ("n")) transistor_561 (.in(1'b0), .out(_101), .gate(nT4));
  Transistor #(.\type ("n")) transistor_562 (.in(1'b0), .out(_101), .gate(or_1_out));
  Transistor #(.\type ("n")) transistor_563 (.in(1'b0), .out(_101), .gate(IR7));
  Transistor #(.\type ("n")) transistor_564 (.in(1'b0), .out(_101), .gate(IR4));
  Transistor #(.\type ("n")) transistor_565 (.in(1'b0), .out(_101), .gate(not_5_out));
  Transistor #(.\type ("n")) transistor_566 (.in(1'b0), .out(_101), .gate(not_6_out));
  Transistor #(.\type ("n")) transistor_567 (.in(1'b0), .out(_101), .gate(not_7_out));
  Pull_Resistor #(.pull(1)) pull_resistor_103 (.node(_102));
  Transistor #(.\type ("n")) transistor_568 (.in(1'b0), .out(_102), .gate(nT5));
  Transistor #(.\type ("n")) transistor_569 (.in(1'b0), .out(_102), .gate(or_1_out));
  Transistor #(.\type ("n")) transistor_570 (.in(1'b0), .out(_102), .gate(IR7));
  Transistor #(.\type ("n")) transistor_571 (.in(1'b0), .out(_102), .gate(IR4));
  Transistor #(.\type ("n")) transistor_572 (.in(1'b0), .out(_102), .gate(IR3));
  Transistor #(.\type ("n")) transistor_573 (.in(1'b0), .out(_102), .gate(IR2));
  Transistor #(.\type ("n")) transistor_574 (.in(1'b0), .out(_102), .gate(not_7_out));
  Pull_Resistor #(.pull(1)) pull_resistor_104 (.node(_103));
  Transistor #(.\type ("n")) transistor_575 (.in(1'b0), .out(_103), .gate(nT5));
  Transistor #(.\type ("n")) transistor_576 (.in(1'b0), .out(_103), .gate(or_1_out));
  Transistor #(.\type ("n")) transistor_577 (.in(1'b0), .out(_103), .gate(IR7));
  Transistor #(.\type ("n")) transistor_578 (.in(1'b0), .out(_103), .gate(IR4));
  Transistor #(.\type ("n")) transistor_579 (.in(1'b0), .out(_103), .gate(IR3));
  Transistor #(.\type ("n")) transistor_580 (.in(1'b0), .out(_103), .gate(IR2));
  Transistor #(.\type ("n")) transistor_581 (.in(1'b0), .out(_103), .gate(IR6));
  Transistor #(.\type ("n")) transistor_582 (.in(1'b0), .out(_103), .gate(not_8_out));
  Pull_Resistor #(.pull(1)) pull_resistor_105 (.node(_104));
  Pull_Resistor #(.pull(1)) pull_resistor_106 (.node(_105));
  Transistor #(.\type ("n")) transistor_583 (.in(1'b0), .out(_105), .gate(nT3));
  Transistor #(.\type ("n")) transistor_584 (.in(1'b0), .out(_104), .gate(nT2));
  Transistor #(.\type ("n")) transistor_585 (.in(1'b0), .out(_105), .gate(or_1_out));
  Transistor #(.\type ("n")) transistor_586 (.in(1'b0), .out(_104), .gate(or_1_out));
  Transistor #(.\type ("n")) transistor_587 (.in(1'b0), .out(_105), .gate(IR7));
  Transistor #(.\type ("n")) transistor_588 (.in(1'b0), .out(_104), .gate(IR7));
  Transistor #(.\type ("n")) transistor_589 (.in(1'b0), .out(_105), .gate(IR4));
  Transistor #(.\type ("n")) transistor_590 (.in(1'b0), .out(_104), .gate(IR4));
  Transistor #(.\type ("n")) transistor_591 (.in(1'b0), .out(_105), .gate(not_5_out));
  Transistor #(.\type ("n")) transistor_592 (.in(1'b0), .out(_104), .gate(not_5_out));
  Transistor #(.\type ("n")) transistor_593 (.in(1'b0), .out(_105), .gate(IR2));
  Transistor #(.\type ("n")) transistor_594 (.in(1'b0), .out(_104), .gate(not_6_out));
  Transistor #(.\type ("n")) transistor_595 (.in(1'b0), .out(_104), .gate(not_7_out));
  Transistor #(.\type ("n")) transistor_596 (.in(1'b0), .out(_104), .gate(IR5));
  Transistor #(.\type ("n")) transistor_597 (.in(1'b0), .out(_105), .gate(not_8_out));
  Pull_Resistor #(.pull(1)) pull_resistor_107 (.node(_106));
  Transistor #(.\type ("n")) transistor_598 (.in(1'b0), .out(_106), .gate(not_1_out));
  Transistor #(.\type ("n")) transistor_599 (.in(1'b0), .out(_106), .gate(not_7_out));
  Pull_Resistor #(.pull(1)) pull_resistor_108 (.node(_107));
  Transistor #(.\type ("n")) transistor_600 (.in(1'b0), .out(_107), .gate(not_1_out));
  Transistor #(.\type ("n")) transistor_601 (.in(1'b0), .out(_107), .gate(IR7));
  Transistor #(.\type ("n")) transistor_602 (.in(1'b0), .out(_107), .gate(IR6));
  Pull_Resistor #(.pull(1)) pull_resistor_109 (.node(_108));
  Transistor #(.\type ("n")) transistor_603 (.in(1'b0), .out(_108), .gate(or_1_out));
  Transistor #(.\type ("n")) transistor_604 (.in(1'b0), .out(_108), .gate(IR7));
  Transistor #(.\type ("n")) transistor_605 (.in(1'b0), .out(_108), .gate(not_4_out));
  Transistor #(.\type ("n")) transistor_606 (.in(1'b0), .out(_108), .gate(not_5_out));
  Transistor #(.\type ("n")) transistor_607 (.in(1'b0), .out(_108), .gate(IR2));
  Transistor #(.\type ("n")) transistor_608 (.in(1'b0), .out(_108), .gate(not_7_out));
  Transistor #(.\type ("n")) transistor_609 (.in(1'b0), .out(_108), .gate(nT0));
  Pull_Resistor #(.pull(1)) pull_resistor_110 (.node(_109));
  Transistor #(.\type ("n")) transistor_610 (.in(1'b0), .out(_109), .gate(or_1_out));
  Transistor #(.\type ("n")) transistor_611 (.in(1'b0), .out(_109), .gate(IR7));
  Transistor #(.\type ("n")) transistor_612 (.in(1'b0), .out(_109), .gate(IR4));
  Transistor #(.\type ("n")) transistor_613 (.in(1'b0), .out(_109), .gate(not_6_out));
  Transistor #(.\type ("n")) transistor_614 (.in(1'b0), .out(_109), .gate(IR6));
  Transistor #(.\type ("n")) transistor_615 (.in(1'b0), .out(_109), .gate(not_8_out));
  Transistor #(.\type ("n")) transistor_616 (.in(1'b0), .out(_109), .gate(nT1X));
  Pull_Resistor #(.pull(1)) pull_resistor_111 (.node(_110));
  Pull_Resistor #(.pull(1)) pull_resistor_112 (.node(_111));
  Transistor #(.\type ("n")) transistor_617 (.in(1'b0), .out(_111), .gate(nT3));
  Transistor #(.\type ("n")) transistor_618 (.in(1'b0), .out(_110), .gate(or_1_out));
  Transistor #(.\type ("n")) transistor_619 (.in(1'b0), .out(_110), .gate(IR7));
  Transistor #(.\type ("n")) transistor_620 (.in(1'b0), .out(_111), .gate(not_4_out));
  Transistor #(.\type ("n")) transistor_621 (.in(1'b0), .out(_110), .gate(not_4_out));
  Transistor #(.\type ("n")) transistor_622 (.in(1'b0), .out(_111), .gate(IR3));
  Transistor #(.\type ("n")) transistor_623 (.in(1'b0), .out(_110), .gate(not_5_out));
  Transistor #(.\type ("n")) transistor_624 (.in(1'b0), .out(_110), .gate(IR2));
  Transistor #(.\type ("n")) transistor_625 (.in(1'b0), .out(_111), .gate(not_6_out));
  Transistor #(.\type ("n")) transistor_626 (.in(1'b0), .out(_110), .gate(IR6));
  Transistor #(.\type ("n")) transistor_627 (.in(1'b0), .out(_110), .gate(nT0));
  Pull_Resistor #(.pull(1)) pull_resistor_113 (.node(_112));
  Transistor #(.\type ("n")) transistor_628 (.in(1'b0), .out(_112), .gate(not_2_out));
  Transistor #(.\type ("n")) transistor_629 (.in(1'b0), .out(_112), .gate(not_7_out));
  Transistor #(.\type ("n")) transistor_630 (.in(1'b0), .out(_112), .gate(not_8_out));
  Transistor #(.\type ("n")) transistor_631 (.in(1'b0), .out(_112), .gate(nT1X));
  Pull_Resistor #(.pull(1)) pull_resistor_114 (.node(_113));
  Transistor #(.\type ("n")) transistor_632 (.in(1'b0), .out(_113), .gate(or_1_out));
  Transistor #(.\type ("n")) transistor_633 (.in(1'b0), .out(_113), .gate(IR7));
  Transistor #(.\type ("n")) transistor_634 (.in(1'b0), .out(_113), .gate(IR4));
  Transistor #(.\type ("n")) transistor_635 (.in(1'b0), .out(_113), .gate(not_6_out));
  Transistor #(.\type ("n")) transistor_636 (.in(1'b0), .out(_113), .gate(IR6));
  Transistor #(.\type ("n")) transistor_637 (.in(1'b0), .out(_113), .gate(not_8_out));
  Transistor #(.\type ("n")) transistor_638 (.in(1'b0), .out(_113), .gate(nT0));
  Pull_Resistor #(.pull(1)) pull_resistor_115 (.node(_114));
  Pull_Resistor #(.pull(1)) pull_resistor_116 (.node(_115));
  Transistor #(.\type ("n")) transistor_639 (.in(1'b0), .out(_115), .gate(nT4));
  Transistor #(.\type ("n")) transistor_640 (.in(1'b0), .out(_115), .gate(or_1_out));
  Transistor #(.\type ("n")) transistor_641 (.in(1'b0), .out(_114), .gate(or_1_out));
  Transistor #(.\type ("n")) transistor_642 (.in(1'b0), .out(_115), .gate(IR7));
  Transistor #(.\type ("n")) transistor_643 (.in(1'b0), .out(_114), .gate(IR7));
  Transistor #(.\type ("n")) transistor_644 (.in(1'b0), .out(_114), .gate(IR4));
  Transistor #(.\type ("n")) transistor_645 (.in(1'b0), .out(_115), .gate(IR4));
  Transistor #(.\type ("n")) transistor_646 (.in(1'b0), .out(_115), .gate(IR3));
  Transistor #(.\type ("n")) transistor_647 (.in(1'b0), .out(_114), .gate(not_5_out));
  Transistor #(.\type ("n")) transistor_648 (.in(1'b0), .out(_114), .gate(IR2));
  Transistor #(.\type ("n")) transistor_649 (.in(1'b0), .out(_115), .gate(IR2));
  Transistor #(.\type ("n")) transistor_650 (.in(1'b0), .out(_114), .gate(IR6));
  Transistor #(.\type ("n")) transistor_651 (.in(1'b0), .out(_115), .gate(not_7_out));
  Transistor #(.\type ("n")) transistor_652 (.in(1'b0), .out(_115), .gate(IR5));
  Transistor #(.\type ("n")) transistor_653 (.in(1'b0), .out(_114), .gate(not_8_out));
  Transistor #(.\type ("n")) transistor_654 (.in(1'b0), .out(_114), .gate(nT0));
  Pull_Resistor #(.pull(1)) pull_resistor_117 (.node(_116));
  Transistor #(.\type ("n")) transistor_655 (.in(1'b0), .out(_116), .gate(not_2_out));
  Transistor #(.\type ("n")) transistor_656 (.in(1'b0), .out(_116), .gate(not_3_out));
  Transistor #(.\type ("n")) transistor_657 (.in(1'b0), .out(_116), .gate(not_7_out));
  Transistor #(.\type ("n")) transistor_658 (.in(1'b0), .out(_116), .gate(IR5));
  Transistor #(.\type ("n")) transistor_659 (.in(1'b0), .out(_116), .gate(nT1X));
  Pull_Resistor #(.pull(1)) pull_resistor_118 (.node(_117));
  Transistor #(.\type ("n")) transistor_660 (.in(1'b0), .out(_117), .gate(or_1_out));
  Transistor #(.\type ("n")) transistor_661 (.in(1'b0), .out(_117), .gate(not_3_out));
  Transistor #(.\type ("n")) transistor_662 (.in(1'b0), .out(_117), .gate(IR4));
  Transistor #(.\type ("n")) transistor_663 (.in(1'b0), .out(_117), .gate(not_5_out));
  Transistor #(.\type ("n")) transistor_664 (.in(1'b0), .out(_117), .gate(not_6_out));
  Transistor #(.\type ("n")) transistor_665 (.in(1'b0), .out(_117), .gate(not_7_out));
  Transistor #(.\type ("n")) transistor_666 (.in(1'b0), .out(_117), .gate(nT1X));
  Pull_Resistor #(.pull(1)) pull_resistor_119 (.node(_118));
  Pull_Resistor #(.pull(1)) pull_resistor_120 (.node(_119));
  Transistor #(.\type ("n")) transistor_667 (.in(1'b0), .out(_118), .gate(not_1_out));
  Transistor #(.\type ("n")) transistor_668 (.in(1'b0), .out(_119), .gate(or_1_out));
  Transistor #(.\type ("n")) transistor_669 (.in(1'b0), .out(_118), .gate(IR7));
  Transistor #(.\type ("n")) transistor_670 (.in(1'b0), .out(_119), .gate(not_3_out));
  Transistor #(.\type ("n")) transistor_671 (.in(1'b0), .out(_119), .gate(IR4));
  Transistor #(.\type ("n")) transistor_672 (.in(1'b0), .out(_118), .gate(IR4));
  Transistor #(.\type ("n")) transistor_673 (.in(1'b0), .out(_119), .gate(IR3));
  Transistor #(.\type ("n")) transistor_674 (.in(1'b0), .out(_118), .gate(not_5_out));
  Transistor #(.\type ("n")) transistor_675 (.in(1'b0), .out(_118), .gate(IR2));
  Transistor #(.\type ("n")) transistor_676 (.in(1'b0), .out(_118), .gate(IR6));
  Transistor #(.\type ("n")) transistor_677 (.in(1'b0), .out(_119), .gate(not_7_out));
  Transistor #(.\type ("n")) transistor_678 (.in(1'b0), .out(_119), .gate(nT1X));
  Transistor #(.\type ("n")) transistor_679 (.in(1'b0), .out(_118), .gate(nT1X));
  Pull_Resistor #(.pull(1)) pull_resistor_121 (.node(pull_resistor_121_node));
  Transistor #(.\type ("n")) transistor_680 (.in(1'b0), .out(pull_resistor_121_node), .gate(or_1_out));
  Transistor #(.\type ("n")) transistor_681 (.in(1'b0), .out(pull_resistor_121_node), .gate(IR7));
  Transistor #(.\type ("n")) transistor_682 (.in(1'b0), .out(pull_resistor_121_node), .gate(IR4));
  Transistor #(.\type ("n")) transistor_683 (.in(1'b0), .out(pull_resistor_121_node), .gate(not_5_out));
  Transistor #(.\type ("n")) transistor_684 (.in(1'b0), .out(pull_resistor_121_node), .gate(IR2));
  Pull_Resistor #(.pull(1)) pull_resistor_122 (.node(_121));
  Pull_Resistor #(.pull(1)) pull_resistor_123 (.node(_120));
  Transistor #(.\type ("n")) transistor_685 (.in(1'b0), .out(_120), .gate(or_1_out));
  Transistor #(.\type ("n")) transistor_686 (.in(1'b0), .out(_120), .gate(not_3_out));
  Transistor #(.\type ("n")) transistor_687 (.in(1'b0), .out(_120), .gate(not_4_out));
  Transistor #(.\type ("n")) transistor_688 (.in(1'b0), .out(_120), .gate(not_5_out));
  Transistor #(.\type ("n")) transistor_689 (.in(1'b0), .out(_120), .gate(IR2));
  Transistor #(.\type ("n")) transistor_690 (.in(1'b0), .out(_121), .gate(IR6));
  Transistor #(.\type ("n")) transistor_691 (.in(1'b0), .out(_120), .gate(not_7_out));
  Transistor #(.\type ("n")) transistor_692 (.in(1'b0), .out(_120), .gate(nT0));
  Pull_Resistor #(.pull(1)) pull_resistor_124 (.node(_122));
  Transistor #(.\type ("n")) transistor_693 (.in(1'b0), .out(_122), .gate(nT3));
  Transistor #(.\type ("n")) transistor_694 (.in(1'b0), .out(_122), .gate(IR4));
  Transistor #(.\type ("n")) transistor_695 (.in(1'b0), .out(_122), .gate(not_5_out));
  Transistor #(.\type ("n")) transistor_696 (.in(1'b0), .out(_122), .gate(not_6_out));
  Pull_Resistor #(.pull(1)) pull_resistor_125 (.node(_123));
  Transistor #(.\type ("n")) transistor_697 (.in(1'b0), .out(_123), .gate(nT2));
  Transistor #(.\type ("n")) transistor_698 (.in(1'b0), .out(_123), .gate(IR4));
  Transistor #(.\type ("n")) transistor_699 (.in(1'b0), .out(_123), .gate(IR3));
  Transistor #(.\type ("n")) transistor_700 (.in(1'b0), .out(_123), .gate(not_6_out));
  Pull_Resistor #(.pull(1)) pull_resistor_126 (.node(_124));
  Pull_Resistor #(.pull(1)) pull_resistor_127 (.node(_125));
  Transistor #(.\type ("n")) transistor_701 (.in(1'b0), .out(_124), .gate(nT5));
  Transistor #(.\type ("n")) transistor_702 (.in(1'b0), .out(_125), .gate(nT4));
  Transistor #(.\type ("n")) transistor_703 (.in(1'b0), .out(_124), .gate(not_2_out));
  Transistor #(.\type ("n")) transistor_704 (.in(1'b0), .out(_125), .gate(not_4_out));
  Transistor #(.\type ("n")) transistor_705 (.in(1'b0), .out(_124), .gate(IR3));
  Transistor #(.\type ("n")) transistor_706 (.in(1'b0), .out(_125), .gate(not_5_out));
  Transistor #(.\type ("n")) transistor_707 (.in(1'b0), .out(_124), .gate(IR2));
  Pull_Resistor #(.pull(1)) pull_resistor_128 (.node(_126));
  Transistor #(.\type ("n")) transistor_708 (.in(1'b0), .out(_126), .gate(IR7));
  Pull_Resistor #(.pull(1)) pull_resistor_129 (.node(_127));
  Transistor #(.\type ("n")) transistor_709 (.in(1'b0), .out(_127), .gate(or_1_out));
  Transistor #(.\type ("n")) transistor_710 (.in(1'b0), .out(_127), .gate(not_3_out));
  Transistor #(.\type ("n")) transistor_711 (.in(1'b0), .out(_127), .gate(not_4_out));
  Transistor #(.\type ("n")) transistor_712 (.in(1'b0), .out(_127), .gate(not_5_out));
  Transistor #(.\type ("n")) transistor_713 (.in(1'b0), .out(_127), .gate(IR2));
  Transistor #(.\type ("n")) transistor_714 (.in(1'b0), .out(_127), .gate(IR6));
  Transistor #(.\type ("n")) transistor_715 (.in(1'b0), .out(_127), .gate(not_8_out));
  Pull_Resistor #(.pull(1)) pull_resistor_130 (.node(_128));
  Transistor #(.\type ("n")) transistor_716 (.in(1'b0), .out(_128), .gate(IR0));
  Transistor #(.\type ("n")) transistor_717 (.in(1'b0), .out(_128), .gate(not_5_out));
  Transistor #(.\type ("n")) transistor_718 (.in(1'b0), .out(_128), .gate(IR2));
  Transistor #(.\type ("n")) transistor_719 (.in(1'b0), .out(_128), .gate(pull_resistor_121_node));

  // Notes on the sheet:
  //   #T5
  //   #T4
  //   #T3
  //   #T2
  //   IR0
  //   IR7
  //   IR3
  //   IR2
  //   IR6
  //   IR5
  //   #T0
  //   #T1X
  //   #IR1
  //   IR01
  //   #IR0
  //   #IR7
  //   IR4
  //   #IR4
  //   #IR3
  //   #IR2
  //   #IR6
  //   #IR5
  //   #PRDY
  //   #T5
  //   #T4
  //   #T3
  //   #T2
  //   IR0
  //   #IR1
  //   IR01
  //   #IR0
  //   IR7
  //   #IR7
  //   IR4
  //   #IR4
  //   IR3
  //   #IR3
  //   IR2
  //   #IR2
  //   IR6
  //   #IR6
  //   IR5
  //   #IR5
  //   #T0
  //   #T1X
  //   #PRDY
  //   #T5
  //   #T4
  //   #T3
  //   #T2
  //   IR0
  //   #IR1
  //   IR01
  //   #IR0
  //   IR7
  //   #IR7
  //   IR4
  //   #IR4
  //   IR3
  //   #IR3
  //   IR2
  //   #IR2
  //   IR6
  //   #IR6
  //   IR5
  //   #IR5
  //   #T0
  //   #T1X
  //   #PRDY
  //   #T5
  //   #T4
  //   #T3
  //   #T2
  //   IR0
  //   #IR1
  //   IR01
  //   #IR0
  //   IR7
  //   #IR7
  //   IR4
  //   #IR4
  //   IR3
  //   #IR3
  //   IR2
  //   #IR2
  //   IR6
  //   #IR6
  //   IR5
  //   #IR5
  //   #T0
  //   #T1X
  //   #PRDY
  //   #T5
  //   #T4
  //   #T3
  //   #T2
  //   IR0
  //   #IR1
  //   IR01
  //   #IR0
  //   IR7
  //   #IR7
  //   IR4
  //   #IR4
  //   IR3
  //   #IR3
  //   IR2
  //   #IR2
  //   IR6
  //   #IR6
  //   IR5
  //   #IR5
  //   #T0
  //   #T1X
  //   #PRDY
  //   #T5
  //   #T4
  //   #T3
  //   #T2
  //   IR0
  //   #IR1
  //   IR01
  //   #IR0
  //   IR7
  //   #IR7
  //   IR4
  //   #IR4
  //   IR3
  //   #IR3
  //   IR2
  //   #IR2
  //   IR6
  //   #IR6
  //   IR5
  //   #IR5
  //   #T0
  //   #T1X
  //   #PRDY
  //   #T5
  //   #T3
  //   #T2
  //   IR0
  //   IR2
  //   IR6
  //   #T0
  //   #T1X
  //   #T4
  //   #IR1
  //   IR01
  //   #IR0
  //   IR7
  //   #IR7
  //   IR4
  //   #IR4
  //   IR3
  //   #IR3
  //   #IR2
  //   #IR6
  //   IR5
  //   #IR5
  //   #T5
  //   #T4
  //   #T3
  //   #T2
  //   IR0
  //   #IR1
  //   IR01
  //   #IR0
  //   IR7
  //   #IR7
  //   IR4
  //   #IR4
  //   IR3
  //   #IR3
  //   IR2
  //   #IR2
  //   IR6
  //   #IR6
  //   IR5
  //   #IR5
  //   #T0
  //   #T1X
  //   PP
  //   #T0
  //   #T5
  //   #T4
  //   #T3
  //   #T2
  //   IR0
  //   #IR1
  //   IR01
  //   #IR0
  //   IR7
  //   #IR7
  //   IR4
  //   #IR4
  //   IR3
  //   #IR3
  //   IR2
  //   #IR2
  //   IR6
  //   #IR6
  //   IR5
  //   #IR5
  //   #T1X
  //   PP
  //   #T5
  //   #T4
  //   #T3
  //   #T2
  //   IR0
  //   #IR1
  //   IR01
  //   #IR0
  //   IR7
  //   #IR7
  //   IR4
  //   #IR4
  //   IR3
  //   #IR3
  //   IR2
  //   #IR2
  //   IR6
  //   #IR6
  //   IR5
  //   #IR5
  //   #T0
  //   #T1X
  //   PP
endmodule

module PREDECODE (
  input  PHI2,
  input  D0,
  input  D1,
  input  D2,
  input  D3,
  input  D4,
  input  D5,
  input  D6,
  input  D7,
  input  _0_IR,
  output IMPLIED,
  output nTWOCYCLE,
  output [7:0] PD
);

  wire _2_out, _3_out, _4_out, _5_out, d_latch_1_q, d_latch_2_q, d_latch_3_q, d_latch_4_q, d_latch_5_q,
       d_latch_6_q, d_latch_7_q, d_latch_8_q, not_1_out, not_2_out, not_3_out, not_4_out, not_5_out;

  D_Latch d_latch_1 (.EN(PHI2), .D(D0), .Q(d_latch_1_q));  // open: NOT_Q
  D_Latch d_latch_2 (.EN(PHI2), .D(D1), .Q(d_latch_2_q));  // open: NOT_Q
  D_Latch d_latch_3 (.EN(PHI2), .D(D2), .Q(d_latch_3_q));  // open: NOT_Q
  D_Latch d_latch_4 (.EN(PHI2), .D(D3), .Q(d_latch_4_q));  // open: NOT_Q
  D_Latch d_latch_5 (.EN(PHI2), .D(D4), .Q(d_latch_5_q));  // open: NOT_Q
  D_Latch d_latch_6 (.EN(PHI2), .D(D5), .Q(d_latch_6_q));  // open: NOT_Q
  D_Latch d_latch_7 (.EN(PHI2), .D(D6), .Q(d_latch_7_q));  // open: NOT_Q
  D_Latch d_latch_8 (.EN(PHI2), .D(D7), .Q(d_latch_8_q));  // open: NOT_Q
  not not_1 (not_1_out, _0_IR);
  and and_1 (PD[0], d_latch_1_q, not_1_out);
  and and_2 (PD[1], d_latch_2_q, not_1_out);
  and and_3 (PD[2], d_latch_3_q, not_1_out);
  and and_4 (PD[3], d_latch_4_q, not_1_out);
  and and_5 (PD[4], d_latch_5_q, not_1_out);
  and and_6 (PD[5], d_latch_6_q, not_1_out);
  and and_7 (PD[6], d_latch_7_q, not_1_out);
  and and_8 (PD[7], d_latch_8_q, not_1_out);
  not not_2 (not_2_out, PD[3]);
  not not_3 (not_3_out, PD[0]);
  not not_4 (not_4_out, PD[3]);
  not not_5 (not_5_out, PD[7]);
  nor _1 (IMPLIED, PD[0], PD[2], not_2_out);
  or _2 (_2_out, PD[1], PD[4], PD[7]);
  nor _3 (_3_out, not_3_out, PD[2], not_4_out, PD[4]);
  nor _4 (_4_out, PD[0], PD[2], PD[3], PD[4], not_5_out);
  and _5 (_5_out, IMPLIED, _2_out);
  nor _6 (nTWOCYCLE, _5_out, _3_out, _4_out);
endmodule
// RANDOM LOGIC
module RANDOM_LOGIC (
  input  X0,
  input  X1,
  input  X2,
  input  X3,
  input  X4,
  input  X5,
  input  X6,
  input  X7,
  input  X8,
  input  X9,
  input  X10,
  input  X11,
  input  X12,
  input  X13,
  input  X14,
  input  X15,
  input  X16,
  input  X17,
  input  X18,
  input  X19,
  input  X20,
  input  X21,
  input  X22,
  input  X23,
  input  X24,
  input  X25,
  input  X26,
  input  X27,
  input  X28,
  input  X29,
  input  X30,
  input  X31,
  input  X32,
  input  X33,
  input  X34,
  input  X35,
  input  X36,
  input  X37,
  input  X38,
  input  X39,
  input  X40,
  input  X41,
  input  X42,
  input  X43,
  input  X44,
  input  X45,
  input  X46,
  input  X47,
  input  X48,
  input  X49,
  input  X50,
  input  X51,
  input  X52,
  input  X53,
  input  X54,
  input  X55,
  input  X56,
  input  X57,
  input  X58,
  input  X59,
  input  X60,
  input  X61,
  input  X62,
  input  X63,
  input  X64,
  input  X65,
  input  X66,
  input  X67,
  input  X68,
  input  X69,
  input  X70,
  input  X71,
  input  X72,
  input  X73,
  input  X74,
  input  X75,
  input  X76,
  input  X77,
  input  X78,
  input  X79,
  input  X80,
  input  X81,
  input  X82,
  input  X83,
  input  X84,
  input  X85,
  input  X86,
  input  X87,
  input  X88,
  input  X89,
  input  X90,
  input  X91,
  input  X92,
  input  X93,
  input  X94,
  input  X95,
  input  X96,
  input  X97,
  input  X98,
  input  X99,
  input  X100,
  input  X101,
  input  X102,
  input  X103,
  input  X104,
  input  X105,
  input  X106,
  input  X107,
  input  X108,
  input  X109,
  input  X110,
  input  X111,
  input  X112,
  input  X113,
  input  X114,
  input  X115,
  input  X116,
  input  X117,
  input  X118,
  input  X119,
  input  X120,
  input  X121,
  input  X122,
  input  X123,
  input  X124,
  input  X125,
  input  X126,
  input  X127,
  input  X128,
  input  PHI1,
  input  PHI2,
  input  AVR,
  input  ACR,
  input  SO,
  input  nNMIP,
  input  RESP,
  input  nIRQP,
  input  IMPLIED,
  input  nTWOCYCLE,
  input  RDY,
  input  nIR5,
  input  [7:0] DB_IN,
  output WR,
  output _0_ADL2,
  output _0_ADL1,
  output _0_ADL0,
  output Y_SB,
  output X_SB,
  output SB_Y,
  output SB_X,
  output S_SB,
  output S_ADL,
  output SB_S,
  output S_S,
  output NDB_ADD,
  output DB_ADD,
  output _0_ADD,
  output SB_ADD,
  output ADL_ADD,
  output ANDS,
  output EORS,
  output ORS,
  output nACIN,
  output SUMS,
  output nDAA,
  output ADD_SB7,
  output ADD_SB06,
  output ADD_ADL,
  output nDSA,
  output SRS,
  output DL_ADL,
  output DL_DB,
  output DL_ADH,
  output ADH_ABH,
  output ADL_ABL,
  output SB_AC,
  output AC_SB,
  output _0_ADH0,
  output _0_ADH17,
  output AC_DB,
  output SB_DB,
  output SB_ADH,
  output ADL_PCL,
  output PCL_PCL,
  output PCH_ADH,
  output PCL_ADL,
  output PCH_DB,
  output PCL_DB,
  output ADH_PCH,
  output PCH_PCH,
  output _0_IR,
  output nT1X,
  output nT0,
  output _1_PC,
  output TRES2,
  output FETCH,
  output nT7,
  output nT6,
  output T1,
  output nREADY,
  output P_DB,
  output [7:0] DB_OUT
);

  wire alu_setup_1_and, alu_setup_1_inc_sb, alu_setup_1_sr, B_OUT, branch_logic_1_brfw,
       branch_logic_1_nbrtaken, BRK6E, bus_control_1_pgx, bus_control_1_ztst, dispatch_1_acrl2, DORES,
       flags_1_nn_out, flags_1_nv_out, flags_1_nz_out, flags_control_1__0_v, flags_control_1_acr_c,
       flags_control_1_db_c, flags_control_1_db_n, flags_control_1_db_p, flags_control_1_db_v,
       flags_control_1_dbz_z, flags_control_1_ir5_c, flags_control_1_ir5_d, flags_control_1_ir5_i, nC_OUT,
       nD_OUT, nI_OUT, pc_setup_1_dl_pch, pc_setup_1_nadl_pcl, pc_setup_1_npch_pch, pc_setup_1_pc_db,
       regs_control_1_nsbxy, regs_control_1_stkop, regs_control_1_stxy, STOR, T0, T6, T7;

  INT_CONTROL int_control_1 (
    .PHI1(PHI1), .PHI2(PHI2), .nready(nREADY), .BRK5(X22), .nNMIP(nNMIP), .RESP(RESP), .BRK6E(BRK6E),
    .DORES(DORES), .B_OUT(B_OUT), .nIRQP(nIRQP), .nI_OUT(nI_OUT), .T0(T0), .BR2(X80), ._0_ADL0(_0_ADL0),
    ._0_ADL1(_0_ADL1), ._0_ADL2(_0_ADL2));
  REGS_CONTROL regs_control_1 (
    .nready(nREADY), .PHI1(PHI1), .STOR(STOR), .Y_SB(Y_SB), .X_SB(X_SB), .S_ADL(S_ADL), .SB_S(SB_S),
    .S_S(S_S), .STXY(regs_control_1_stxy), .nSBXY(regs_control_1_nsbxy), .STKOP(regs_control_1_stkop),
    .D0(X0), .D1(X1), .D2(X2), .D3(X3), .D4(X4), .D5(X5), .D6(X6), .D7(X7), .D8(X8), .D9(X9), .D10(X10),
    .D11(X11), .D12(X12), .D13(X13), .D14(X14), .D15(X15), .D16(X16), .D17(X17), .D18(X18), .D19(X19),
    .D20(X20), .D21(X21), .D22(X22), .D23(X23), .D24(X24), .D25(X25), .D26(X26), .D48(X48), .SB_X(SB_X),
    .SB_Y(SB_Y), .S_SB(S_SB), .D35(X35), .PHI2(PHI2));
  ALU_SETUP alu_setup_1 (
    .NDB_ADD(NDB_ADD), .DB_ADD(DB_ADD), .D27(X27), ._0_ADD(_0_ADD), .D29(X29), .D30(X30), .SB_ADD(SB_ADD),
    .D31(X31), .D32(X32), .D33(X33), .ADL_ADD(ADL_ADD), .D34(X34), .D35(X35), .ANDS(ANDS), .D36(X36),
    .D37(X37), .D38(X38), .EORS(EORS), .D39(X39), .D40(X40), .ORS(ORS), .D41(X41), .D42(X42), .nACIN(nACIN),
    .D43(X43), .D44(X44), .D45(X45), .SRS(SRS), .D47(X47), .SUMS(SUMS), .D48(X48), .D49(X49), .nDAA(nDAA),
    .D50(X50), .D51(X51), .D52(X52), .ADD_SB7(ADD_SB7), .D53(X53), .D54(X54), .ADD_SB06(ADD_SB06), .D56(X56),
    .ADD_ADL(ADD_ADL), .nDSA(nDSA), .PHI1(PHI1), .PHI2(PHI2), .nready(nREADY), .T0(T0), .T6(T6),
    .STKOP(regs_control_1_stkop), .PGX(bus_control_1_pgx), .T1(T1), .T7(T7), .BRK6E(BRK6E), .BR3(X93),
    .nD_OUT(nD_OUT), .nC_OUT(nC_OUT), .D75(X75), .D76(X76), .D84(X84), .T4(X85), .T3(X86), .D87(X87),
    .D88(X88), .D89(X89), .INC_SB(alu_setup_1_inc_sb), .SR(alu_setup_1_sr), .D26(X26),
    .BRFW(branch_logic_1_brfw), .D69(X69), .D70(X70), .AND(alu_setup_1_and));
  BUS_CONTROL bus_control_1 (
    .PHI1(PHI1), .PHI2(PHI2), .D58(X58), .D59(X59), .D60(X60), .D61(X61), .D62(X62), .D63(X63), .D64(X64),
    .D65(X65), .D66(X66), .D67(X67), .D68(X68), .D71(X71), .D72(X72), .BR0(X73), .D81(X81), .D82(X82),
    .D89(X89), .D90(X90), .D91(X91), .DL_ADH(DL_ADH), .DL_DB(DL_DB), .DL_ADL(DL_ADL), .BR2(X80),
    .SB_ADH(SB_ADH), .ADH_ABH(ADH_ABH), .ADL_ABL(ADL_ABL), .SB_AC(SB_AC), .AC_SB(AC_SB), .D57(X57),
    ._0_ADH17(_0_ADH17), .SB_DB(SB_DB), .BR3(X93), .nready(nREADY), .T2(X28), .PGX(bus_control_1_pgx),
    .D84(X84), .D128(X128), .D101(X101), .D46(X46), .D48(X48), .D47(X47), .D45(X45),
    .INC_SB(alu_setup_1_inc_sb), .BRK6E(BRK6E), .D55(X55), .D83(X83), .STXY(regs_control_1_stxy),
    ._0_ADL0(_0_ADL0), .nSBXY(regs_control_1_nsbxy), .ZTST(bus_control_1_ztst), .DL_PCH(pc_setup_1_dl_pch),
    .ACRL2(dispatch_1_acrl2), .STOR(STOR), .nPCH_PCH(pc_setup_1_npch_pch), .T7(T7), .T6(T6), .T1(T1),
    .D56(X56), .T0(T0), .D74(X74), .D79(X79), .AC_DB(AC_DB), .AND(alu_setup_1_and), ._0_ADH0(_0_ADH0));
  PC_SETUP pc_setup_1 (
    .BR0(X73), .PHI1(PHI1), .PHI2(PHI2), .D56(X56), .D77(X77), .D78(X78), .D83(X83), .D84(X84), .D94(X94),
    .D95(X95), .D96(X96), .nready(nREADY), .BR3(X93), .BR2(X80), .T0(T0), .T1(T1), .PCL_DB(PCL_DB),
    .PCH_DB(PCH_DB), .PC_DB(pc_setup_1_pc_db), .PCL_ADL(PCL_ADL), .PCH_ADH(PCH_ADH), .PCL_PCL(PCL_PCL),
    .ADL_PCL(ADL_PCL), .DL_PCH(pc_setup_1_dl_pch), .nADL_PCL(pc_setup_1_nadl_pcl), .ADH_PCH(ADH_PCH),
    .PCH_PCH(PCH_PCH), .nPCH_PCH(pc_setup_1_npch_pch));
  DISPATCH dispatch_1 (
    .PHI1(PHI1), .PHI2(PHI2), .BRK6E(BRK6E), .BR2(X80), .RESP(RESP), .ACR(ACR), .D91(X91), .D92(X92),
    .D106(X106), .D107(X107), .D111(X111), .D122(X122), .D123(X123), .D124(X124), .D125(X125), .B_OUT(B_OUT),
    .nBRTAKEN(branch_logic_1_nbrtaken), .nTWOCYCLE(nTWOCYCLE), .RDY(RDY), .T6(T6), .T7(T7), ._0_IR(_0_IR),
    .FETCH(FETCH), .T0(T0), .nT1X(nT1X), .nready(nREADY), ._1_PC(_1_PC), .D97(X97), .D98(X98), .D100(X100),
    .BR3(X93), .D96(X96), .STOR(STOR), .DORES(DORES), .D101(X101), .D102(X102), .D103(X103), .D104(X104),
    .D105(X105), .PC_DB(pc_setup_1_pc_db), .BRFW(branch_logic_1_brfw), .IMPLIED(IMPLIED),
    .nADL_PCL(pc_setup_1_nadl_pcl), .TRES2(TRES2), .T1(T1), .nT0(nT0), .ACRL2(dispatch_1_acrl2), .WR(WR));
  not not_1 (nT6, T6);
  not not_2 (nT7, T7);
  FLAGS_CONTROL flags_control_1 (
    .PHI2(PHI2), .D98(X98), .D99(X99), .D108(X108), .D110(X110), .D120(X120), .D127(X127), .D107(X107),
    .T7(T7), .D109(X109), .D112(X112), .D116(X116), .D117(X117), .D118(X118), .D119(X119), .D114(X114),
    .D115(X115), .nready(nREADY), .SR(alu_setup_1_sr), .D113(X113), .P_DB(P_DB),
    .IR5_I(flags_control_1_ir5_i), .IR5_C(flags_control_1_ir5_c), .IR5_D(flags_control_1_ir5_d),
    ._0_V(flags_control_1__0_v), .ACR_C(flags_control_1_acr_c), .DBZ_Z(flags_control_1_dbz_z),
    .DB_N(flags_control_1_db_n), .DB_P(flags_control_1_db_p), .DB_C(flags_control_1_db_c),
    .DB_V(flags_control_1_db_v), .ZTST(bus_control_1_ztst));
  FLAGS flags_1 (
    .PHI1(PHI1), .PHI2(PHI2), .B_OUT(B_OUT), .DB(DB_IN), .DB_P(flags_control_1_db_p),
    .DBZ_Z(flags_control_1_dbz_z), .DB_N(flags_control_1_db_n), .IR5_C(flags_control_1_ir5_c),
    .ACR_C(flags_control_1_acr_c), .DB_C(flags_control_1_db_c), .IR5_D(flags_control_1_ir5_d),
    .IR5_I(flags_control_1_ir5_i), .ACR(ACR), .nIR5(nIR5), .AVR(AVR), .D112(X112),
    .DB_V(flags_control_1_db_v), ._0_V(flags_control_1__0_v), .DB0(DB_OUT[0]), .DB1(DB_OUT[1]),
    .DB2(DB_OUT[2]), .DB3(DB_OUT[3]), .DB4(DB_OUT[4]), .DB5(DB_OUT[5]), .DB6(DB_OUT[6]), .DB7(DB_OUT[7]),
    .nZ_OUT(flags_1_nz_out), .nN_OUT(flags_1_nn_out), .nC_OUT(nC_OUT), .nD_OUT(nD_OUT), .nI_OUT(nI_OUT),
    .nV_OUT(flags_1_nv_out), .SO(SO), .BRK6E(BRK6E));
  BRANCH_LOGIC branch_logic_1 (
    .nIR5(nIR5), .D126(X126), .nC_OUT(nC_OUT), .nV_OUT(flags_1_nv_out), .nN_OUT(flags_1_nn_out),
    .nZ_OUT(flags_1_nz_out), .PHI1(PHI1), .PHI2(PHI2), .DB7(DB_IN[7]), .BR2(X80),
    .nBRTAKEN(branch_logic_1_nbrtaken), .BRFW(branch_logic_1_brfw), .D121(X121));

  // Other names for the same wires on the sheet: BR0 = X73; BR2 = X80; BR3 = X93; T2 = X28; T3 = X86; T4 = X85

  // Notes on the sheet:
  //   BRK5
  //   STK2
  //   JSR2
endmodule

module INT_CONTROL (
  input  PHI1,
  input  PHI2,
  input  BRK5,
  input  nready,
  input  RESP,
  input  nNMIP,
  input  BR2,
  input  T0,
  input  nIRQP,
  input  nI_OUT,
  output BRK6E,
  output _0_ADL0,
  output _0_ADL1,
  output _0_ADL2,
  output DORES,
  output B_OUT
);

  wire and_1_out, and_2_out, and_3_out, b_latch1_q, b_latch2_q, brk5_latch_q, brk6_latch1_not_q,
       brk6_latch2_not_q, brk6e_latch_q, BRK7, brk7_latch_not_q, delay_latch2_q, donmi_latch_q,
       ff1_latch_not_q, ff1_latch_q, ff2_latch_q, nand_1_out, nmip_latch_q, nor_1_out, nor_2_out, nor_3_out,
       nor_4_out, nor_5_out, nor_6_out, nor_7_out, nor_8_out, nor_9_out, nor_10_out, nor_13_out, not_1_out,
       not_2_out, not_4_out, not_5_out, or_1_out, or_2_out, or_3_out, res_latch1_q, res_latch2_q;

  not not_1 (not_1_out, nI_OUT);
  and and_1 (and_1_out, BRK5, not_2_out);
  not not_2 (not_2_out, nready);
  or or_1 (or_1_out, BR2, T0);
  and and_2 (and_2_out, or_1_out, nand_1_out);
  or or_2 (or_2_out, nIRQP, not_1_out);
  nand nand_1 (nand_1_out, or_2_out, nor_6_out);
  D_Latch brk5_latch (.EN(PHI2), .D(and_1_out), .Q(brk5_latch_q));  // open: NOT_Q
  D_Latch res_latch1 (.EN(PHI2), .D(RESP), .Q(res_latch1_q));  // open: NOT_Q
  D_Latch brk7_latch (.EN(PHI2), .D(BRK7), .NOT_Q(brk7_latch_not_q));  // open: Q
  D_Latch nmip_latch (.EN(PHI1), .D(nNMIP), .Q(nmip_latch_q));  // open: NOT_Q
  D_Latch delay_latch2 (.EN(PHI1), .D(ff1_latch_not_q), .Q(delay_latch2_q));  // open: NOT_Q
  D_Latch donmi_latch (.EN(PHI1), .D(nor_10_out), .Q(donmi_latch_q));  // open: NOT_Q
  D_Latch brk6e_latch (.EN(PHI1), .D(BRK6E), .Q(brk6e_latch_q));  // open: NOT_Q
  nor nor_1 (nor_1_out, brk5_latch_q, and_3_out);
  and and_3 (and_3_out, brk6_latch1_not_q, nready);
  nor nor_2 (nor_2_out, BRK6E, nor_3_out);
  nor nor_3 (nor_3_out, res_latch2_q, res_latch1_q);
  nor nor_4 (nor_4_out, nmip_latch_q, nor_5_out);
  nor nor_5 (nor_5_out, ff2_latch_q, delay_latch2_q);
  nor nor_6 (nor_6_out, donmi_latch_q, nor_7_out);
  nor nor_7 (nor_7_out, ff1_latch_q, brk6e_latch_q);
  nor nor_8 (nor_8_out, and_2_out, b_latch1_q);
  nor nor_9 (nor_9_out, b_latch2_q, BRK6E);
  D_Latch brk6_latch1 (.EN(PHI1), .D(nor_1_out), .NOT_Q(brk6_latch1_not_q));  // open: Q
  D_Latch res_latch2 (.EN(PHI1), .D(nor_2_out), .Q(res_latch2_q));  // open: NOT_Q
  not not_3 (DORES, nor_3_out);
  nor nor_10 (nor_10_out, brk7_latch_not_q, nNMIP, nor_4_out);
  D_Latch ff2_latch (.EN(PHI2), .D(nor_4_out), .Q(ff2_latch_q));  // open: NOT_Q
  D_Latch ff1_latch (.EN(PHI2), .D(nor_6_out), .Q(ff1_latch_q), .NOT_Q(ff1_latch_not_q));
  D_Latch b_latch2 (.EN(PHI2), .D(nor_8_out), .Q(b_latch2_q));  // open: NOT_Q
  D_Latch b_latch1 (.EN(PHI1), .D(nor_9_out), .Q(b_latch1_q));  // open: NOT_Q
  nor nor_11 (BRK7, and_1_out, brk6_latch1_not_q);
  not not_4 (not_4_out, and_1_out);
  not not_5 (not_5_out, DORES);
  nor nor_12 (B_OUT, DORES, nor_9_out);
  or or_3 (or_3_out, BRK7, not_5_out);
  nor nor_13 (nor_13_out, BRK7, DORES, nor_6_out);
  D_Latch brk6_latch2 (.EN(PHI2), .D(brk6_latch1_not_q), .NOT_Q(brk6_latch2_not_q));  // open: Q
  D_Latch zadl0_latch (.EN(PHI2), .D(not_4_out), .NOT_Q(_0_ADL0));  // open: Q
  D_Latch zadl1_latch (.EN(PHI2), .D(or_3_out), .NOT_Q(_0_ADL1));  // open: Q
  D_Latch zadl2_latch (.EN(PHI2), .D(nor_13_out), .Q(_0_ADL2));  // open: NOT_Q
  nor nor_14 (BRK6E, brk6_latch2_not_q, nready);

  // Notes on the sheet:
  //   BRK_FF
  //   RES_FF
  //   NMI EDGE DETECT
  //   NMI_FF1
  //   B_FF
  //   INTERRUPT CYCLE 6-7
  //   RESET FLIP/FLOP
  //   NMI_FF2
  //   INTERRUPT CHECK
  //   /DONMI
  //   B FLAG
  //   FFFA:NMI, 1010
  //   FFFC:RESET, 1100
  //   FFFE:IRQ/BRK, 1110
endmodule

// REGS CONTROL
module REGS_CONTROL (
  input  PHI1,
  input  PHI2,
  input  D17,
  input  D1,
  input  D0,
  input  D2,
  input  D3,
  input  D4,
  input  D5,
  input  D6,
  input  STOR,
  input  D7,
  input  D8,
  input  D9,
  input  D10,
  input  D11,
  input  D12,
  input  D13,
  input  D14,
  input  D15,
  input  D16,
  input  D18,
  input  D19,
  input  D20,
  input  D48,
  input  D21,
  input  D22,
  input  D23,
  input  D24,
  input  D25,
  input  D26,
  input  nready,
  input  D35,
  output S_SB,
  output Y_SB,
  output STXY,
  output X_SB,
  output SB_X,
  output nSBXY,
  output SB_Y,
  output SB_S,
  output S_S,
  output STKOP,
  output S_ADL
);

  wire and_1_out, and_2_out, and_3_out, and_4_out, and_5_out, nor_1_out, nor_2_out, nor_3_out, nor_5_out,
       nor_6_out, nor_7_out, nor_9_out, nor_10_out, nor_11_out, nor_12_out, nor_13_out, nor_14_out,
       nor_15_out, nor_16_out, not_1_out, not_2_out, not_3_out, not_4_out, nready_latch_not_q,
       nready_latch_q, sadl_latch_not_q, sbs_latch_q, sbx_latch_q, sby_latch_q, ss_latch_q, ssb_latch_not_q,
       xsb_latch_q, ysb_latch_q;

  not not_1 (not_1_out, D17);
  and and_1 (and_1_out, D7, D6);
  and and_2 (and_2_out, D6, not_2_out);
  not not_2 (not_2_out, D7);
  nor nor_1 (nor_1_out, D14, D15, D16);
  nor nor_2 (nor_2_out, D18, D19, D20);
  not not_3 (not_3_out, D48);
  nor nor_3 (nor_3_out, D21, D22, D23, D24, D25, D26);
  and and_3 (and_3_out, D0, STOR);
  nor nor_4 (STXY, and_3_out, and_4_out);
  and and_4 (and_4_out, STOR, D12);
  D_Latch nready_latch (.EN(PHI1), .D(nready), .Q(nready_latch_q), .NOT_Q(nready_latch_not_q));
  nor nor_5 (nor_5_out, D1, D2, D3, D4, D5, and_1_out, and_3_out);
  nor nor_6 (nor_6_out, and_4_out, and_2_out, D8, D9, D10, D11, D13);
  nor nor_7 (nor_7_out, not_3_out, nready);
  nor nor_8 (STKOP, nor_3_out, nready_latch_q);
  and and_5 (and_5_out, D21, nready_latch_not_q);
  nor nor_9 (nor_9_out, D13, nor_7_out, STKOP);
  nor nor_10 (nor_10_out, and_5_out, D35);
  nand nand_1 (nSBXY, nor_1_out, nor_2_out);
  not not_4 (not_4_out, nor_9_out);
  D_Latch ssb_latch (.EN(PHI2), .D(not_1_out), .NOT_Q(ssb_latch_not_q));  // open: Q
  D_Latch ysb_latch (.EN(PHI2), .D(nor_5_out), .Q(ysb_latch_q));  // open: NOT_Q
  D_Latch xsb_latch (.EN(PHI2), .D(nor_6_out), .Q(xsb_latch_q));  // open: NOT_Q
  D_Latch sbx_latch (.EN(PHI2), .D(nor_1_out), .Q(sbx_latch_q));  // open: NOT_Q
  D_Latch sby_latch (.EN(PHI2), .D(nor_2_out), .Q(sby_latch_q));  // open: NOT_Q
  D_Latch sbs_latch (.EN(PHI2), .D(nor_9_out), .Q(sbs_latch_q));  // open: NOT_Q
  D_Latch ss_latch (.EN(PHI2), .D(not_4_out), .Q(ss_latch_q));  // open: NOT_Q
  D_Latch sadl_latch (.EN(PHI2), .D(nor_10_out), .NOT_Q(sadl_latch_not_q));  // open: Q
  buf buffer_1 (S_SB, ssb_latch_not_q);
  nor nor_11 (nor_11_out, ysb_latch_q, PHI2);
  buf buffer_2 (Y_SB, nor_11_out);
  buf buffer_3 (X_SB, nor_12_out);
  nor nor_12 (nor_12_out, xsb_latch_q, PHI2);
  buf buffer_4 (SB_X, nor_13_out);
  nor nor_13 (nor_13_out, sbx_latch_q, PHI2);
  buf buffer_5 (SB_Y, nor_14_out);
  nor nor_14 (nor_14_out, sby_latch_q, PHI2);
  buf buffer_6 (SB_S, nor_15_out);
  nor nor_15 (nor_15_out, sbs_latch_q, PHI2);
  buf buffer_7 (S_S, nor_16_out);
  nor nor_16 (nor_16_out, ss_latch_q, PHI2);
  buf buffer_8 (S_ADL, sadl_latch_not_q);

  // Notes on the sheet:
  //   JSR2
  //   STK2
  //   #S/SB
  //   TXS
  //   #SB/X
  //   #SB/Y
  //   STKOP
  //   #S/SB
  //   #Y/SB
  //   #X/SB
  //   #SBXY
  //   #SB/S
  //   #S/ADL
endmodule

// EXTENDED CYCLE COUNTER
module EXTENDED_CYCLE_COUNTER (
  input  PHI1,
  input  PHI2,
  input  nready,
  input  T1,
  input  TRES2,
  output nT2,
  output nT3,
  output nT4,
  output nT5
);

  wire multiplexer_1_out, multiplexer_2_out, multiplexer_3_out, multiplexer_4_out, t1_latch_not_q,
       t2_latch1_q, t2_latch2_q, t3_latch1_q, t3_latch2_q, t4_latch1_q, t4_latch2_q, t5_latch1_q, t5_latch2_q;

  D_Latch t1_latch (.EN(PHI2), .D(T1), .NOT_Q(t1_latch_not_q));  // open: Q
  Multiplexer #(.enable("false")) multiplexer_1 (
    .in0(t1_latch_not_q), .in1(t2_latch2_q), .out(multiplexer_1_out), .sel(nready));
  Multiplexer #(.enable("false")) multiplexer_2 (
    .in0(t2_latch2_q), .in1(t3_latch2_q), .out(multiplexer_2_out), .sel(nready));
  Multiplexer #(.enable("false")) multiplexer_3 (
    .in0(t3_latch2_q), .in1(t4_latch2_q), .out(multiplexer_3_out), .sel(nready));
  Multiplexer #(.enable("false")) multiplexer_4 (
    .in0(t4_latch2_q), .in1(t5_latch2_q), .out(multiplexer_4_out), .sel(nready));
  D_Latch t2_latch1 (.EN(PHI1), .D(multiplexer_1_out), .Q(t2_latch1_q));  // open: NOT_Q
  D_Latch t3_latch1 (.EN(PHI1), .D(multiplexer_2_out), .Q(t3_latch1_q));  // open: NOT_Q
  D_Latch t4_latch1 (.EN(PHI1), .D(multiplexer_3_out), .Q(t4_latch1_q));  // open: NOT_Q
  D_Latch t5_latch1 (.EN(PHI1), .D(multiplexer_4_out), .Q(t5_latch1_q));  // open: NOT_Q
  or or_1 (nT2, t2_latch1_q, TRES2);
  or or_2 (nT3, t3_latch1_q, TRES2);
  or or_3 (nT4, t4_latch1_q, TRES2);
  or or_4 (nT5, t5_latch1_q, TRES2);
  D_Latch t2_latch2 (.EN(PHI2), .D(nT2), .Q(t2_latch2_q));  // open: NOT_Q
  D_Latch t3_latch2 (.EN(PHI2), .D(nT3), .Q(t3_latch2_q));  // open: NOT_Q
  D_Latch t4_latch2 (.EN(PHI2), .D(nT4), .Q(t4_latch2_q));  // open: NOT_Q
  D_Latch t5_latch2 (.EN(PHI2), .D(nT5), .Q(t5_latch2_q));  // open: NOT_Q
endmodule

// ALU SETUP
module ALU_SETUP (
  input  PHI1,
  input  PHI2,
  input  BRFW,
  input  nready,
  input  STKOP,
  input  D26,
  input  BRK6E,
  input  D30,
  input  D31,
  input  D45,
  input  D48,
  input  D47,
  input  D33,
  input  D34,
  input  D35,
  input  D36,
  input  D37,
  input  D38,
  input  D39,
  input  D40,
  input  D41,
  input  D42,
  input  D43,
  input  D44,
  input  D49,
  input  D50,
  input  D51,
  input  D54,
  input  nC_OUT,
  input  D56,
  input  D53,
  input  D52,
  input  nD_OUT,
  input  PGX,
  input  BR3,
  input  T0,
  input  T1,
  input  T6,
  input  T7,
  input  D29,
  input  D75,
  input  D76,
  input  D69,
  input  D70,
  input  D32,
  input  D27,
  input  D84,
  input  T4,
  input  T3,
  input  D87,
  input  D88,
  input  D89,
  output _0_ADD,
  output SB_ADD,
  output NDB_ADD,
  output DB_ADD,
  output ADL_ADD,
  output AND,
  output ANDS,
  output EORS,
  output ORS,
  output SRS,
  output SUMS,
  output nACIN,
  output nDAA,
  output nDSA,
  output ADD_SB06,
  output INC_SB,
  output SR,
  output ADD_SB7,
  output ADD_ADL
);

  wire acin_latch1_q, acin_latch2_q, acin_latch3_q, acin_latch4_q, addadl_latch_not_q, addsb06_latch_not_q,
       addsb7_latch_q, adladd_latch_q, and_1_out, and_2_out, and_3_out, ands_latch1_not_q, ands_latch2_not_q,
       BRX, cout_latch_q, daa_latch1_not_q, daa_latch2_not_q, dbadd_latch_q, dsa_latch1_not_q,
       eors_latch1_not_q, eors_latch2_not_q, ff_latch1_q, ff_latch2_q, multiplexer_1_out, mux_latch1_q,
       nand_1_out, nand_2_out, nand_3_out, nand_4_out, nand_5_out, nand_6_out, ndbadd_latch_q, nor_1_out,
       nor_2_out, nor_3_out, nor_4_out, nor_5_out, nor_6_out, nor_7_out, nor_8_out, nor_9_out, nor_10_out,
       nor_11_out, nor_12_out, nor_13_out, nor_14_out, nor_15_out, nor_16_out, nor_17_out, nor_18_out,
       not_1_out, not_2_out, not_3_out, not_4_out, not_5_out, not_6_out, not_7_out, not_8_out, not_9_out,
       nready_latch_q, OR, or_5_out, or_7_out, or_8_out, or_9_out, ors_latch1_not_q, ors_latch2_not_q,
       sbadd_latch_q, sr_latch1_not_q, sr_latch2_q, srs_latch1_not_q, srs_latch2_not_q, sums_latch1_not_q,
       sums_latch2_not_q, zadd_latch_q;

  not not_1 (not_1_out, D54);
  and and_1 (and_1_out, D33, not_2_out);
  not not_2 (not_2_out, D34);
  and and_2 (and_2_out, T6, D44);
  not not_3 (not_3_out, nD_OUT);
  and and_3 (and_3_out, D76, T6);
  or or_1 (INC_SB, D39, D40, D41, D42, D43, and_2_out);
  or or_2 (SR, D75, and_3_out);
  or or_3 (AND, D69, D70);
  or or_4 (OR, D32, nready);
  nor nor_1 (nor_1_out, D84, T4, T3, D87, D88, D89, D26);
  nor nor_2 (nor_2_out, and_1_out, D35, D36, D37, D38, D39, nready);
  not not_4 (not_4_out, BR3);
  nor nor_3 (nor_3_out, T0, T6);
  nor nor_4 (nor_4_out, not_4_out, BRFW);
  nor nor_5 (nor_5_out, nC_OUT, nor_3_out);
  or or_5 (or_5_out, D53, D52);
  nand nand_1 (nand_1_out, D52, not_3_out);
  nor nor_6 (nor_6_out, STKOP, BRK6E, D30, D31, D45, D48, D47, nready, INC_SB);
  or or_6 (BRX, D49, D50, nor_4_out);
  nand nand_2 (nand_2_out, nor_5_out, or_5_out);
  or or_7 (or_7_out, nand_1_out, D51);
  nand nand_3 (nand_3_out, D51, not_3_out);
  D_Latch nready_latch (.EN(PHI1), .D(nready), .Q(nready_latch_q));  // open: NOT_Q
  not not_5 (not_5_out, SR);
  nand nand_4 (nand_4_out, not_1_out, nand_2_out);
  nor nor_7 (nor_7_out, nready_latch_q, not_5_out);
  not not_6 (not_6_out, D47);
  D_Latch mux_latch1 (.EN(PHI2), .D(nor_7_out), .Q(mux_latch1_q));  // open: NOT_Q
  D_Latch ff_latch2 (.EN(PHI2), .D(ff_latch1_q), .Q(ff_latch2_q));  // open: NOT_Q
  D_Latch cout_latch (.EN(PHI2), .D(nC_OUT), .Q(cout_latch_q));  // open: NOT_Q
  D_Latch sr_latch1 (.EN(PHI2), .D(SR), .NOT_Q(sr_latch1_not_q));  // open: Q
  nor nor_8 (nor_8_out, nor_2_out, not_6_out);
  Multiplexer #(.enable("false")) multiplexer_1 (
    .in0(ff_latch2_q), .in1(cout_latch_q), .out(multiplexer_1_out), .sel(mux_latch1_q));
  D_Latch acin_latch1 (.EN(PHI2), .D(nor_8_out), .Q(acin_latch1_q));  // open: NOT_Q
  D_Latch acin_latch2 (.EN(PHI2), .D(INC_SB), .Q(acin_latch2_q));  // open: NOT_Q
  D_Latch acin_latch3 (.EN(PHI2), .D(BRX), .Q(acin_latch3_q));  // open: NOT_Q
  D_Latch acin_latch4 (.EN(PHI2), .D(nand_4_out), .Q(acin_latch4_q));  // open: NOT_Q
  D_Latch ff_latch1 (.EN(PHI1), .D(multiplexer_1_out), .Q(ff_latch1_q));  // open: NOT_Q
  not not_7 (not_7_out, D27);
  D_Latch sr_latch2 (.EN(PHI1), .D(sr_latch1_not_q), .Q(sr_latch2_q));  // open: NOT_Q
  or or_8 (or_8_out, BRX, D56, D51);
  not not_8 (not_8_out, nready);
  nor nor_9 (nor_9_out, ff_latch1_q, not_7_out, sr_latch2_q);
  nand nand_5 (nand_5_out, or_8_out, not_8_out);
  nor nor_10 (nor_10_out, acin_latch1_q, acin_latch2_q, acin_latch3_q, acin_latch4_q);
  nor nor_11 (nor_11_out, T7, STKOP, D56, T1, PGX);
  nand nand_6 (nand_6_out, nand_5_out, nor_2_out);
  not not_9 (not_9_out, nor_6_out);
  nor nor_12 (nor_12_out, SR, OR, D29, AND);
  nor nor_13 (nor_13_out, nor_11_out, nor_9_out);
  or or_9 (or_9_out, nor_1_out, PGX);
  D_Latch zadd_latch (.EN(PHI2), .D(nor_6_out), .Q(zadd_latch_q));  // open: NOT_Q
  D_Latch sbadd_latch (.EN(PHI2), .D(not_9_out), .Q(sbadd_latch_q));  // open: NOT_Q
  D_Latch ndbadd_latch (.EN(PHI2), .D(nand_5_out), .Q(ndbadd_latch_q));  // open: NOT_Q
  D_Latch dbadd_latch (.EN(PHI2), .D(nand_6_out), .Q(dbadd_latch_q));  // open: NOT_Q
  D_Latch adladd_latch (.EN(PHI2), .D(nor_2_out), .Q(adladd_latch_q));  // open: NOT_Q
  D_Latch ands_latch1 (.EN(PHI2), .D(AND), .NOT_Q(ands_latch1_not_q));  // open: Q
  D_Latch eors_latch1 (.EN(PHI2), .D(D29), .NOT_Q(eors_latch1_not_q));  // open: Q
  D_Latch ors_latch1 (.EN(PHI2), .D(OR), .NOT_Q(ors_latch1_not_q));  // open: Q
  D_Latch srs_latch1 (.EN(PHI2), .D(SR), .NOT_Q(srs_latch1_not_q));  // open: Q
  D_Latch sums_latch1 (.EN(PHI2), .D(nor_12_out), .NOT_Q(sums_latch1_not_q));  // open: Q
  D_Latch daa_latch1 (.EN(PHI2), .D(or_7_out), .NOT_Q(daa_latch1_not_q));  // open: Q
  D_Latch dsa_latch1 (.EN(PHI2), .D(nand_3_out), .NOT_Q(dsa_latch1_not_q));  // open: Q
  D_Latch addsb06_latch (.EN(PHI2), .D(nor_11_out), .NOT_Q(addsb06_latch_not_q));  // open: Q
  D_Latch addsb7_latch (.EN(PHI2), .D(nor_13_out), .Q(addsb7_latch_q));  // open: NOT_Q
  D_Latch addadl_latch (.EN(PHI2), .D(or_9_out), .NOT_Q(addadl_latch_not_q));  // open: Q
  nor nor_14 (nor_14_out, zadd_latch_q, PHI2);
  buf buffer_1 (_0_ADD, nor_14_out);
  buf buffer_2 (SB_ADD, nor_15_out);
  nor nor_15 (nor_15_out, sbadd_latch_q, PHI2);
  nor nor_16 (nor_16_out, ndbadd_latch_q, PHI2);
  buf buffer_3 (NDB_ADD, nor_16_out);
  nor nor_17 (nor_17_out, dbadd_latch_q, PHI2);
  buf buffer_4 (DB_ADD, nor_17_out);
  nor nor_18 (nor_18_out, adladd_latch_q, PHI2);
  buf buffer_5 (ADL_ADD, nor_18_out);
  D_Latch ands_latch2 (.EN(PHI1), .D(ands_latch1_not_q), .NOT_Q(ands_latch2_not_q));  // open: Q
  buf buffer_6 (ANDS, ands_latch2_not_q);
  D_Latch eors_latch2 (.EN(PHI1), .D(eors_latch1_not_q), .NOT_Q(eors_latch2_not_q));  // open: Q
  buf buffer_7 (EORS, eors_latch2_not_q);
  D_Latch ors_latch2 (.EN(PHI1), .D(ors_latch1_not_q), .NOT_Q(ors_latch2_not_q));  // open: Q
  buf buffer_8 (ORS, ors_latch2_not_q);
  D_Latch srs_latch2 (.EN(PHI1), .D(srs_latch1_not_q), .NOT_Q(srs_latch2_not_q));  // open: Q
  buf buffer_9 (SRS, srs_latch2_not_q);
  D_Latch sums_latch2 (.EN(PHI1), .D(sums_latch1_not_q), .NOT_Q(sums_latch2_not_q));  // open: Q
  buf buffer_10 (SUMS, sums_latch2_not_q);
  D_Latch acin_latch5 (.EN(PHI1), .D(nor_10_out), .Q(nACIN));  // open: NOT_Q
  D_Latch daa_latch2 (.EN(PHI1), .D(daa_latch1_not_q), .NOT_Q(daa_latch2_not_q));  // open: Q
  buf buffer_11 (nDAA, daa_latch2_not_q);
  D_Latch dsa_latch2 (.EN(PHI1), .D(dsa_latch1_not_q), .NOT_Q(nDSA));  // open: Q
  buf buffer_12 (ADD_SB06, addsb06_latch_not_q);
  buf buffer_13 (ADD_SB7, addsb7_latch_q);
  buf buffer_14 (ADD_ADL, addadl_latch_not_q);

  // Other names for the same wires on the sheet: EOR = D29; JSR_5 = D56; ROR = D27; RTI_5 = D26; RTS_5 = D84;
  //   SBC0 = D51

  // Notes on the sheet:
  //   JSR2
  //   RET
  //   STK2
  //   D_OUT
  //   #ADL/ADD
  //   NOADL
  //   SB/ADD
  //   CSET
  //   FF
  //   ADD SB7
  //   /ACIN
  //   #NDB/ADD
  //   #ADL/ADD
  //   #ADD/SB06
  //   care!
endmodule

// BRANCH LOGIC
module BRANCH_LOGIC (
  input  nIR5,
  input  D121,
  input  D126,
  input  nZ_OUT,
  input  nC_OUT,
  input  nV_OUT,
  input  nN_OUT,
  input  PHI1,
  input  PHI2,
  input  BR2,
  input  DB7,
  output nBRTAKEN,
  output BRFW
);

  wire br2_latch_q, brfw_latch2_q, multiplexer_1_out, multiplexer_2_out;

  Multiplexer #(.select(2), .disabled(0), .enable("false")) multiplexer_1 (
    .in0(nZ_OUT), .in1(nC_OUT), .in2(nV_OUT), .in3(nN_OUT), .out(multiplexer_1_out), .sel({D126, D121}));
  D_Latch br2_latch (.EN(PHI2), .D(BR2), .Q(br2_latch_q));  // open: NOT_Q
  D_Latch brfw_latch2 (.EN(PHI2), .D(BRFW), .Q(brfw_latch2_q));  // open: NOT_Q
  Multiplexer #(.enable("false")) multiplexer_2 (
    .in0(brfw_latch2_q), .in1(DB7), .out(multiplexer_2_out), .sel(br2_latch_q));
  xor xor_1 (nBRTAKEN, nIR5, multiplexer_1_out);
  D_Latch brfw_latch1 (.EN(PHI1), .D(multiplexer_2_out), .Q(BRFW));  // open: NOT_Q

  // Notes on the sheet:
  //   /IR6
  //   /IR7
  //   0
  //   1
  //   2
  //   3
  //   BRFW_FF
endmodule

// PROGRAM COUNTER SETUP
module PC_SETUP (
  input  PHI1,
  input  PHI2,
  input  BR3,
  input  BR2,
  input  D77,
  input  D78,
  input  D84,
  input  T0,
  input  T1,
  input  D83,
  input  BR0,
  input  D56,
  input  D94,
  input  D95,
  input  D96,
  input  nready,
  output PCL_DB,
  output PC_DB,
  output PCH_DB,
  output ADH_PCH,
  output PCH_PCH,
  output nPCH_PCH,
  output DL_PCH,
  output PCH_ADH,
  output PCL_ADL,
  output nADL_PCL,
  output ADL_PCL,
  output PCL_PCL
);

  wire adh_pch_latch_q, adl_pcl_latch_q, and_1_out, JB, nor_1_out, nor_3_out, nor_4_out, nor_5_out,
       nor_6_out, nor_8_out, nor_10_out, nor_11_out, nor_12_out, nor_13_out, nor_14_out, nor_15_out,
       not_1_out, not_2_out, not_3_out, not_5_out, nready_latch_not_q, nready_latch_q, pch_adh_latch_not_q,
       pch_db_latch1_q, pch_db_latch2_not_q, pch_pch_latch_q, pcl_adl_latch_not_q, pcl_db_latch1_not_q,
       pcl_db_latch2_not_q, pcl_pcl_latch_q;

  nor nor_1 (nor_1_out, D77, D78);
  nor nor_2 (JB, D94, D95, D96);
  D_Latch pch_db_latch1 (.EN(PHI2), .D(nor_1_out), .Q(pch_db_latch1_q));  // open: NOT_Q
  D_Latch nready_latch (.EN(PHI1), .D(nready), .Q(nready_latch_q), .NOT_Q(nready_latch_not_q));
  nor nor_3 (nor_3_out, pch_db_latch1_q, nready);
  not not_1 (not_1_out, T0);
  nor nor_4 (nor_4_out, JB, nready_latch_q);
  and and_1 (and_1_out, nready_latch_not_q, BR3);
  nor nor_5 (nor_5_out, not_1_out, nor_4_out);
  D_Latch pcl_db_latch1 (.EN(PHI1), .D(nor_3_out), .NOT_Q(pcl_db_latch1_not_q));  // open: Q
  nand nand_1 (PC_DB, pcl_db_latch1_not_q, nor_1_out);
  nor nor_6 (nor_6_out, D84, BR3, T0, T1, BR2, D83);
  not not_2 (not_2_out, T0);
  nor nor_7 (DL_PCH, not_2_out, JB);
  nor nor_8 (nor_8_out, T1, D83, D56, nor_5_out, BR2);
  not not_3 (not_3_out, nor_8_out);
  nor nor_9 (nADL_PCL, not_3_out, D84, T0, and_1_out);
  nor nor_10 (nor_10_out, DL_PCH, BR0, nor_8_out);
  not not_4 (nPCH_PCH, nor_6_out);
  nor nor_11 (nor_11_out, nor_10_out, BR3);
  not not_5 (not_5_out, nADL_PCL);
  D_Latch pcl_db_latch2 (.EN(PHI2), .D(pcl_db_latch1_not_q), .NOT_Q(pcl_db_latch2_not_q));  // open: Q
  D_Latch pch_db_latch2 (.EN(PHI2), .D(nor_1_out), .NOT_Q(pch_db_latch2_not_q));  // open: Q
  D_Latch adh_pch_latch (.EN(PHI2), .D(nor_6_out), .Q(adh_pch_latch_q));  // open: NOT_Q
  D_Latch pch_pch_latch (.EN(PHI2), .D(nPCH_PCH), .Q(pch_pch_latch_q));  // open: NOT_Q
  D_Latch pch_adh_latch (.EN(PHI2), .D(nor_11_out), .NOT_Q(pch_adh_latch_not_q));  // open: Q
  D_Latch pcl_adl_latch (.EN(PHI2), .D(nor_8_out), .NOT_Q(pcl_adl_latch_not_q));  // open: Q
  D_Latch adl_pcl_latch (.EN(PHI2), .D(nADL_PCL), .Q(adl_pcl_latch_q));  // open: NOT_Q
  D_Latch pcl_pcl_latch (.EN(PHI2), .D(not_5_out), .Q(pcl_pcl_latch_q));  // open: NOT_Q
  nor nor_12 (nor_12_out, adh_pch_latch_q, PHI2);
  nor nor_13 (nor_13_out, pch_pch_latch_q, PHI2);
  nor nor_14 (nor_14_out, adl_pcl_latch_q, PHI2);
  nor nor_15 (nor_15_out, pcl_pcl_latch_q, PHI2);
  buf buffer_1 (PCL_DB, pcl_db_latch2_not_q);
  buf buffer_2 (PCH_DB, pch_db_latch2_not_q);
  buf buffer_3 (ADH_PCH, nor_12_out);
  buf buffer_4 (PCH_PCH, nor_13_out);
  buf buffer_5 (PCH_ADH, pch_adh_latch_not_q);
  buf buffer_6 (PCL_ADL, pcl_adl_latch_not_q);
  buf buffer_7 (ADL_PCL, nor_14_out);
  buf buffer_8 (PCL_PCL, nor_15_out);

  // Other names for the same wires on the sheet: RTS_5 = D84

  // Notes on the sheet:
  //   ABS/2
  //   JSR/5
  //   #PCH/DB
  //   #PCL/DB
  //   PC/DB
  //   #ADH/PCH
  //   DL/PCH
  //   #PCL/ADL
  //   #ADL/PCL
endmodule

module DISPATCH (
  input  PHI1,
  input  PHI2,
  input  ACR,
  input  BRK6E,
  input  RESP,
  input  DORES,
  input  D106,
  input  D107,
  input  D91,
  input  D92,
  input  D97,
  input  PC_DB,
  input  D98,
  input  D100,
  input  D101,
  input  D102,
  input  D103,
  input  D104,
  input  D105,
  input  D96,
  input  RDY,
  input  D111,
  input  D122,
  input  D123,
  input  D124,
  input  D125,
  input  nBRTAKEN,
  input  BR2,
  input  BR3,
  input  nADL_PCL,
  input  IMPLIED,
  input  B_OUT,
  input  BRFW,
  input  nTWOCYCLE,
  output ACRL2,
  output T6,
  output T7,
  output TRES2,
  output STOR,
  output _0_IR,
  output FETCH,
  output nready,
  output WR,
  output _1_PC,
  output T1,
  output nT0,
  output T0,
  output nT1X
);

  wire acr_latch1_not_q, and_1_out, and_2_out, and_3_out, and_4_out, and_5_out, and_6_out, br_latch1_q,
       br_latch2_not_q, br_latch2_q, comp_latch2_q, comp_latch3_q, ENDS, ends_latch1_q, ends_latch2_q,
       fetch_latch_not_q, ipc_latch1_q, ipc_latch2_q, ipc_latch3_q, multiplexer_1_out, multiplexer_2_out,
       nand_1_out, nand_2_out, nMemOP, nor_2_out, nor_5_out, nor_6_out, nor_7_out, nor_8_out, nor_9_out,
       nor_10_out, nor_11_out, nor_12_out, nor_13_out, nor_14_out, nor_15_out, nor_16_out, nor_18_out,
       nor_19_out, nor_20_out, nor_22_out, nor_24_out, nor_25_out, nor_26_out, nor_27_out, nor_29_out,
       nor_30_out, not_1_out, not_2_out, not_3_out, not_4_out, not_5_out, not_6_out, not_7_out,
       NotReady_prime_prime, nready_latch_q, nSHIFT, nTRESX, or_1_out, or_2_out, or_3_out, or_4_out,
       rdydelay_latch1_not_q, ready_latch2_q, step_latch1_q, step_latch2_q, t0_latch_q, t1x_latch_q,
       t6_latch2_q, t7_latch1_not_q, t67_latch_q, tresx_latch1_q, tresx_latch2_not_q, wr_latch_q;

  not not_1 (not_1_out, D97);
  nor nor_1 (nSHIFT, D106, D107);
  nor nor_2 (nor_2_out, D91, D92);
  nor nor_3 (nMemOP, D111, D122, D123, D124, D125);
  Multiplexer #(.enable("false")) multiplexer_1 (
    .in0(ACR), .in1(ACRL2), .out(multiplexer_1_out), .sel(NotReady_prime_prime));
  or or_1 (or_1_out, D100, D101, D102, D103, D104, D105);
  not not_2 (not_2_out, nSHIFT);
  and and_1 (and_1_out, nBRTAKEN, BR2);
  or or_2 (or_2_out, BR2, BR3);
  nand nand_1 (nand_1_out, nSHIFT, not_1_out);
  nor nor_4 (STOR, not_1_out, nMemOP);
  nor nor_5 (nor_5_out, not_2_out, D96, nMemOP);
  nor nor_6 (nor_6_out, or_2_out, nADL_PCL);
  nor nor_7 (nor_7_out, BRFW, br_latch2_not_q);
  D_Latch acr_latch1 (.EN(PHI1), .D(multiplexer_1_out), .NOT_Q(acr_latch1_not_q));  // open: Q
  D_Latch tresx_latch1 (.EN(PHI2), .D(nor_2_out), .Q(tresx_latch1_q));  // open: NOT_Q
  nor nor_8 (nor_8_out, STOR, PC_DB, D98, D100, T6, T7);
  nor nor_9 (nor_9_out, T7, BR3, or_1_out, nor_5_out);
  nor nor_10 (nor_10_out, T0, and_1_out);
  not not_3 (not_3_out, T1);
  nor nor_11 (nor_11_out, and_1_out, nor_6_out);
  not not_4 (not_4_out, BR3);
  and and_2 (and_2_out, BRFW, ACR);
  not not_5 (not_5_out, ACR);
  and and_3 (and_3_out, not_5_out, nor_7_out);
  D_Latch acr_latch2 (.EN(PHI2), .D(acr_latch1_not_q), .NOT_Q(ACRL2));  // open: Q
  Multiplexer #(.enable("false")) multiplexer_2 (
    .in0(nor_10_out), .in1(not_3_out), .out(multiplexer_2_out), .sel(nready));
  D_Latch rdydelay_latch1 (.EN(PHI1), .D(nready), .NOT_Q(rdydelay_latch1_not_q));  // open: Q
  nor nor_12 (nor_12_out, not_4_out, NotReady_prime_prime);
  or or_3 (or_3_out, and_2_out, and_3_out);
  nor nor_13 (nor_13_out, multiplexer_1_out, tresx_latch1_q, nready, nand_1_out);
  nor nor_14 (nor_14_out, nready, nor_9_out);
  not not_6 (not_6_out, nready);
  nor nor_15 (nor_15_out, nSHIFT, nMemOP, nready);
  not not_7 (not_7_out, nready);
  D_Latch wr_latch (.EN(PHI2), .D(nor_8_out), .Q(wr_latch_q));  // open: NOT_Q
  D_Latch ends_latch1 (.EN(PHI2), .D(multiplexer_2_out), .Q(ends_latch1_q));  // open: NOT_Q
  D_Latch ends_latch2 (.EN(PHI2), .D(RESP), .Q(ends_latch2_q));  // open: NOT_Q
  D_Latch br_latch1 (.EN(PHI2), .D(nor_11_out), .Q(br_latch1_q));  // open: NOT_Q
  D_Latch rdydelay_latch2 (.EN(PHI2), .D(rdydelay_latch1_not_q), .NOT_Q(NotReady_prime_prime));  // open: Q
  D_Latch nready_latch (.EN(PHI1), .D(not_6_out), .Q(nready_latch_q));  // open: NOT_Q
  D_Latch br_latch2 (.EN(PHI2), .D(nor_12_out), .Q(br_latch2_q), .NOT_Q(br_latch2_not_q));
  D_Latch comp_latch2 (.EN(PHI1), .D(nTWOCYCLE), .Q(comp_latch2_q));  // open: NOT_Q
  D_Latch comp_latch3 (.EN(PHI1), .D(nTRESX), .Q(comp_latch3_q));  // open: NOT_Q
  and and_4 (and_4_out, t6_latch2_q, nready);
  nand nand_2 (nand_2_out, T6, not_7_out);
  nor nor_16 (nor_16_out, RESP, nor_14_out, ENDS);
  nor nor_17 (ENDS, ends_latch1_q, ends_latch2_q);
  and and_5 (and_5_out, br_latch2_q, or_3_out);
  and and_6 (and_6_out, comp_latch2_q, comp_latch3_q);
  D_Latch t67_latch (.EN(PHI2), .D(nor_15_out), .Q(t67_latch_q));  // open: NOT_Q
  D_Latch t7_latch1 (.EN(PHI2), .D(nand_2_out), .NOT_Q(t7_latch1_not_q));  // open: Q
  D_Latch tresx_latch2 (.EN(PHI2), .D(nor_16_out), .NOT_Q(tresx_latch2_not_q));  // open: Q
  nor nor_18 (nor_18_out, nor_26_out, nready);
  nor nor_19 (nor_19_out, T1, and_6_out);
  nor nor_20 (nor_20_out, and_4_out, t67_latch_q);
  nor nor_21 (nTRESX, nor_13_out, BRK6E, tresx_latch2_not_q);
  nor nor_22 (nor_22_out, RDY, ready_latch2_q);
  nor nor_23 (WR, nready, wr_latch_q, DORES);
  nor nor_24 (nor_24_out, br_latch1_q, nready, IMPLIED);
  nor nor_25 (nor_25_out, RESP, nready_latch_q, step_latch2_q);
  nor nor_26 (nor_26_out, step_latch1_q, and_5_out);
  nor nor_27 (nor_27_out, nor_18_out, ENDS);
  nor nor_28 (nT0, nor_19_out, nor_29_out);
  nor nor_29 (nor_29_out, t0_latch_q, t1x_latch_q);
  nor nor_30 (nor_30_out, t0_latch_q, nready);
  D_Latch t6_latch2 (.EN(PHI2), .D(T6), .Q(t6_latch2_q));  // open: NOT_Q
  D_Latch t6_latch1 (.EN(PHI1), .D(nor_20_out), .NOT_Q(T6));  // open: Q
  D_Latch t7_latch2 (.EN(PHI1), .D(t7_latch1_not_q), .Q(T7));  // open: NOT_Q
  D_Latch tres2_latch (.EN(PHI1), .D(nTRESX), .NOT_Q(TRES2));  // open: Q
  D_Latch fetch_latch (.EN(PHI2), .D(T1), .NOT_Q(fetch_latch_not_q));  // open: Q
  D_Latch ready_latch1 (.EN(PHI2), .D(nor_22_out), .Q(nready));  // open: NOT_Q
  D_Latch ready_latch2 (.EN(PHI1), .D(WR), .Q(ready_latch2_q));  // open: NOT_Q
  D_Latch ipc_latch1 (.EN(PHI1), .D(B_OUT), .Q(ipc_latch1_q));  // open: NOT_Q
  D_Latch ipc_latch3 (.EN(PHI1), .D(nor_24_out), .Q(ipc_latch3_q));  // open: NOT_Q
  or or_4 (or_4_out, ipc_latch3_q, ipc_latch2_q);
  D_Latch ipc_latch2 (.EN(PHI1), .D(and_5_out), .Q(ipc_latch2_q));  // open: NOT_Q
  D_Latch step_latch1 (.EN(PHI2), .D(nor_25_out), .Q(step_latch1_q));  // open: NOT_Q
  D_Latch step_latch2 (.EN(PHI1), .D(nor_26_out), .Q(step_latch2_q));  // open: NOT_Q
  D_Latch t1_latch (.EN(PHI1), .D(nor_27_out), .NOT_Q(T1));  // open: Q
  D_Latch t0_latch (.EN(PHI2), .D(nT0), .Q(t0_latch_q));  // open: NOT_Q
  D_Latch t1x_latch (.EN(PHI1), .D(nor_30_out), .Q(t1x_latch_q), .NOT_Q(nT1X));
  nor nor_31 (FETCH, fetch_latch_not_q, nready);
  nand nand_3 (_1_PC, ipc_latch1_q, or_4_out);
  not not_8 (T0, nT0);
  nand nand_4 (_0_IR, B_OUT, FETCH);

  // Notes on the sheet:
  //   /STORE
  //   ACRL1
  //   STOR
  //   ACRL_FF
  //   REST
  //   ENDX
  //   ReadyDelay
  //   RDY
  //   T6_FF
  //   T0_FF
  //   RDY_FF
  //   STEP_FF
endmodule

// BUS CONTROL
module BUS_CONTROL (
  input  PHI1,
  input  PHI2,
  input  nSBXY,
  input  D58,
  input  D59,
  input  D60,
  input  D61,
  input  D62,
  input  D63,
  input  D64,
  input  D65,
  input  D66,
  input  D67,
  input  D68,
  input  AND,
  input  D55,
  input  D74,
  input  D79,
  input  STOR,
  input  D57,
  input  T0,
  input  T1,
  input  T6,
  input  T7,
  input  D81,
  input  D82,
  input  D71,
  input  D72,
  input  BR0,
  input  BR2,
  input  BR3,
  input  ACRL2,
  input  nready,
  input  T2,
  input  nPCH_PCH,
  input  D56,
  input  D89,
  input  D90,
  input  D91,
  input  D84,
  input  DL_PCH,
  input  _0_ADL0,
  input  D83,
  input  D128,
  input  INC_SB,
  input  BRK6E,
  input  D45,
  input  D46,
  input  D47,
  input  D48,
  input  STXY,
  input  D101,
  output SB_AC,
  output ZTST,
  output AC_SB,
  output SB_DB,
  output AC_DB,
  output _0_ADH17,
  output _0_ADH0,
  output DL_ADL,
  output ADL_ABL,
  output PGX,
  output SB_ADH,
  output ADH_ABH,
  output DL_ADH,
  output DL_DB
);

  wire ac_db_latch_q, ac_sb_latch_q, adh_abh_latch_not_q, adl_abl_latch_not_q, and_1_out, and_2_out,
       and_3_out, and_4_out, dl_adh_latch_not_q, dl_adl_latch_not_q, dl_db_latch_not_q, JSXY, nand_3_out,
       nand_4_out, nor_1_out, nor_2_out, nor_3_out, nor_4_out, nor_5_out, nor_6_out, nor_7_out, nor_8_out,
       nor_9_out, nor_10_out, nor_11_out, nor_12_out, nor_13_out, nor_14_out, nor_15_out, nor_16_out,
       nor_17_out, nor_18_out, nor_19_out, nor_20_out, nor_21_out, nor_22_out, nor_23_out, not_1_out,
       not_2_out, not_3_out, not_4_out, not_5_out, not_6_out, nready_latch_not_q, or_1_out, or_2_out,
       or_3_out, sb_ac_latch_q, sb_adh_latch_not_q, sb_db_latch_not_q, z_adh17_latch_not_q;

  not not_1 (not_1_out, D64);
  and and_1 (and_1_out, D79, STOR);
  nor nor_1 (nor_1_out, D81, D82);
  nor nor_2 (nor_2_out, D71, D72);
  nor nor_3 (nor_3_out, D83, T0);
  not not_2 (not_2_out, D48);
  nor nor_4 (nor_4_out, D58, D59, D60, D61, D62, D63, D64);
  and and_2 (and_2_out, not_1_out, D65);
  nor nor_5 (nor_5_out, D74, and_1_out);
  not not_3 (not_3_out, BR0);
  D_Latch nready_latch (.EN(PHI1), .D(nready), .NOT_Q(nready_latch_not_q));  // open: Q
  or or_1 (or_1_out, D89, D90, D91, D84);
  nor nor_6 (nor_6_out, nor_3_out, D128);
  or or_2 (or_2_out, INC_SB, BRK6E, D45, D46, D47, D48);
  nand nand_1 (JSXY, not_2_out, STXY);
  not not_4 (not_4_out, nor_4_out);
  nor nor_7 (nor_7_out, and_2_out, D66, D67, D68, AND);
  not not_5 (not_5_out, nor_2_out);
  nand nand_2 (PGX, nor_2_out, not_3_out);
  nor nor_8 (nor_8_out, nSBXY, not_4_out, T7, AND);
  nor nor_9 (nor_9_out, PGX, BR3);
  nand nand_3 (nand_3_out, ACRL2, nready_latch_not_q);
  nor nor_10 (nor_10_out, T2, nPCH_PCH, D56, or_1_out);
  nor nor_11 (nor_11_out, or_1_out, DL_PCH);
  nor nor_12 (nor_12_out, nor_8_out, AND);
  and and_3 (and_3_out, D55, T6);
  nor nor_13 (nor_13_out, T7, T6);
  nor nor_14 (nor_14_out, not_5_out, nready);
  nor nor_15 (nor_15_out, nor_9_out, nand_3_out);
  nor nor_16 (nor_16_out, nready, nor_10_out);
  nor nor_17 (nor_17_out, BR2, nor_6_out, or_2_out, D101, T6);
  or or_3 (or_3_out, nor_15_out, nor_16_out);
  nor nor_18 (nor_18_out, T1, nor_12_out, D67, and_3_out, BR2, JSXY);
  nand nand_4 (nand_4_out, nor_13_out, nor_14_out);
  and and_4 (and_4_out, or_3_out, ~BR3);  // AND_Gate
  nor nor_19 (nor_19_out, D57, not_6_out);
  not not_6 (not_6_out, nor_1_out);
  nor nor_20 (nor_20_out, and_4_out, _0_ADL0);
  D_Latch sb_ac_latch (.EN(PHI2), .D(nor_4_out), .Q(sb_ac_latch_q));  // open: NOT_Q
  D_Latch ac_sb_latch (.EN(PHI2), .D(nor_7_out), .Q(ac_sb_latch_q));  // open: NOT_Q
  D_Latch sb_db_latch (.EN(PHI2), .D(nor_18_out), .NOT_Q(sb_db_latch_not_q));  // open: Q
  D_Latch ac_db_latch (.EN(PHI2), .D(nor_5_out), .Q(ac_db_latch_q));  // open: NOT_Q
  D_Latch z_adh17_latch (.EN(PHI2), .D(nor_19_out), .NOT_Q(z_adh17_latch_not_q));  // open: Q
  D_Latch z_adh0_latch (.EN(PHI2), .D(nor_1_out), .NOT_Q(_0_ADH0));  // open: Q
  D_Latch dl_adl_latch (.EN(PHI2), .D(nor_1_out), .NOT_Q(dl_adl_latch_not_q));  // open: Q
  D_Latch adl_abl_latch (.EN(PHI2), .D(nand_4_out), .NOT_Q(adl_abl_latch_not_q));  // open: Q
  D_Latch sb_adh_latch (.EN(PHI2), .D(nor_9_out), .NOT_Q(sb_adh_latch_not_q));  // open: Q
  D_Latch adh_abh_latch (.EN(PHI2), .D(nor_20_out), .NOT_Q(adh_abh_latch_not_q));  // open: Q
  D_Latch dl_adh_latch (.EN(PHI2), .D(nor_11_out), .NOT_Q(dl_adh_latch_not_q));  // open: Q
  D_Latch dl_db_latch (.EN(PHI2), .D(nor_17_out), .NOT_Q(dl_db_latch_not_q));  // open: Q
  buf buffer_1 (SB_AC, nor_21_out);
  nor nor_21 (nor_21_out, sb_ac_latch_q, PHI2);
  not not_7 (ZTST, nor_8_out);
  buf buffer_2 (AC_SB, nor_22_out);
  nor nor_22 (nor_22_out, ac_sb_latch_q, PHI2);
  buf buffer_3 (SB_DB, sb_db_latch_not_q);
  buf buffer_4 (AC_DB, nor_23_out);
  nor nor_23 (nor_23_out, ac_db_latch_q, PHI2);
  buf buffer_5 (_0_ADH17, z_adh17_latch_not_q);
  buf buffer_6 (DL_ADL, dl_adl_latch_not_q);
  buf buffer_7 (ADL_ABL, adl_abl_latch_not_q);
  buf buffer_8 (SB_ADH, sb_adh_latch_not_q);
  buf buffer_9 (ADH_ABH, adh_abh_latch_not_q);
  buf buffer_10 (DL_ADH, dl_adh_latch_not_q);
  buf buffer_11 (DL_DB, dl_db_latch_not_q);

  // Notes on the sheet:
  //   STA
  //   JSR/5
  //   ABS/2
  //   JSR2
  //   IMPLIED
  //   #SB/AC
  //   IND
  //   #SBXY
  //   AND
  //   PGX
  //   JMP/4
  //   #ZTST
  //   SBA
  //   #DL/ADL
  //   #SB/AC
  //   #AC/SB
  //   #SB/DB
  //   #ADL/ABL
  //   #DL/DB
endmodule

// FLAGS CONTROL
module FLAGS_CONTROL (
  input  PHI2,
  input  D98,
  input  D99,
  input  D108,
  input  D110,
  input  D120,
  input  D127,
  input  D107,
  input  T7,
  input  D112,
  input  D116,
  input  D117,
  input  D118,
  input  D119,
  input  ZTST,
  input  D109,
  input  nready,
  input  SR,
  input  D114,
  input  D115,
  input  D113,
  output P_DB,
  output IR5_I,
  output IR5_C,
  output IR5_D,
  output _0_V,
  output ACR_C,
  output DBZ_Z,
  output DB_N,
  output DB_P,
  output DB_C,
  output DB_V
);

  wire and_1_out, and_2_out, bit_latch_q, dbn_latch_q, dbz_latch_q, nor_1_out, nor_2_out, nor_3_out,
       nor_4_out, nor_5_out, not_1_out, pin_latch_q;

  and and_1 (and_1_out, D107, T7);
  nor nor_1 (nor_1_out, D98, D99);
  nor nor_2 (nor_2_out, D114, D115);
  not not_1 (not_1_out, D113);
  nor nor_3 (nor_3_out, and_1_out, D112, D116, D117, D118, D119);
  nor nor_4 (nor_4_out, ACR_C, ZTST, D109);
  nor nor_5 (nor_5_out, DB_P, SR);
  D_Latch pdb_latch (.EN(PHI2), .D(nor_1_out), .NOT_Q(P_DB));  // open: Q
  D_Latch iri_latch (.EN(PHI2), .D(D108), .Q(IR5_I));  // open: NOT_Q
  D_Latch irc_latch (.EN(PHI2), .D(D110), .Q(IR5_C));  // open: NOT_Q
  D_Latch ird_latch (.EN(PHI2), .D(D120), .Q(IR5_D));  // open: NOT_Q
  D_Latch zv_latch (.EN(PHI2), .D(D127), .Q(_0_V));  // open: NOT_Q
  D_Latch acrc_latch (.EN(PHI2), .D(nor_3_out), .NOT_Q(ACR_C));  // open: Q
  D_Latch dbz_latch (.EN(PHI2), .D(nor_4_out), .Q(dbz_latch_q), .NOT_Q(DBZ_Z));
  D_Latch dbn_latch (.EN(PHI2), .D(D109), .Q(dbn_latch_q));  // open: NOT_Q
  D_Latch dbc_latch (.EN(PHI2), .D(nor_5_out), .NOT_Q(DB_C));  // open: Q
  D_Latch pin_latch (.EN(PHI2), .D(nor_2_out), .Q(pin_latch_q));  // open: NOT_Q
  D_Latch bit_latch (.EN(PHI2), .D(not_1_out), .Q(bit_latch_q));  // open: NOT_Q
  and and_2 (and_2_out, dbz_latch_q, pin_latch_q);
  nor nor_6 (DB_N, and_2_out, dbn_latch_q);
  nor nor_7 (DB_P, pin_latch_q, nready);
  nand nand_1 (DB_V, pin_latch_q, bit_latch_q);

  // Notes on the sheet:
  //   AVR/V
  //   BIT1
  //   BIT0
  //   /POUT
  //   /CSI
  //   /PIN
  //   /ARIT
endmodule

module FLAGS (
  input  PHI1,
  input  PHI2,
  input  B_OUT,
  input  [7:0] DB,
  input  DB_P,
  input  DBZ_Z,
  input  DB_N,
  input  IR5_C,
  input  ACR,
  input  DB_C,
  input  ACR_C,
  input  IR5_D,
  input  nIR5,
  input  IR5_I,
  input  BRK6E,
  input  AVR,
  input  DB_V,
  input  D112,
  input  _0_V,
  input  SO,
  output DB0,
  output DB1,
  output DB2,
  output DB3,
  output DB4,
  output DB5,
  output DB6,
  output DB7,
  output nZ_OUT,
  output nN_OUT,
  output nC_OUT,
  output nD_OUT,
  output nI_OUT,
  output nV_OUT
);

  wire and_1_out, and_2_out, and_3_out, and_4_out, and_5_out, and_6_out, and_7_out, and_8_out, and_9_out,
       and_10_out, and_11_out, and_12_out, and_13_out, and_14_out, and_15_out, and_16_out, and_17_out,
       and_18_out, avr_latch_q, c_latch2_q, d_latch2_q, i_latch1_not_q, i_latch2_q, n_latch2_q, nor_1_out,
       nor_2_out, nor_3_out, nor_4_out, nor_5_out, nor_6_out, not_1_out, not_2_out, not_3_out, not_4_out,
       not_5_out, not_6_out, not_7_out, not_8_out, not_9_out, not_10_out, or_1_out, or_2_out, or_3_out,
       or_4_out, or_5_out, or_6_out, or_7_out, so_latch1_not_q, so_latch2_not_q, so_latch3_q, v_latch2_q,
       vset_latch_q, z_latch2_q;

  not not_1 (not_1_out, ACR);
  not not_2 (not_2_out, SO);
  D_Latch avr_latch (.EN(PHI2), .D(D112), .Q(avr_latch_q));  // open: NOT_Q
  D_Latch so_latch1 (.EN(PHI1), .D(not_2_out), .NOT_Q(so_latch1_not_q));  // open: Q
  or or_1 (or_1_out, DB[0], DB[0], DB[1], DB[2], DB[3], DB[4], DB[5], DB[6], DB[7]);
  D_Latch so_latch2 (.EN(PHI2), .D(so_latch1_not_q), .NOT_Q(so_latch2_not_q));  // open: Q
  nor nor_1 (nor_1_out, DB_P, DBZ_Z);
  D_Latch so_latch3 (.EN(PHI1), .D(so_latch2_not_q), .Q(so_latch3_q));  // open: NOT_Q
  not not_3 (not_3_out, DB[1]);
  not not_4 (not_4_out, DB[7]);
  not not_5 (not_5_out, DB_N);
  not not_6 (not_6_out, DB[0]);
  nor nor_2 (nor_2_out, DB_C, IR5_C, ACR_C);
  not not_7 (not_7_out, DB[3]);
  nor nor_3 (nor_3_out, DB_P, IR5_D);
  not not_8 (not_8_out, DB[2]);
  nor nor_4 (nor_4_out, DB_P, IR5_I);
  not not_9 (not_9_out, AVR);
  not not_10 (not_10_out, DB[6]);
  nor nor_5 (nor_5_out, DB_V, avr_latch_q, vset_latch_q);
  nor nor_6 (nor_6_out, so_latch3_q, so_latch1_not_q);
  and and_1 (and_1_out, not_3_out, DB_P);
  and and_2 (and_2_out, DBZ_Z, or_1_out);
  and and_3 (and_3_out, nor_1_out, z_latch2_q);
  and and_4 (and_4_out, not_4_out, DB_N);
  and and_5 (and_5_out, not_5_out, n_latch2_q);
  and and_6 (and_6_out, nIR5, IR5_C);
  and and_7 (and_7_out, not_1_out, ACR_C);
  and and_8 (and_8_out, not_6_out, DB_C);
  and and_9 (and_9_out, nor_2_out, c_latch2_q);
  and and_10 (and_10_out, IR5_D, nIR5);
  and and_11 (and_11_out, not_7_out, DB_P);
  and and_12 (and_12_out, nor_3_out, d_latch2_q);
  and and_13 (and_13_out, nIR5, IR5_I);
  and and_14 (and_14_out, not_8_out, DB_P);
  and and_15 (and_15_out, nor_4_out, i_latch2_q);
  and and_16 (and_16_out, not_9_out, avr_latch_q);
  and and_17 (and_17_out, not_10_out, DB_V);
  and and_18 (and_18_out, nor_5_out, v_latch2_q);
  or or_2 (or_2_out, and_1_out, and_2_out, and_3_out);
  or or_3 (or_3_out, and_4_out, and_5_out);
  or or_4 (or_4_out, and_6_out, and_7_out, and_8_out, and_9_out);
  or or_5 (or_5_out, and_10_out, and_11_out, and_12_out);
  or or_6 (or_6_out, and_13_out, and_14_out, and_15_out);
  nor nor_7 (nI_OUT, i_latch1_not_q, BRK6E);
  or or_7 (or_7_out, and_16_out, and_17_out, and_18_out, _0_V);
  D_Latch z_latch1 (.EN(PHI1), .D(or_2_out), .Q(nZ_OUT));  // open: NOT_Q
  D_Latch z_latch2 (.EN(PHI2), .D(nZ_OUT), .Q(z_latch2_q));  // open: NOT_Q
  D_Latch n_latch1 (.EN(PHI1), .D(or_3_out), .Q(nN_OUT));  // open: NOT_Q
  D_Latch n_latch2 (.EN(PHI2), .D(nN_OUT), .Q(n_latch2_q));  // open: NOT_Q
  D_Latch c_latch1 (.EN(PHI1), .D(or_4_out), .Q(nC_OUT));  // open: NOT_Q
  D_Latch c_latch2 (.EN(PHI2), .D(nC_OUT), .Q(c_latch2_q));  // open: NOT_Q
  D_Latch d_latch1 (.EN(PHI1), .D(or_5_out), .Q(nD_OUT));  // open: NOT_Q
  D_Latch d_latch2 (.EN(PHI2), .D(nD_OUT), .Q(d_latch2_q));  // open: NOT_Q
  D_Latch i_latch1 (.EN(PHI1), .D(or_6_out), .NOT_Q(i_latch1_not_q));  // open: Q
  D_Latch i_latch2 (.EN(PHI2), .D(nI_OUT), .Q(i_latch2_q));  // open: NOT_Q
  D_Latch v_latch1 (.EN(PHI1), .D(or_7_out), .Q(nV_OUT));  // open: NOT_Q
  D_Latch v_latch2 (.EN(PHI2), .D(nV_OUT), .Q(v_latch2_q));  // open: NOT_Q
  D_Latch vset_latch (.EN(PHI2), .D(nor_6_out), .Q(vset_latch_q));  // open: NOT_Q
  not not_11 (DB0, nC_OUT);
  not not_12 (DB1, nZ_OUT);
  not not_13 (DB2, nI_OUT);
  not not_14 (DB3, nD_OUT);
  not not_15 (DB6, nV_OUT);
  not not_16 (DB7, nN_OUT);

  assign DB4 = B_OUT;
  assign DB5 = 1'b1;

  // Other names for the same wires on the sheet: DB0_t = DB[0]; DB1_t = DB[1]; DB2_t = DB[2]; DB3_t = DB[3];
  //   DB6_t = DB[6]; DB7_t = DB[7]

  // Notes on the sheet:
  //   AVR/V
  //   ACR/C
  //   /DBZ
  //   IR5/C
  //   DB/C
  //   IR5/D
  //   1/V
  //   /DB1
  //   /ACR
  //   /DB0
  //   DB/C
  //   IR5/D
  //   /DB3
  //   IR5/I
  //   /DB2
  //   /AVR
  //   /DB6
  //   DB/V
  //   0/V
  //   Z FLAG
  //   N FLAG
  //   C FLAG
  //   D FLAG
  //   I FLAG
  //   V FLAG
  //   /Z_OUT
  //   /N_OUT
  //   /C_OUT
  //   /D_OUT
  //   /V_OUT
  //   /I_OUT
endmodule

module ALU (
  input  PHI2,
  input  PHI1,
  input  nDAA,
  input  nDSA,
  input  nACIN,
  input  NDB_ADD,
  input  DB_ADD,
  input  _0_ADD,
  input  SB_ADD,
  input  ADL_ADD,
  input  ANDS,
  input  EORS,
  input  ORS,
  input  SRS,
  input  SUMS,
  input  [7:0] DB_IN,
  input  [7:0] ADL_IN,
  input  [7:0] SB_IN,
  input  SB_AC,
  output [7:0] ACC,
  output [7:0] ADD,
  output ACR,
  output AVR
);

  wire ACLatch_q, alu_ops_1_carry3, alu_ops_1_carry4, alu_ops_1_carry6, alu_ops_1_carry7, bcd_carry_1_dc3,
       bcd_carry_1_dc7, DCLatch_q, multiplexer_1_out, not_1_out;
  wire [7:0] alu_bcd_1_out0, alu_ops_1_and, alu_ops_1_or, alu_ops_1_result, alu_ops_1_xor;

  ALU_OPS alu_ops_1 (
    .NDB_ADD(NDB_ADD), .DB_ADD(DB_ADD), ._0_ADD(_0_ADD), .SB_ADD(SB_ADD), .ADL_ADD(ADL_ADD), .ANDS(ANDS),
    .EORS(EORS), .ORS(ORS), .SRS(SRS), .SUMS(SUMS), .nACIN(nACIN), .RESULT(alu_ops_1_result),
    .carry7(alu_ops_1_carry7), .SB(SB_IN), .DB(DB_IN), .ADL(ADL_IN), .OR(alu_ops_1_or), .AND(alu_ops_1_and),
    .XOR(alu_ops_1_xor), .DC3(bcd_carry_1_dc3), .carry6(alu_ops_1_carry6), .carry3(alu_ops_1_carry3),
    .carry4(alu_ops_1_carry4), .PHI1(PHI1));
  BCD_CARRY bcd_carry_1 (
    .nACIN(nACIN), .carry4(alu_ops_1_carry4), .\or (alu_ops_1_or), .\and (alu_ops_1_and),
    .\xor (alu_ops_1_xor), .DC3(bcd_carry_1_dc3), .DC7(bcd_carry_1_dc7), .nDAA(nDAA));
  not not_1 (not_1_out, alu_ops_1_and[7]);
  Multiplexer #(.disabled(0), .enable("false")) multiplexer_1 (
    .in0(not_1_out), .in1(alu_ops_1_or[7]), .out(multiplexer_1_out), .sel(alu_ops_1_carry6));
  D_Latch DCLatch (.EN(PHI2), .D(bcd_carry_1_dc7), .Q(DCLatch_q));  // open: NOT_Q
  Register #(.trigger("high")) register_1 (.D(alu_ops_1_result), .Q(ADD), .clk(PHI2));  // open: en, clr
  D_Latch ACLatch (.EN(PHI2), .D(alu_ops_1_carry7), .Q(ACLatch_q));  // open: NOT_Q
  D_Latch AVRLatch (.EN(PHI2), .D(multiplexer_1_out), .NOT_Q(AVR));  // open: Q
  or or_1 (ACR, DCLatch_q, ACLatch_q);
  ALU_BCD alu_bcd_1 (
    .PHI2(PHI2), .ACR(ACR), .nDAA(nDAA), .nDSA(nDSA), .SB(SB_IN), .ADDx(ADD), .out0(alu_bcd_1_out0[0]),
    .out1(alu_bcd_1_out0[1]), .out2(alu_bcd_1_out0[2]), .out3(alu_bcd_1_out0[3]), .out4(alu_bcd_1_out0[4]),
    .out5(alu_bcd_1_out0[5]), .out6(alu_bcd_1_out0[6]), .out7(alu_bcd_1_out0[7]), .carry3(alu_ops_1_carry3));
  Register #(.trigger("high")) register_2 (.D(alu_bcd_1_out0), .Q(ACC), .clk(SB_AC));  // open: en, clr

  // Notes on the sheet:
  //   ADDER HOLD
  //   AVR
  //   ACC
endmodule

module PC (
  input  PHI2,
  input  PHI1,
  input  PCL_PCL,
  input  [7:0] ADL_IN,
  input  ADL_PCL,
  input  _1_PC,
  input  PCH_PCH,
  input  [7:0] ADH_IN,
  input  ADH_PCH,
  output [7:0] PCL,
  output [7:0] PCH
);

  wire or_1_out, or_2_out;
  wire [7:0] and_1_out, and_2_out, and_3_out, and_4_out, and_7_out, bit_extender_1_out, bit_extender_2_out,
       bit_extender_3_out, bit_extender_4_out, not_1_out, or_3_out, or_4_out, register_1_q, register_2_q,
       xor_1_out, xor_2_out;
  wire [7:3] and_6_out;
  wire [7:7] and_5_out;

  assign bit_extender_1_out = {{7{PCL_PCL}}, PCL_PCL};  // Bit_Extender bit_extender_1
  assign bit_extender_2_out = {{7{ADL_PCL}}, ADL_PCL};  // Bit_Extender bit_extender_2
  not not_1 (not_1_out[0], _1_PC);
  assign bit_extender_3_out = {{7{PCH_PCH}}, PCH_PCH};  // Bit_Extender bit_extender_3
  assign bit_extender_4_out = {{7{ADH_PCH}}, ADH_PCH};  // Bit_Extender bit_extender_4
  assign and_1_out = PCL & bit_extender_1_out;  // AND_Gate and_1, 8 bits wide
  assign and_2_out = ADL_IN & bit_extender_2_out;  // AND_Gate and_2, 8 bits wide
  or or_1 (or_1_out, ADL_PCL, PCL_PCL);
  assign and_3_out = PCH & bit_extender_3_out;  // AND_Gate and_3, 8 bits wide
  assign and_4_out = ADH_IN & bit_extender_4_out;  // AND_Gate and_4, 8 bits wide
  or or_2 (or_2_out, ADH_PCH, PCH_PCH);
  assign or_3_out = and_1_out | and_2_out;  // OR_Gate or_3, 8 bits wide
  assign or_4_out = and_3_out | and_4_out;  // OR_Gate or_4, 8 bits wide
  Register #(.trigger("high")) register_1 (.D(or_3_out), .en(or_1_out), .Q(register_1_q), .clk(PHI1));  // open: clr
  Register #(.trigger("high")) register_2 (.D(or_4_out), .en(or_2_out), .Q(register_2_q), .clk(PHI1));  // open: clr
  assign xor_1_out = register_1_q ^ not_1_out;  // XOR_Gate xor_1, 8 bits wide
  assign {and_5_out[7], not_1_out[7:1]} = not_1_out & register_1_q;  // AND_Gate and_5, 8 bits wide
  assign xor_2_out = register_2_q ^ and_7_out;  // XOR_Gate xor_2, 8 bits wide
  assign {and_6_out[7], and_7_out[7:5], and_6_out[3], and_7_out[3:1]} = and_7_out & register_2_q;  // AND_Gate and_6, 8 bits wide
  Register #(.trigger("high")) register_3 (.D(xor_1_out), .Q(PCL), .clk(PHI2));  // open: en, clr
  Register #(.trigger("high")) register_4 (.D(xor_2_out), .Q(PCH), .clk(PHI2));  // open: en, clr
  and and_7 (and_7_out[0], not_1_out[0], register_1_q[0], register_1_q[1], register_1_q[2], register_1_q[3], register_1_q[4], register_1_q[5], register_1_q[6], register_1_q[7]);
  and and_8 (and_7_out[4], and_7_out[0], register_2_q[0], register_2_q[1], register_2_q[2], register_2_q[3]);
endmodule

// ALU OPS
module ALU_OPS (
  input  PHI1,
  input  SUMS,
  input  SRS,
  input  ORS,
  input  EORS,
  input  ANDS,
  input  nACIN,
  input  _0_ADD,
  input  [7:0] SB,
  input  SB_ADD,
  input  [7:0] DB,
  input  [7:0] ADL,
  input  DB_ADD,
  input  NDB_ADD,
  input  ADL_ADD,
  input  DC3,
  output [7:0] RESULT,
  output [7:0] AND,
  output [7:0] XOR,
  output [7:0] OR,
  output carry3,
  output carry4,
  output carry6,
  output carry7
);

  wire or_1_out;
  wire [0:0] not_1_out;
  wire [5:0] or_4_out;
  wire [7:0] and_1_out, and_2_out, and_3_out, and_5_out, and_8_out, and_9_out, and_10_out, and_11_out,
       and_12_out, bit_extender_1_out, bit_extender_2_out, bit_extender_3_out, bit_extender_4_out,
       bit_extender_5_out, bit_extender_6_out, bit_extender_7_out, bit_extender_8_out, not_2_out, or_2_out,
       register_1_q, register_2_q, xor_1_out;

  assign bit_extender_1_out = {{7{SUMS}}, SUMS};  // Bit_Extender bit_extender_1
  assign bit_extender_2_out = {{7{SRS}}, SRS};  // Bit_Extender bit_extender_2
  assign bit_extender_3_out = {{7{ORS}}, ORS};  // Bit_Extender bit_extender_3
  assign bit_extender_4_out = {{7{EORS}}, EORS};  // Bit_Extender bit_extender_4
  assign bit_extender_5_out = {{7{ANDS}}, ANDS};  // Bit_Extender bit_extender_5
  not not_1 (not_1_out[0], nACIN);
  assign bit_extender_6_out = {{7{DB_ADD}}, DB_ADD};  // Bit_Extender bit_extender_6
  assign bit_extender_7_out = {{7{NDB_ADD}}, NDB_ADD};  // Bit_Extender bit_extender_7
  assign bit_extender_8_out = {{7{ADL_ADD}}, ADL_ADD};  // Bit_Extender bit_extender_8
  or or_1 (or_1_out, ADL_ADD, NDB_ADD, DB_ADD);
  assign and_1_out = DB & bit_extender_6_out;  // AND_Gate and_1, 8 bits wide
  assign or_2_out = and_1_out | and_2_out | and_3_out;  // OR_Gate or_2, 8 bits wide
  assign and_2_out = ~DB & bit_extender_7_out;  // AND_Gate and_2, 8 bits wide
  assign and_3_out = ADL & bit_extender_8_out;  // AND_Gate and_3, 8 bits wide
  Register #(.trigger("high")) register_1 (.D(SB), .en(SB_ADD), .Q(register_1_q), .clk(PHI1), .clr(_0_ADD));
  Register #(.trigger("high")) register_2 (.D(or_2_out), .en(or_1_out), .Q(register_2_q), .clk(PHI1));  // open: clr
  assign AND = register_1_q & register_2_q;  // AND_Gate and_4, 8 bits wide
  assign OR = register_1_q | register_2_q;  // OR_Gate or_3, 8 bits wide
  assign not_2_out = ~AND;  // NOT_Gate not_2, 8 bits wide
  assign and_5_out = XOR & {carry6, or_4_out[5], carry4, carry3, or_4_out[2:0], not_1_out[0]};  // AND_Gate and_5, 8 bits wide
  assign XOR = not_2_out & OR;  // AND_Gate and_6, 8 bits wide
  assign {carry7, carry6, or_4_out[5], carry4, or_4_out[3:0]} = AND | and_5_out;  // OR_Gate or_4, 8 bits wide
  assign xor_1_out = {carry6, or_4_out[5], carry4, carry3, or_4_out[2:0], not_1_out[0]} ^ XOR;  // XOR_Gate xor_1, 8 bits wide
  and and_7 (carry3, or_4_out[3], ~DC3);  // AND_Gate
  assign and_8_out = bit_extender_1_out & xor_1_out;  // AND_Gate and_8, 8 bits wide
  assign and_9_out = bit_extender_2_out & {1'b0, AND[7:1]};  // AND_Gate and_9, 8 bits wide
  assign and_10_out = bit_extender_3_out & OR;  // AND_Gate and_10, 8 bits wide
  assign and_11_out = bit_extender_4_out & XOR;  // AND_Gate and_11, 8 bits wide
  assign and_12_out = bit_extender_5_out & AND;  // AND_Gate and_12, 8 bits wide
  assign RESULT = and_8_out | and_9_out | and_10_out | and_11_out | and_12_out;  // OR_Gate or_5, 8 bits wide

  // Notes on the sheet:
  //   ADL: pull=down
  //   DB: pull=down
  //   SB: pull=down
endmodule

module ALU_EVEN_BIT (
  input  PHI1,
  input  ORS,
  input  ANDS,
  input  SB_ADD,
  input  SBx,
  input  _0_ADD,
  input  DB_ADD,
  input  DBx,
  input  NDB_ADD,
  input  ADL_ADD,
  input  ADLx,
  input  EORS,
  input  ncin,
  input  SUMS,
  input  SRS,
  input  prev_res,
  output nres,
  output \nand ,
  output \nor ,
  output \xor ,
  output cout
);

  wire and_1_out, and_2_out, and_3_out, d_ff_1_q, d_ff_2_q, nand_2_out, nand_3_out, not_1_out, not_2_out,
       not_3_out, or_1_out, or_2_out, xor_1_out;

  not not_1 (not_1_out, DBx);
  assign nres = SRS ? prev_res : 1'bz;  // Controlled_Buffer controlled_buffer_1
  or or_1 (or_1_out, DB_ADD, NDB_ADD, ADL_ADD);
  and and_1 (and_1_out, DB_ADD, DBx);
  and and_2 (and_2_out, NDB_ADD, not_1_out);
  or or_2 (or_2_out, and_1_out, and_2_out, and_3_out);
  and and_3 (and_3_out, ADL_ADD, ADLx);
  D_Flip_Flop #(.trigger("high")) d_ff_1 (.clk(SB_ADD), .D(SBx), .Q(d_ff_1_q), .reset(_0_ADD));  // open: Qn, preset, en
  D_Flip_Flop #(.trigger("high")) d_ff_2 (.clk(or_1_out), .D(or_2_out), .Q(d_ff_2_q));  // open: Qn, preset, en, reset
  not not_2 (not_2_out, \nor );
  nand nand_1 (\nand , d_ff_1_q, d_ff_2_q);
  nor nor_1 (\nor , d_ff_1_q, d_ff_2_q);
  not not_3 (not_3_out, ncin);
  nand nand_2 (nand_2_out, not_2_out, \nand );
  nand nand_3 (nand_3_out, ncin, \nand );
  assign nres = ANDS ? \nand  : 1'bz;  // Controlled_Buffer controlled_buffer_2
  assign nres = ORS ? \nor  : 1'bz;  // Controlled_Buffer controlled_buffer_3
  assign nres = EORS ? nand_2_out : 1'bz;  // Controlled_Buffer controlled_buffer_4
  not not_4 (\xor , nand_2_out);
  assign nres = SUMS ? xor_1_out : 1'bz;  // Controlled_Buffer controlled_buffer_5
  xor xor_1 (xor_1_out, nand_2_out, not_3_out);
  and and_4 (cout, nand_3_out, not_2_out);

  // Notes on the sheet:
  //   AI
  //   BI
  //   xnor
endmodule

module ALU_ODD_BIT (
  input  PHI1,
  input  ORS,
  input  ANDS,
  input  SB_ADD,
  input  SBx,
  input  _0_ADD,
  input  DB_ADD,
  input  DBx,
  input  NDB_ADD,
  input  ADL_ADD,
  input  ADLx,
  input  EORS,
  input  cin,
  input  SUMS,
  input  SRS,
  input  prev_res,
  output nres,
  output \nand ,
  output \nor ,
  output \xor ,
  output ncout
);

  wire and_1_out, and_2_out, and_3_out, d_ff_1_q, d_ff_2_q, nand_2_out, not_1_out, not_2_out, not_3_out,
       not_4_out, not_5_out, or_1_out, or_2_out, xor_1_out;

  not not_1 (not_1_out, DBx);
  assign nres = SRS ? prev_res : 1'bz;  // Controlled_Buffer controlled_buffer_1
  or or_1 (or_1_out, DB_ADD, NDB_ADD, ADL_ADD);
  and and_1 (and_1_out, DB_ADD, DBx);
  or or_2 (or_2_out, and_1_out, and_2_out, and_3_out);
  and and_2 (and_2_out, NDB_ADD, not_1_out);
  and and_3 (and_3_out, ADL_ADD, ADLx);
  D_Flip_Flop #(.trigger("high")) d_ff_1 (.clk(SB_ADD), .D(SBx), .Q(d_ff_1_q), .reset(_0_ADD));  // open: Qn, preset, en
  D_Flip_Flop #(.trigger("high")) d_ff_2 (.clk(or_1_out), .D(or_2_out), .Q(d_ff_2_q));  // open: Qn, preset, en, reset
  nand nand_1 (\nand , d_ff_1_q, d_ff_2_q);
  nor nor_1 (\nor , d_ff_1_q, d_ff_2_q);
  not not_2 (not_2_out, \nand );
  not not_3 (not_3_out, cin);
  not not_4 (not_4_out, \nor );
  nor nor_2 (\xor , \nor , not_2_out);
  nand nand_2 (nand_2_out, cin, not_4_out);
  assign nres = ANDS ? \nand  : 1'bz;  // Controlled_Buffer controlled_buffer_2
  assign nres = ORS ? \nor  : 1'bz;  // Controlled_Buffer controlled_buffer_3
  not not_5 (not_5_out, \xor );
  assign nres = EORS ? not_5_out : 1'bz;  // Controlled_Buffer controlled_buffer_4
  assign nres = SUMS ? xor_1_out : 1'bz;  // Controlled_Buffer controlled_buffer_5
  xor xor_1 (xor_1_out, \xor , not_3_out);
  and and_4 (ncout, nand_2_out, \nand );

  // Notes on the sheet:
  //   AI
  //   BI
  //   xnor
endmodule

// BCD CARRY
module BCD_CARRY (
  input  nDAA,
  input  nACIN,
  input  [7:0] \or ,
  input  [7:0] \and ,
  input  [7:0] \xor ,
  input  carry4,
  output DC3,
  output DC7
);

  wire _1_out, _2_out, _3_2_out, _3_out, _4_out, _5_2_out, _5_out, _6_2_out, _6_out, _7_2_out, _7_out,
       _11_out, _12_out, _61_out, _62_out, not_1_out, not_2_out, not_3_out, not_4_out;

  not not_1 (not_1_out, \and [0]);
  not not_2 (not_2_out, \or [0]);
  not not_3 (not_3_out, \or [2]);
  nand _2 (_2_out, \and [5], carry4);
  and _7 (_7_out, nACIN, not_1_out);
  nor _7_2 (_7_2_out, _7_out, not_2_out);
  nor _3 (_3_out, \and [2], \xor [3]);
  nor _4 (_4_out, \and [2], not_3_out);
  nor _5 (_5_out, \and [6], \xor [7]);
  nand _6 (_6_out, _7_2_out, \and [1]);
  not not_4 (not_4_out, \xor [6]);
  or _11 (_11_out, _6_out, not_3_out);
  or _12 (_12_out, _3_out, _5_2_out);
  nor _5_2 (_5_2_out, _7_2_out, _4_out, \and [1], \xor [1]);
  or _61 (_61_out, _2_out, not_4_out);
  or _62 (_62_out, _5_out, _3_2_out);
  nor _3_2 (_3_2_out, \xor [5], \xor [6], \and [5], carry4);
  and _1 (_1_out, _11_out, _12_out);
  and _6_2 (_6_2_out, _61_out, _62_out);
  nor _1_2 (DC3, nDAA, _1_out);
  nor _6_3 (DC7, nDAA, _6_2_out);

  // Notes on the sheet:
  //   a
  //   c
  //   b
  //   d
  //   e
  //   f
  //   g
endmodule

// BCD
module ALU_BCD (
  input  PHI2,
  input  nDAA,
  input  carry3,
  input  nDSA,
  input  ACR,
  input  [7:0] ADDx,
  input  [7:0] SB,
  output out0,
  output out1,
  output out2,
  output out3,
  output out4,
  output out5,
  output out6,
  output out7
);

  wire and_1_out, and_2_out, and_3_out, and_4_out, and_5_out, and_6_out, and_7_out, and_8_out, and_9_out,
       DAAH, daah_latch_q, DAAL, DSAH, dsah_latch_q, DSAL, nand_1_out, nand_2_out, nor_1_out, not_1_out,
       or_1_out, or_2_out, or_3_out, or_4_out, or_5_out, or_6_out, or_7_out, or_8_out;

  not not_1 (not_1_out, nDAA);
  and and_1 (and_1_out, not_1_out, carry3);
  nor nor_1 (nor_1_out, carry3, nDSA);
  nand nand_1 (nand_1_out, ADDx[1], ADDx[2]);
  or or_1 (or_1_out, ADDx[1], ADDx[2]);
  nand nand_2 (nand_2_out, ADDx[5], ADDx[6]);
  or or_2 (or_2_out, ADDx[5], ADDx[6]);
  D_Latch daal_latch (.EN(PHI2), .D(and_1_out), .Q(DAAL));  // open: NOT_Q
  D_Latch daah_latch (.EN(PHI2), .D(not_1_out), .Q(daah_latch_q));  // open: NOT_Q
  D_Latch dsal_latch (.EN(PHI2), .D(nor_1_out), .Q(DSAL));  // open: NOT_Q
  D_Latch dsah_latch (.EN(PHI2), .D(nDSA), .Q(dsah_latch_q));  // open: NOT_Q
  or or_3 (or_3_out, DSAL, DAAL);
  and and_2 (and_2_out, DAAL, ~ADDx[1]);  // AND_Gate
  and and_3 (and_3_out, ADDx[1], DSAL);
  and and_4 (and_4_out, nand_1_out, DSAL);
  and and_5 (and_5_out, DAAL, or_1_out);
  or or_4 (or_4_out, DSAH, DAAH);
  and and_6 (and_6_out, DAAH, ~ADDx[5]);  // AND_Gate
  and and_7 (and_7_out, ADDx[5], DSAH);
  and and_8 (and_8_out, nand_2_out, DSAH);
  and and_9 (and_9_out, DAAH, or_2_out);
  and and_10 (DAAH, daah_latch_q, ACR);
  or or_5 (or_5_out, and_2_out, and_3_out);
  or or_6 (or_6_out, and_4_out, and_5_out);
  or or_7 (or_7_out, and_6_out, and_7_out);
  or or_8 (or_8_out, and_8_out, and_9_out);
  nor nor_2 (DSAH, dsah_latch_q, ACR);
  xor xor_1 (out1, or_3_out, SB[1]);
  xor xor_2 (out2, or_5_out, SB[2]);
  xor xor_3 (out3, or_6_out, SB[3]);
  xor xor_4 (out5, or_4_out, SB[5]);
  xor xor_5 (out6, or_7_out, SB[6]);
  xor xor_6 (out7, or_8_out, SB[7]);

  assign out0 = SB[0];
  assign out4 = SB[4];
endmodule

module D_Latch (
  input  EN,
  input  D,
  output Q,
  output NOT_Q
);

  D_Flip_Flop #(.trigger("high")) d_ff_1 (.clk(EN), .D(D), .Q(Q), .Qn(NOT_Q));  // open: preset, en, reset
endmodule

module BUS_MUX (
  input  SB_ADH,
  input  SB_DB,
  input  PCL_DB,
  input  [7:0] PCL_DATA,
  input  PCH_DB,
  input  [7:0] PCH_DATA,
  input  AC_DB,
  input  [7:0] ACC_DATA,
  input  DL_DB,
  input  [7:0] DL,
  input  P_DB,
  input  [7:0] FLAG_DATA,
  input  X_SB,
  input  [7:0] X_REG,
  input  Y_SB,
  input  [7:0] Y_REG,
  input  S_SB,
  input  [7:0] S_REG,
  input  AC_SB,
  input  ADD_SB06,
  input  ADD_SB7,
  input  [7:0] ADD_DATA,
  input  S_ADL,
  input  PCL_ADL,
  input  DL_ADL,
  input  ADD_ADL,
  input  _0_ADL0,
  input  _0_ADL1,
  input  _0_ADL2,
  input  DL_ADH,
  input  PCH_ADH,
  input  _0_ADH0,
  input  _0_ADH17,
  output [7:0] DB,
  output [7:0] DB_2,
  output [7:0] DB_3,
  output [7:0] SB,
  output [7:0] ADH,
  output [7:0] ADH_2,
  output [7:0] ADL,
  output [7:0] ADL_2
);

  wire not_1_out, not_2_out, not_3_out, not_4_out, not_5_out, not_6_out, not_7_out, not_8_out, not_9_out,
       not_10_out, not_11_out, not_12_out, not_13_out, not_14_out, not_15_out, not_19_out, not_20_out,
       not_22_out;
  wire [0:0] not_21_out;
  wire [2:0] not_16_out;
  wire [6:0] bit_extender_10_out, bit_extender_17_out, or_10_out;
  wire [7:0] ADH_t, and_5_out, and_6_out, bit_extender_1_out, bit_extender_2_out, bit_extender_3_out,
       bit_extender_4_out, bit_extender_5_out, bit_extender_6_out, bit_extender_7_out, bit_extender_8_out,
       bit_extender_9_out, bit_extender_11_out, bit_extender_12_out, bit_extender_13_out,
       bit_extender_14_out, bit_extender_15_out, bit_extender_16_out, DB_t, multiplexer_2_out, or_1_out,
       or_2_out, or_3_out, or_4_out, or_5_out, or_6_out, or_7_out, or_8_out, or_9_out, or_12_out, or_13_out,
       or_14_out, or_15_out, or_16_out, or_17_out, SB_t;
  wire [7:7] or_11_out;

  not not_1 (not_1_out, PCL_DB);
  not not_2 (not_2_out, PCH_DB);
  not not_3 (not_3_out, AC_DB);
  not not_4 (not_4_out, DL_DB);
  not not_5 (not_5_out, P_DB);
  not not_6 (not_6_out, X_SB);
  not not_7 (not_7_out, Y_SB);
  not not_8 (not_8_out, S_SB);
  not not_9 (not_9_out, AC_SB);
  not not_10 (not_10_out, ADD_SB06);
  not not_11 (not_11_out, ADD_SB7);
  not not_12 (not_12_out, S_ADL);
  not not_13 (not_13_out, PCL_ADL);
  not not_14 (not_14_out, DL_ADL);
  not not_15 (not_15_out, ADD_ADL);
  not not_16 (not_16_out[0], _0_ADL0);
  not not_17 (not_16_out[1], _0_ADL1);
  not not_18 (not_16_out[2], _0_ADL2);
  not not_19 (not_19_out, DL_ADH);
  not not_20 (not_20_out, PCH_ADH);
  not not_21 (not_21_out[0], _0_ADH0);
  not not_22 (not_22_out, _0_ADH17);
  assign bit_extender_1_out = {{7{not_1_out}}, not_1_out};  // Bit_Extender bit_extender_1
  assign bit_extender_2_out = {{7{not_2_out}}, not_2_out};  // Bit_Extender bit_extender_2
  assign bit_extender_3_out = {{7{not_3_out}}, not_3_out};  // Bit_Extender bit_extender_3
  assign bit_extender_4_out = {{7{not_4_out}}, not_4_out};  // Bit_Extender bit_extender_4
  assign bit_extender_5_out = {{7{not_5_out}}, not_5_out};  // Bit_Extender bit_extender_5
  assign bit_extender_6_out = {{7{not_6_out}}, not_6_out};  // Bit_Extender bit_extender_6
  assign bit_extender_7_out = {{7{not_7_out}}, not_7_out};  // Bit_Extender bit_extender_7
  assign bit_extender_8_out = {{7{not_8_out}}, not_8_out};  // Bit_Extender bit_extender_8
  assign bit_extender_9_out = {{7{not_9_out}}, not_9_out};  // Bit_Extender bit_extender_9
  assign bit_extender_10_out = {{6{not_10_out}}, not_10_out};  // Bit_Extender bit_extender_10
  assign bit_extender_11_out = {{7{not_12_out}}, not_12_out};  // Bit_Extender bit_extender_11
  assign bit_extender_12_out = {{7{not_13_out}}, not_13_out};  // Bit_Extender bit_extender_12
  assign bit_extender_13_out = {{7{not_14_out}}, not_14_out};  // Bit_Extender bit_extender_13
  assign bit_extender_14_out = {{7{not_15_out}}, not_15_out};  // Bit_Extender bit_extender_14
  assign bit_extender_15_out = {{7{not_19_out}}, not_19_out};  // Bit_Extender bit_extender_15
  assign bit_extender_16_out = {{7{not_20_out}}, not_20_out};  // Bit_Extender bit_extender_16
  assign bit_extender_17_out = {{6{not_22_out}}, not_22_out};  // Bit_Extender bit_extender_17
  assign or_1_out = bit_extender_1_out | PCL_DATA;  // OR_Gate or_1, 8 bits wide
  assign or_2_out = bit_extender_2_out | PCH_DATA;  // OR_Gate or_2, 8 bits wide
  assign or_3_out = bit_extender_3_out | ACC_DATA;  // OR_Gate or_3, 8 bits wide
  assign or_4_out = bit_extender_4_out | DL;  // OR_Gate or_4, 8 bits wide
  assign or_5_out = bit_extender_5_out | FLAG_DATA;  // OR_Gate or_5, 8 bits wide
  assign or_6_out = bit_extender_6_out | X_REG;  // OR_Gate or_6, 8 bits wide
  assign or_7_out = bit_extender_7_out | Y_REG;  // OR_Gate or_7, 8 bits wide
  assign or_8_out = bit_extender_8_out | S_REG;  // OR_Gate or_8, 8 bits wide
  assign or_9_out = bit_extender_9_out | ACC_DATA;  // OR_Gate or_9, 8 bits wide
  assign or_10_out = bit_extender_10_out | ADD_DATA[6:0];  // OR_Gate or_10, 7 bits wide
  or or_11 (or_11_out[7], not_11_out, ADD_DATA[7]);
  assign or_12_out = bit_extender_11_out | S_REG;  // OR_Gate or_12, 8 bits wide
  assign or_13_out = bit_extender_12_out | PCL_DATA;  // OR_Gate or_13, 8 bits wide
  assign or_14_out = bit_extender_13_out | DL;  // OR_Gate or_14, 8 bits wide
  assign or_15_out = bit_extender_14_out | ADD_DATA;  // OR_Gate or_15, 8 bits wide
  assign or_16_out = bit_extender_15_out | DL;  // OR_Gate or_16, 8 bits wide
  assign or_17_out = bit_extender_16_out | PCH_DATA;  // OR_Gate or_17, 8 bits wide
  assign DB_t = or_1_out & or_2_out & or_3_out & or_4_out & or_5_out;  // AND_Gate and_1, 8 bits wide
  assign SB_t = or_6_out & or_7_out & or_8_out & or_9_out & {or_11_out[7], or_10_out};  // AND_Gate and_2, 8 bits wide
  assign ADL = or_12_out & or_13_out & {{5{1'b1}}, not_16_out} & or_14_out & or_15_out;  // AND_Gate and_3, 8 bits wide
  assign ADH_t = or_16_out & {bit_extender_17_out, not_21_out[0]} & or_17_out;  // AND_Gate and_4, 8 bits wide
  assign and_5_out = DB_t & SB_t;  // AND_Gate and_5, 8 bits wide
  assign and_6_out = SB_t & ADH_t;  // AND_Gate and_6, 8 bits wide
  Multiplexer #(.width(8), .disabled(0), .enable("false")) multiplexer_1 (
    .in0(DB_t), .in1(and_5_out), .out(DB), .sel(SB_DB));
  Multiplexer #(.width(8), .disabled(0), .enable("false")) multiplexer_2 (
    .in0(SB_t), .in1(and_5_out), .out(multiplexer_2_out), .sel(SB_DB));
  Multiplexer #(.width(8), .disabled(0), .enable("false")) multiplexer_3 (
    .in0(multiplexer_2_out), .in1(and_6_out), .out(SB), .sel(SB_ADH));
  Multiplexer #(.width(8), .disabled(0), .enable("false")) multiplexer_4 (
    .in0(ADH_t), .in1(and_6_out), .out(ADH), .sel(SB_ADH));

  assign ADH_2 = ADH;
  assign ADL_2 = ADL;
  assign DB_2 = DB;
  assign DB_3 = DB;

  // Other names for the same wires on the sheet: ACC[7:0] = ACC_DATA; ADD[7:0] = ADD_DATA; P[7:0] = FLAG_DATA;
  //   PCH[7:0] = PCH_DATA; PCL[7:0] = PCL_DATA

  // Notes on the sheet:
  //   ADH_2: pull=down
  //   DB: pull=down
  //   ADL: pull=down
  //   DB_3: pull=down
  //   ADL_2: pull=down
  //   ADH: pull=down
  //   DB_2: pull=down
  //   SB: pull=down
endmodule

module ALU_ops_2 (
  input  PHI1,
  input  PHI1_2,
  input  nACIN,
  input  NDB_ADD,
  input  SUMS,
  input  DB_ADD,
  input  _0_ADD,
  input  SRS,
  input  SB_ADD,
  input  ADL_ADD,
  input  ORS,
  input  ANDS,
  input  EORS,
  input  EORS_2,
  input  ORS_2,
  input  SRS_2,
  input  ANDS_2,
  input  SUMS_2,
  input  nACIN_2,
  input  [7:0] SB,
  input  _0_ADD_2,
  input  [7:0] DB,
  input  [7:0] ADL,
  input  [7:0] SB_2,
  input  SB_ADD_2,
  input  [7:0] DB_2,
  input  [7:0] ADL_2,
  input  DB_ADD_2,
  input  NDB_ADD_2,
  input  ADL_ADD_2,
  input  DC3,
  input  DC3_2,
  output [7:0] nRESULT,
  output [7:0] AND,
  output [7:0] nRESULT_2,
  output [7:0] AND_2,
  output [7:0] XOR,
  output [7:0] XOR_2,
  output [7:0] OR,
  output carry3,
  output carry4,
  output carry6,
  output carry7,
  output [7:0] OR_2,
  output carry3_2,
  output carry4_2,
  output carry6_2,
  output carry7_2
);

  wire alu_even_bit_1_cout, alu_even_bit_2_cout, alu_odd_bit_1_ncout, alu_odd_bit_3_ncout, and_1_out,
       or_1_out;
  wire [4:0] not_1_out;
  wire [5:0] and_7_out;
  wire [7:0] and_2_out, and_3_out, and_4_out, and_9_out, and_10_out, and_11_out, and_12_out, and_13_out,
       bit_extender_1_out, bit_extender_2_out, bit_extender_3_out, bit_extender_4_out, bit_extender_5_out,
       bit_extender_6_out, bit_extender_7_out, bit_extender_8_out, not_2_out, or_2_out, or_4_out,
       register_1_q, register_2_q, xor_1_out;

  ALU_EVEN_BIT alu_even_bit_1 (
    .NDB_ADD(NDB_ADD), .DB_ADD(DB_ADD), ._0_ADD(_0_ADD), .SB_ADD(SB_ADD), .ADL_ADD(ADL_ADD), .ANDS(ANDS),
    .EORS(EORS), .ORS(ORS_2), .SRS(SRS_2), .SUMS(SUMS_2), .ncin(nACIN), .prev_res(AND[1]), .SBx(SB[0]),
    .DBx(DB[0]), .ADLx(ADL[0]), .nres(nRESULT[0]), .cout(alu_even_bit_1_cout), .\nor (OR_2[0]),
    .\nand (AND[0]), .\xor (XOR_2[0]), .PHI1(PHI1));
  ALU_ODD_BIT alu_odd_bit_1 (
    .NDB_ADD(NDB_ADD), .DB_ADD(DB_ADD), ._0_ADD(_0_ADD), .SB_ADD(SB_ADD), .ADL_ADD(ADL_ADD), .ANDS(ANDS),
    .EORS(EORS), .ORS(ORS_2), .SRS(SRS_2), .SUMS(SUMS_2), .cin(alu_even_bit_1_cout), .prev_res(AND[2]),
    .SBx(SB[1]), .DBx(DB[1]), .ADLx(ADL[1]), .nres(nRESULT[1]), .ncout(alu_odd_bit_1_ncout), .\nor (OR_2[1]),
    .\nand (AND[1]), .\xor (XOR_2[1]), .PHI1(PHI1));
  ALU_EVEN_BIT alu_even_bit_2 (
    .NDB_ADD(NDB_ADD), .DB_ADD(DB_ADD), ._0_ADD(_0_ADD), .SB_ADD(SB_ADD), .ADL_ADD(ADL_ADD), .ANDS(ANDS),
    .EORS(EORS), .ORS(ORS_2), .SRS(SRS_2), .SUMS(SUMS_2), .ncin(alu_odd_bit_1_ncout), .prev_res(AND[3]),
    .SBx(SB[2]), .DBx(DB[2]), .ADLx(ADL[2]), .nres(nRESULT[2]), .cout(alu_even_bit_2_cout), .\nor (OR_2[2]),
    .\nand (AND[2]), .\xor (XOR_2[2]), .PHI1(PHI1));
  ALU_ODD_BIT alu_odd_bit_2 (
    .NDB_ADD(NDB_ADD), .DB_ADD(DB_ADD), ._0_ADD(_0_ADD), .SB_ADD(SB_ADD), .ADL_ADD(ADL_ADD), .ANDS(ANDS),
    .EORS(EORS), .ORS(ORS_2), .SRS(SRS_2), .SUMS(SUMS_2), .cin(alu_even_bit_2_cout), .prev_res(AND[4]),
    .SBx(SB[3]), .DBx(DB[3]), .ADLx(ADL[3]), .nres(nRESULT[3]), .ncout(carry3_2), .\nor (OR_2[3]),
    .\nand (AND[3]), .\xor (XOR_2[3]), .PHI1(PHI1));
  and and_1 (and_1_out, carry3_2, ~DC3_2);  // AND_Gate
  ALU_EVEN_BIT alu_even_bit_3 (
    .NDB_ADD(NDB_ADD), .DB_ADD(DB_ADD), ._0_ADD(_0_ADD), .SB_ADD(SB_ADD), .ADL_ADD(ADL_ADD), .ANDS(ANDS),
    .EORS(EORS), .ORS(ORS_2), .SRS(SRS_2), .SUMS(SUMS_2), .ncin(and_1_out), .prev_res(AND[5]), .SBx(SB[4]),
    .DBx(DB[4]), .ADLx(ADL[4]), .nres(nRESULT[4]), .cout(carry4_2), .\nor (OR_2[4]), .\nand (AND[4]),
    .\xor (XOR_2[4]), .PHI1(PHI1));
  ALU_ODD_BIT alu_odd_bit_3 (
    .NDB_ADD(NDB_ADD), .DB_ADD(DB_ADD), ._0_ADD(_0_ADD), .SB_ADD(SB_ADD), .ADL_ADD(ADL_ADD), .ANDS(ANDS),
    .EORS(EORS), .ORS(ORS_2), .SRS(SRS_2), .SUMS(SUMS_2), .cin(carry4_2), .prev_res(AND[6]), .SBx(SB[5]),
    .DBx(DB[5]), .ADLx(ADL[5]), .nres(nRESULT[5]), .ncout(alu_odd_bit_3_ncout), .\nor (OR_2[5]),
    .\nand (AND[5]), .\xor (XOR_2[5]), .PHI1(PHI1));
  ALU_EVEN_BIT alu_even_bit_4 (
    .NDB_ADD(NDB_ADD), .DB_ADD(DB_ADD), ._0_ADD(_0_ADD), .SB_ADD(SB_ADD), .ADL_ADD(ADL_ADD), .ANDS(ANDS),
    .EORS(EORS), .ORS(ORS_2), .SRS(SRS_2), .SUMS(SUMS_2), .ncin(alu_odd_bit_3_ncout), .prev_res(AND[7]),
    .SBx(SB[6]), .DBx(DB[6]), .ADLx(ADL[6]), .nres(nRESULT[6]), .cout(carry6_2), .\nor (OR_2[6]),
    .\nand (AND[6]), .\xor (XOR_2[6]), .PHI1(PHI1));
  ALU_ODD_BIT alu_odd_bit_4 (
    .NDB_ADD(NDB_ADD), .DB_ADD(DB_ADD), ._0_ADD(_0_ADD), .SB_ADD(SB_ADD), .ADL_ADD(ADL_ADD), .ANDS(ANDS),
    .EORS(EORS), .ORS(ORS_2), .SRS(SRS_2), .SUMS(SUMS_2), .cin(carry6_2), .prev_res(1'b1), .SBx(SB[7]),
    .DBx(DB[7]), .ADLx(ADL[7]), .nres(nRESULT[7]), .ncout(carry7_2), .\nor (OR_2[7]), .\nand (AND[7]),
    .\xor (XOR_2[7]), .PHI1(PHI1));
  not not_1 (not_1_out[0], nACIN_2);
  assign bit_extender_1_out = {{7{DB_ADD_2}}, DB_ADD_2};  // Bit_Extender bit_extender_1
  assign bit_extender_2_out = {{7{NDB_ADD_2}}, NDB_ADD_2};  // Bit_Extender bit_extender_2
  assign bit_extender_3_out = {{7{ADL_ADD_2}}, ADL_ADD_2};  // Bit_Extender bit_extender_3
  or or_1 (or_1_out, ADL_ADD_2, NDB_ADD_2, DB_ADD_2);
  assign and_2_out = DB_2 & bit_extender_1_out;  // AND_Gate and_2, 8 bits wide
  assign and_3_out = ~DB_2 & bit_extender_2_out;  // AND_Gate and_3, 8 bits wide
  assign or_2_out = and_2_out | and_3_out | and_4_out;  // OR_Gate or_2, 8 bits wide
  assign and_4_out = ADL_2 & bit_extender_3_out;  // AND_Gate and_4, 8 bits wide
  Register #(.trigger("high")) register_1 (.D(SB_2), .en(SB_ADD_2), .Q(register_1_q), .clk(PHI1_2), .clr(_0_ADD_2));
  Register #(.trigger("high")) register_2 (.D(or_2_out), .en(or_1_out), .Q(register_2_q), .clk(PHI1_2));  // open: clr
  assign bit_extender_4_out = {{7{ANDS_2}}, ANDS_2};  // Bit_Extender bit_extender_4
  assign AND_2 = register_1_q & register_2_q;  // AND_Gate and_5, 8 bits wide
  assign OR = register_1_q | register_2_q;  // OR_Gate or_3, 8 bits wide
  assign bit_extender_5_out = {{7{EORS_2}}, EORS_2};  // Bit_Extender bit_extender_5
  assign not_2_out = ~AND_2;  // NOT_Gate not_2, 8 bits wide
  assign or_4_out = AND_2 | {carry6, and_7_out[5], carry4, not_1_out[4], and_7_out[2:0], not_1_out[0]};  // OR_Gate or_4, 8 bits wide
  assign bit_extender_6_out = {{7{SRS}}, SRS};  // Bit_Extender bit_extender_6
  assign bit_extender_7_out = {{7{ORS}}, ORS};  // Bit_Extender bit_extender_7
  assign XOR = not_2_out & OR;  // AND_Gate and_6, 8 bits wide
  assign {carry7, carry6, and_7_out[5], carry4, carry3, and_7_out[2:0]} = OR & or_4_out;  // AND_Gate and_7, 8 bits wide
  assign bit_extender_8_out = {{7{SUMS}}, SUMS};  // Bit_Extender bit_extender_8
  assign xor_1_out = {carry6, and_7_out[5], carry4, not_1_out[4], and_7_out[2:0], not_1_out[0]} ^ XOR;  // XOR_Gate xor_1, 8 bits wide
  and and_8 (not_1_out[4], carry3, ~DC3);  // AND_Gate
  assign and_9_out = bit_extender_8_out & xor_1_out;  // AND_Gate and_9, 8 bits wide
  assign and_10_out = bit_extender_6_out & {1'b0, AND_2[7:1]};  // AND_Gate and_10, 8 bits wide
  assign and_11_out = bit_extender_7_out & OR;  // AND_Gate and_11, 8 bits wide
  assign and_12_out = bit_extender_5_out & XOR;  // AND_Gate and_12, 8 bits wide
  assign and_13_out = bit_extender_4_out & AND_2;  // AND_Gate and_13, 8 bits wide
  assign nRESULT_2 = and_9_out | and_10_out | and_11_out | and_12_out | and_13_out;  // OR_Gate or_5, 8 bits wide

  // Notes on the sheet:
  //   ADL_2: pull=down
  //   DB: pull=down
  //   DB_2: pull=down
  //   SB: pull=down
  //   ADL: pull=down
  //   SB_2: pull=down
endmodule

module PC_OLD (
  input  PHI1,
  input  PHI2,
  input  [7:0] ADL_IN,
  input  ADL_PCL,
  input  PCL_PCL,
  input  _1_PC,
  input  [7:0] ADH_IN,
  input  ADH_PCH,
  input  PCH_PCH,
  output [7:0] PCL,
  output [7:0] PCH
);

  wire and_1_out, and_2_out, and_3_out, and_4_out, and_5_out, and_6_out, and_7_out, and_8_out, and_9_out,
       and_10_out, and_11_out, and_12_out, and_13_out, and_14_out, and_15_out, and_16_out, and_17_out,
       and_18_out, and_19_out, and_20_out, and_21_out, and_22_out, and_23_out, and_24_out, and_25_out,
       and_26_out, and_27_out, and_28_out, and_29_out, and_30_out, and_31_out, and_32_out, and_33_out,
       and_34_out, and_35_out, and_36_out, and_37_out, and_38_out, and_39_out, and_40_out, d_ff_1_qn,
       d_ff_2_q, d_ff_3_qn, d_ff_4_q, d_ff_5_qn, d_ff_6_q, d_ff_7_qn, d_ff_8_q, d_ff_17_q, d_ff_18_qn,
       d_ff_19_q, d_ff_20_qn, d_ff_21_q, d_ff_22_qn, d_ff_23_q, d_ff_24_qn, nand_1_out, nand_2_out,
       nand_3_out, nand_4_out, nand_5_out, nand_6_out, nand_7_out, nand_8_out, nand_9_out, nand_10_out,
       nand_11_out, nand_12_out, nand_13_out, nand_14_out, nand_15_out, nand_16_out, nor_1_out, nor_2_out,
       nor_3_out, nor_4_out, nor_5_out, nor_6_out, nor_7_out, nor_8_out, nor_9_out, nor_10_out, nor_11_out,
       nor_12_out, nor_13_out, nor_14_out, nor_15_out, nor_16_out, nor_17_out, nor_18_out, not_1_out,
       not_2_out, not_3_out, not_4_out, not_5_out, not_6_out, not_7_out, not_8_out, not_9_out, not_10_out,
       not_11_out, not_12_out, not_13_out, not_14_out, not_15_out, not_16_out, not_17_out, not_18_out,
       not_19_out, not_20_out, not_21_out, not_22_out, not_23_out, not_24_out, not_25_out, or_1_out,
       or_2_out, or_3_out, or_4_out, or_5_out, or_6_out, or_7_out, or_8_out, or_9_out, or_10_out, or_11_out,
       or_12_out, or_13_out, or_14_out, or_15_out, or_16_out, or_17_out, or_18_out, or_19_out, or_20_out,
       or_21_out, or_22_out, or_23_out, or_24_out, or_25_out, or_26_out, or_27_out, or_28_out, or_29_out,
       or_30_out, or_31_out, or_32_out, or_33_out, or_34_out, or_35_out, or_36_out, or_37_out, or_38_out,
       or_39_out, or_40_out, or_41_out, or_42_out, undriven, undriven_2, undriven_4, undriven_5, undriven_7,
       undriven_8;
  wire [7:0] and_41_out, and_42_out, and_43_out, and_44_out, and_47_out, bit_extender_1_out,
       bit_extender_2_out, bit_extender_3_out, bit_extender_4_out, d_ff_9_q, d_ff_25_qn, not_26_out,
       or_43_out, or_44_out, register_1_q, register_2_q, undriven_3, undriven_6, xor_1_out, xor_2_out;
  wire [7:4] and_46_out;
  wire [7:7] and_45_out;

  and and_1 (and_1_out, undriven_5, undriven_3[0]);
  and and_2 (and_2_out, undriven_4, d_ff_9_q[0]);
  and and_3 (and_3_out, undriven_5, undriven_3[1]);
  and and_4 (and_4_out, undriven_4, d_ff_9_q[1]);
  and and_5 (and_5_out, undriven_5, undriven_3[2]);
  and and_6 (and_6_out, undriven_4, d_ff_9_q[2]);
  and and_7 (and_7_out, undriven_5, undriven_3[3]);
  and and_8 (and_8_out, undriven_4, d_ff_9_q[3]);
  and and_9 (and_9_out, undriven_5, undriven_3[4]);
  and and_10 (and_10_out, undriven_4, d_ff_9_q[4]);
  and and_11 (and_11_out, undriven_5, undriven_3[5]);
  and and_12 (and_12_out, undriven_4, d_ff_9_q[5]);
  and and_13 (and_13_out, undriven_5, undriven_3[6]);
  and and_14 (and_14_out, undriven_4, d_ff_9_q[6]);
  and and_15 (and_15_out, undriven_5, undriven_3[7]);
  and and_16 (and_16_out, undriven_4, d_ff_9_q[7]);
  or or_1 (or_1_out, undriven_4, undriven_5);
  or or_2 (or_2_out, and_1_out, and_2_out);
  or or_3 (or_3_out, undriven_4, undriven_5);
  or or_4 (or_4_out, and_3_out, and_4_out);
  or or_5 (or_5_out, undriven_4, undriven_5);
  or or_6 (or_6_out, and_5_out, and_6_out);
  or or_7 (or_7_out, undriven_4, undriven_5);
  or or_8 (or_8_out, and_7_out, and_8_out);
  or or_9 (or_9_out, undriven_4, undriven_5);
  or or_10 (or_10_out, and_9_out, and_10_out);
  or or_11 (or_11_out, undriven_4, undriven_5);
  or or_12 (or_12_out, and_11_out, and_12_out);
  or or_13 (or_13_out, undriven_4, undriven_5);
  or or_14 (or_14_out, and_13_out, and_14_out);
  or or_15 (or_15_out, undriven_4, undriven_5);
  or or_16 (or_16_out, and_15_out, and_16_out);
  D_Flip_Flop #(.trigger("high")) d_ff_1 (.clk(or_1_out), .D(or_2_out), .Qn(d_ff_1_qn));  // open: Q, preset, en, reset
  D_Flip_Flop #(.trigger("high")) d_ff_2 (.clk(or_3_out), .D(or_4_out), .Q(d_ff_2_q));  // open: Qn, preset, en, reset
  D_Flip_Flop #(.trigger("high")) d_ff_3 (.clk(or_5_out), .D(or_6_out), .Qn(d_ff_3_qn));  // open: Q, preset, en, reset
  D_Flip_Flop #(.trigger("high")) d_ff_4 (.clk(or_7_out), .D(or_8_out), .Q(d_ff_4_q));  // open: Qn, preset, en, reset
  D_Flip_Flop #(.trigger("high")) d_ff_5 (.clk(or_9_out), .D(or_10_out), .Qn(d_ff_5_qn));  // open: Q, preset, en, reset
  D_Flip_Flop #(.trigger("high")) d_ff_6 (.clk(or_11_out), .D(or_12_out), .Q(d_ff_6_q));  // open: Qn, preset, en, reset
  D_Flip_Flop #(.trigger("high")) d_ff_7 (
    .clk(or_13_out), .D(or_14_out), .Qn(d_ff_7_qn));  // open: Q, preset, en, reset
  D_Flip_Flop #(.trigger("high")) d_ff_8 (.clk(or_15_out), .D(or_16_out), .Q(d_ff_8_q));  // open: Qn, preset, en, reset
  nand nand_1 (nand_1_out, undriven_2, d_ff_1_qn);
  nor nor_1 (nor_1_out, undriven_2, d_ff_1_qn);
  nor nor_2 (nor_2_out, nor_1_out, d_ff_2_q);
  nand nand_2 (nand_2_out, nor_1_out, d_ff_2_q);
  nand nand_3 (nand_3_out, nand_2_out, d_ff_3_qn);
  nor nor_3 (nor_3_out, nand_2_out, d_ff_3_qn);
  nor nor_4 (nor_4_out, nor_3_out, d_ff_4_q);
  nand nand_4 (nand_4_out, nor_3_out, d_ff_4_q);
  nand nand_5 (nand_5_out, nand_4_out, d_ff_5_qn);
  nor nor_5 (nor_5_out, nand_4_out, d_ff_5_qn);
  nor nor_6 (nor_6_out, nor_5_out, d_ff_6_q);
  nand nand_6 (nand_6_out, nor_5_out, d_ff_6_q);
  nand nand_7 (nand_7_out, nand_6_out, d_ff_7_qn);
  nor nor_7 (nor_7_out, nand_6_out, d_ff_7_qn);
  nor nor_8 (nor_8_out, nor_7_out, d_ff_8_q);
  nand nand_8 (nand_8_out, nor_7_out, d_ff_8_q);
  and and_17 (and_17_out, nand_1_out, not_1_out);
  not not_1 (not_1_out, nor_1_out);
  or or_17 (or_17_out, nor_2_out, not_2_out);
  not not_2 (not_2_out, nand_2_out);
  not not_3 (not_3_out, d_ff_2_q);
  and and_18 (and_18_out, nand_3_out, not_4_out);
  not not_4 (not_4_out, nor_3_out);
  or or_18 (or_18_out, nor_4_out, not_5_out);
  not not_5 (not_5_out, nand_4_out);
  not not_6 (not_6_out, d_ff_4_q);
  and and_19 (and_19_out, nand_5_out, not_7_out);
  not not_7 (not_7_out, nor_5_out);
  or or_19 (or_19_out, nor_6_out, not_8_out);
  not not_8 (not_8_out, nand_6_out);
  not not_9 (not_9_out, d_ff_6_q);
  and and_20 (and_20_out, nand_7_out, not_10_out);
  not not_10 (not_10_out, nor_7_out);
  or or_20 (or_20_out, nor_8_out, not_11_out);
  not not_11 (not_11_out, nand_8_out);
  not not_12 (not_12_out, d_ff_8_q);
  D_Flip_Flop #(.trigger("high")) d_ff_9 (
    .clk(undriven), .D(and_17_out), .Q(d_ff_9_q[0]));  // open: Qn, preset, en, reset
  D_Flip_Flop #(.trigger("high")) d_ff_10 (
    .clk(undriven), .D(or_17_out), .Qn(d_ff_9_q[1]));  // open: Q, preset, en, reset
  D_Flip_Flop #(.trigger("high")) d_ff_11 (
    .clk(undriven), .D(and_18_out), .Q(d_ff_9_q[2]));  // open: Qn, preset, en, reset
  D_Flip_Flop #(.trigger("high")) d_ff_12 (
    .clk(undriven), .D(or_18_out), .Qn(d_ff_9_q[3]));  // open: Q, preset, en, reset
  D_Flip_Flop #(.trigger("high")) d_ff_13 (
    .clk(undriven), .D(and_19_out), .Q(d_ff_9_q[4]));  // open: Qn, preset, en, reset
  D_Flip_Flop #(.trigger("high")) d_ff_14 (
    .clk(undriven), .D(or_19_out), .Qn(d_ff_9_q[5]));  // open: Q, preset, en, reset
  D_Flip_Flop #(.trigger("high")) d_ff_15 (
    .clk(undriven), .D(and_20_out), .Q(d_ff_9_q[6]));  // open: Qn, preset, en, reset
  D_Flip_Flop #(.trigger("high")) d_ff_16 (
    .clk(undriven), .D(or_20_out), .Qn(d_ff_9_q[7]));  // open: Q, preset, en, reset
  nor nor_9 (nor_9_out, undriven_2, d_ff_1_qn, not_3_out, d_ff_3_qn, not_6_out, d_ff_5_qn, not_9_out, d_ff_7_qn, not_12_out);
  or or_21 (or_21_out, undriven_7, undriven_8);
  and and_21 (and_21_out, undriven_8, undriven_6[0]);
  or or_22 (or_22_out, and_21_out, and_22_out);
  and and_22 (and_22_out, undriven_7, d_ff_25_qn[0]);
  or or_23 (or_23_out, undriven_7, undriven_8);
  and and_23 (and_23_out, undriven_8, undriven_6[1]);
  or or_24 (or_24_out, and_23_out, and_24_out);
  and and_24 (and_24_out, undriven_7, d_ff_25_qn[1]);
  or or_25 (or_25_out, undriven_7, undriven_8);
  and and_25 (and_25_out, undriven_8, undriven_6[2]);
  or or_26 (or_26_out, and_25_out, and_26_out);
  and and_26 (and_26_out, undriven_7, d_ff_25_qn[2]);
  or or_27 (or_27_out, undriven_7, undriven_8);
  and and_27 (and_27_out, undriven_8, undriven_6[3]);
  or or_28 (or_28_out, and_27_out, and_28_out);
  and and_28 (and_28_out, undriven_7, d_ff_25_qn[3]);
  or or_29 (or_29_out, undriven_7, undriven_8);
  and and_29 (and_29_out, undriven_8, undriven_6[4]);
  or or_30 (or_30_out, and_29_out, and_30_out);
  and and_30 (and_30_out, undriven_7, d_ff_25_qn[4]);
  or or_31 (or_31_out, undriven_7, undriven_8);
  and and_31 (and_31_out, undriven_8, undriven_6[5]);
  or or_32 (or_32_out, and_31_out, and_32_out);
  and and_32 (and_32_out, undriven_7, d_ff_25_qn[5]);
  or or_33 (or_33_out, undriven_7, undriven_8);
  and and_33 (and_33_out, undriven_8, undriven_6[6]);
  or or_34 (or_34_out, and_33_out, and_34_out);
  and and_34 (and_34_out, undriven_7, d_ff_25_qn[6]);
  or or_35 (or_35_out, undriven_7, undriven_8);
  and and_35 (and_35_out, undriven_8, undriven_6[7]);
  or or_36 (or_36_out, and_35_out, and_36_out);
  and and_36 (and_36_out, undriven_7, d_ff_25_qn[7]);
  D_Flip_Flop #(.trigger("high")) d_ff_17 (
    .clk(or_21_out), .D(or_22_out), .Q(d_ff_17_q));  // open: Qn, preset, en, reset
  D_Flip_Flop #(.trigger("high")) d_ff_18 (
    .clk(or_23_out), .D(or_24_out), .Qn(d_ff_18_qn));  // open: Q, preset, en, reset
  D_Flip_Flop #(.trigger("high")) d_ff_19 (
    .clk(or_25_out), .D(or_26_out), .Q(d_ff_19_q));  // open: Qn, preset, en, reset
  D_Flip_Flop #(.trigger("high")) d_ff_20 (
    .clk(or_27_out), .D(or_28_out), .Qn(d_ff_20_qn));  // open: Q, preset, en, reset
  D_Flip_Flop #(.trigger("high")) d_ff_21 (
    .clk(or_29_out), .D(or_30_out), .Q(d_ff_21_q));  // open: Qn, preset, en, reset
  D_Flip_Flop #(.trigger("high")) d_ff_22 (
    .clk(or_31_out), .D(or_32_out), .Qn(d_ff_22_qn));  // open: Q, preset, en, reset
  D_Flip_Flop #(.trigger("high")) d_ff_23 (
    .clk(or_33_out), .D(or_34_out), .Q(d_ff_23_q));  // open: Qn, preset, en, reset
  D_Flip_Flop #(.trigger("high")) d_ff_24 (
    .clk(or_35_out), .D(or_36_out), .Qn(d_ff_24_qn));  // open: Q, preset, en, reset
  nor nor_10 (nor_10_out, nor_9_out, d_ff_17_q);
  not not_13 (not_13_out, nand_9_out);
  nand nand_9 (nand_9_out, nor_9_out, d_ff_17_q);
  not not_14 (not_14_out, d_ff_17_q);
  nand nand_10 (nand_10_out, nand_9_out, d_ff_18_qn);
  not not_15 (not_15_out, nor_11_out);
  nor nor_11 (nor_11_out, nand_9_out, d_ff_18_qn);
  nor nor_12 (nor_12_out, nor_11_out, d_ff_19_q);
  not not_16 (not_16_out, nand_11_out);
  nand nand_11 (nand_11_out, nor_11_out, d_ff_19_q);
  not not_17 (not_17_out, d_ff_19_q);
  nand nand_12 (nand_12_out, nand_11_out, d_ff_20_qn);
  not not_18 (not_18_out, nor_13_out);
  nor nor_13 (nor_13_out, nand_11_out, d_ff_20_qn);
  nor nor_14 (nor_14_out, nor_18_out, d_ff_21_q);
  nand nand_13 (nand_13_out, nor_18_out, d_ff_21_q);
  not not_19 (not_19_out, nand_13_out);
  not not_20 (not_20_out, d_ff_21_q);
  nand nand_14 (nand_14_out, nand_13_out, d_ff_22_qn);
  not not_21 (not_21_out, nor_15_out);
  nor nor_15 (nor_15_out, nand_13_out, d_ff_22_qn);
  nor nor_16 (nor_16_out, nor_15_out, d_ff_23_q);
  not not_22 (not_22_out, nand_15_out);
  nand nand_15 (nand_15_out, nor_15_out, d_ff_23_q);
  not not_23 (not_23_out, d_ff_23_q);
  nand nand_16 (nand_16_out, nand_15_out, d_ff_24_qn);
  not not_24 (not_24_out, nor_17_out);
  nor nor_17 (nor_17_out, nand_15_out, d_ff_24_qn);
  or or_37 (or_37_out, nor_10_out, not_13_out);
  and and_37 (and_37_out, nand_10_out, not_15_out);
  or or_38 (or_38_out, nor_12_out, not_16_out);
  and and_38 (and_38_out, nand_12_out, not_18_out);
  or or_39 (or_39_out, nor_14_out, not_19_out);
  and and_39 (and_39_out, nand_14_out, not_21_out);
  or or_40 (or_40_out, nor_16_out, not_22_out);
  and and_40 (and_40_out, nand_16_out, not_24_out);
  not not_25 (not_25_out, nor_9_out);
  D_Flip_Flop #(.trigger("high")) d_ff_25 (
    .clk(undriven), .D(or_37_out), .Qn(d_ff_25_qn[0]));  // open: Q, preset, en, reset
  D_Flip_Flop #(.trigger("high")) d_ff_26 (
    .clk(undriven), .D(and_37_out), .Q(d_ff_25_qn[1]));  // open: Qn, preset, en, reset
  D_Flip_Flop #(.trigger("high")) d_ff_27 (
    .clk(undriven), .D(or_38_out), .Qn(d_ff_25_qn[2]));  // open: Q, preset, en, reset
  D_Flip_Flop #(.trigger("high")) d_ff_28 (
    .clk(undriven), .D(and_38_out), .Q(d_ff_25_qn[3]));  // open: Qn, preset, en, reset
  D_Flip_Flop #(.trigger("high")) d_ff_29 (
    .clk(undriven), .D(or_39_out), .Qn(d_ff_25_qn[4]));  // open: Q, preset, en, reset
  D_Flip_Flop #(.trigger("high")) d_ff_30 (
    .clk(undriven), .D(and_39_out), .Q(d_ff_25_qn[5]));  // open: Qn, preset, en, reset
  D_Flip_Flop #(.trigger("high")) d_ff_31 (
    .clk(undriven), .D(or_40_out), .Qn(d_ff_25_qn[6]));  // open: Q, preset, en, reset
  D_Flip_Flop #(.trigger("high")) d_ff_32 (
    .clk(undriven), .D(and_40_out), .Q(d_ff_25_qn[7]));  // open: Qn, preset, en, reset
  nor nor_18 (nor_18_out, not_25_out, not_14_out, d_ff_18_qn, not_17_out, d_ff_20_qn);
  assign bit_extender_1_out = {{7{PCL_PCL}}, PCL_PCL};  // Bit_Extender bit_extender_1
  assign bit_extender_2_out = {{7{ADL_PCL}}, ADL_PCL};  // Bit_Extender bit_extender_2
  not not_26 (not_26_out[0], _1_PC);
  assign bit_extender_3_out = {{7{PCH_PCH}}, PCH_PCH};  // Bit_Extender bit_extender_3
  assign bit_extender_4_out = {{7{ADH_PCH}}, ADH_PCH};  // Bit_Extender bit_extender_4
  assign and_41_out = PCL & bit_extender_1_out;  // AND_Gate and_41, 8 bits wide
  assign and_42_out = ADL_IN & bit_extender_2_out;  // AND_Gate and_42, 8 bits wide
  or or_41 (or_41_out, ADL_PCL, PCL_PCL);
  assign and_43_out = PCH & bit_extender_3_out;  // AND_Gate and_43, 8 bits wide
  assign and_44_out = ADH_IN & bit_extender_4_out;  // AND_Gate and_44, 8 bits wide
  or or_42 (or_42_out, ADH_PCH, PCH_PCH);
  assign or_43_out = and_41_out | and_42_out;  // OR_Gate or_43, 8 bits wide
  assign or_44_out = and_43_out | and_44_out;  // OR_Gate or_44, 8 bits wide
  Register #(.trigger("high")) register_1 (.D(or_43_out), .en(or_41_out), .Q(register_1_q), .clk(PHI1));  // open: clr
  Register #(.trigger("high")) register_2 (.D(or_44_out), .en(or_42_out), .Q(register_2_q), .clk(PHI1));  // open: clr
  assign xor_1_out = register_1_q ^ not_26_out;  // XOR_Gate xor_1, 8 bits wide
  assign {and_45_out[7], not_26_out[7:1]} = not_26_out & register_1_q;  // AND_Gate and_45, 8 bits wide
  assign xor_2_out = register_2_q ^ and_47_out;  // XOR_Gate xor_2, 8 bits wide
  assign {and_46_out[7], and_47_out[7:6], and_46_out[4], and_47_out[4:1]} = and_47_out & register_2_q;  // AND_Gate and_46, 8 bits wide
  Register #(.trigger("high")) register_3 (.D(xor_1_out), .Q(PCL), .clk(PHI2));  // open: en, clr
  Register #(.trigger("high")) register_4 (.D(xor_2_out), .Q(PCH), .clk(PHI2));  // open: en, clr
  and and_47 (and_47_out[0], not_26_out[0], register_1_q[0], register_1_q[1], register_1_q[2], register_1_q[3], register_1_q[4], register_1_q[5], register_1_q[6], register_1_q[7]);
  and and_48 (and_47_out[5], and_47_out[0], register_2_q[0], register_2_q[1], register_2_q[2], register_2_q[3]);
endmodule
